// Logisim project Ideal_Pipeline.circ as structural Verilog
module main (
);

  wire and_1_out, BneOrBeq, Branch, clk, clock_1_out, control_1_alusrc, control_1_bneorbeq, control_1_branch,
       control_1_isexception, control_1_isjal, control_1_isjr, control_1_isshamt, control_1_issyscall,
       control_1_jump, control_1_memread, control_1_memtoreg, control_1_memwrite, Equal, Halt,
       id_ex_1_issyscallex, IsJAL, IsJALID, IsJR, IsShamt, IsSyscall, IsUnsignedID, Jump, MemRead, MemtoReg,
       MemWrite, not_1_out, not_2_out, not_3_out, RegDstID, statistics_1_i, statistics_1_j, statistics_1_r,
       xor_1_out;
  wire [3:0] control_1_aluop, undriven_4, undriven_5, undriven_6, undriven_7, undriven_8, undriven_15,
       undriven_16, undriven_17;
  wire [4:0] multiplexer_3_out, multiplexer_4_out, multiplexer_5_out, multiplexer_6_out;
  wire [5:0] undriven_2;
  wire [31:0] adder_1_out, adder_2_out, adder_4_out, alu_wrapper_1_result, bit_extender_1_out,
       bit_extender_2_out, bit_extender_3_out, counter_1_q, counter_2_q, counter_3_q, Cycle_q, id_ex_1_immex,
       id_ex_1_pcplusex, id_ex_1_r1ex, id_ex_1_r2ex, id_ex_1_shamtex, if_id_1_instid, if_id_1_pcplus4if,
       multiplexer_1_out, multiplexer_7_out, multiplexer_11_out, multiplexer_12_out, multiplexer_13_out,
       multiplexer_14_out, multiplexer_15_out, multiplexer_16_out, multiplexer_17_out, PC_q, ram_1_data,
       regfile_wrapper_1_r1, regfile_wrapper_1_r2, rom_1_data, shifter_1_out, shifter_2_out, undriven,
       undriven_3, undriven_9, undriven_10, undriven_11, undriven_12, undriven_13, undriven_14, undriven_18;

  Multiplexer #(.width(32), .enable("false")) multiplexer_1 (
    .in0(adder_1_out), .in1(undriven), .out(multiplexer_1_out));  // open: sel
  Register #(.width(32)) PC (.D(multiplexer_1_out), .Q(PC_q), .clk(clk));  // open: en, clr
  Counter #(.width(32), .max('hffffffff)) Cycle (.Q(Cycle_q), .clk(clk));  // open: load, D, count, carry, clr
  // Probe on Cycle_q
  Adder #(.width(32)) adder_1 (.a(PC_q), .b(32'h4), .out(adder_1_out));  // open: cin, cout
  IF_ID if_id_1 (
    .InstIF(rom_1_data), .InstID(if_id_1_instid), .PCPlus4ID(adder_1_out), .PCPlus4IF(if_id_1_pcplus4if));  // open: clk
  ROM #(.addrWidth(10), .dataWidth(32)) rom_1 (.addr(PC_q[11:2]), .data(rom_1_data));  // open: sel
  Clock clock_1 (.out(clock_1_out));
  Multiplexer #(.enable("false")) multiplexer_2 (.in0(clock_1_out), .in1(1'b1), .out(clk), .sel(Halt));
  Control control_1 (
    .op(if_id_1_instid[31:26]), .Funct(if_id_1_instid[5:0]), .ALUop(control_1_aluop),
    .IsJAL(control_1_isjal), .IsShamt(control_1_isshamt), .MemtoReg(control_1_memtoreg), .RegWrite(IsJALID),
    .MemRead(control_1_memread), .MemWrite(control_1_memwrite), .Jump(control_1_jump),
    .Branch(control_1_branch), .RegDst(RegDstID), .BneOrBeq(control_1_bneorbeq), .ALUSrc(control_1_alusrc),
    .IsJR(control_1_isjr), .IsSyscall(control_1_issyscall), .IsException(control_1_isexception),
    .IsUnsigned(IsUnsignedID));
  not not_1 (not_1_out, IsSyscall);
  assign bit_extender_1_out = {{16{if_id_1_instid[15]}}, if_id_1_instid[15:0]};  // Bit_Extender bit_extender_1
  Multiplexer #(.width(5), .enable("false")) multiplexer_3 (
    .in0(5'b00010), .in1(if_id_1_instid[25:21]), .out(multiplexer_3_out), .sel(not_1_out));
  Multiplexer #(.width(5), .enable("false")) multiplexer_4 (
    .in0(if_id_1_instid[20:16]), .in1(if_id_1_instid[15:11]), .out(multiplexer_4_out), .sel(RegDstID));
  assign bit_extender_2_out = {{16{1'b0}}, if_id_1_instid[15:0]};  // Bit_Extender bit_extender_2
  Counter #(.width(32), .max('hffffffff)) counter_1 (
    .count(statistics_1_r), .Q(counter_1_q), .clk(clk));  // open: load, D, carry, clr
  Counter #(.width(32), .max('hffffffff)) counter_2 (
    .count(statistics_1_j), .Q(counter_2_q), .clk(clk));  // open: load, D, carry, clr
  // Probe on counter_2_q
  Regfile_Wrapper regfile_wrapper_1 (
    .R1_num(multiplexer_3_out), .R2_num(multiplexer_5_out), .R1(regfile_wrapper_1_r1),
    .R2(regfile_wrapper_1_r2), .clk(clk));  // open: RW, Din, WE
  Multiplexer #(.width(5), .enable("false")) multiplexer_5 (
    .in0(5'b00100), .in1(if_id_1_instid[20:16]), .out(multiplexer_5_out), .sel(not_1_out));
  Multiplexer #(.width(5), .enable("false")) multiplexer_6 (
    .in0(multiplexer_4_out), .in1({5{1'b1}}), .out(multiplexer_6_out), .sel(IsJALID));
  assign bit_extender_3_out = {{27{1'b0}}, if_id_1_instid[10:6]};  // Bit_Extender bit_extender_3
  Multiplexer #(.width(32), .enable("false")) multiplexer_7 (
    .in0(bit_extender_1_out), .in1(bit_extender_2_out), .out(multiplexer_7_out), .sel(IsUnsignedID));
  Counter #(.width(32), .max('hffffffff)) counter_3 (
    .count(statistics_1_i), .Q(counter_3_q), .clk(clk));  // open: load, D, carry, clr
  // Probe on counter_3_q
  // Probe on counter_1_q
  Statistics statistics_1 (
    .op0(undriven_2[5]), .op1(undriven_2[4]), .op2(undriven_2[3]), .op3(undriven_2[2]), .op4(undriven_2[1]),
    .op5(undriven_2[0]), .i(statistics_1_i), .r(statistics_1_r), .j(statistics_1_j));
  ID_EX id_ex_1 (
    .IsJALID(control_1_isjal), .MemReadID(control_1_memread), .IsShamtID(control_1_isshamt),
    .MemWriteID(control_1_memwrite), .MemtoRegID(control_1_memtoreg), .JumpID(control_1_jump),
    .RegWriteID(IsJALID), .BranchID(control_1_branch), .BneOrBeqID(control_1_bneorbeq),
    .ALUSrcID(control_1_alusrc), .IsJRID(control_1_isjr), .IsExceptionID(control_1_isexception),
    .ALUopID(control_1_aluop), .WriteReg_ID(multiplexer_6_out), .ImmID(multiplexer_7_out),
    .ImmEX(id_ex_1_immex), .R1ID(regfile_wrapper_1_r1), .R1EX(id_ex_1_r1ex), .R2ID(regfile_wrapper_1_r2),
    .R2EX(id_ex_1_r2ex), .PCPlus4ID(if_id_1_pcplus4if), .PCPlusEX(id_ex_1_pcplusex),
    .ShamtID(bit_extender_3_out), .ShamtEX(id_ex_1_shamtex),
    .JumpAddr({if_id_1_pcplus4if[31:28], if_id_1_instid[25:0], 2'b00}), .IsSyscallID(control_1_issyscall),
    .IsSyscallEX(id_ex_1_issyscallex));  // open: clk, IsJALEX, MemReadEX, IsShamtEX, MemWriteEX, MemtoRegEX, JumpEX, RegWriteEX, BranchEX, BneOrBeqEX, ALUSrcEX, IsJREX, IsExceptionEX, ALUopEX, WriteReg_EX, JumpAddr_2
  Syscall_Decoder syscall_decoder_1 (
    .v0(id_ex_1_r1ex), .a0(id_ex_1_r2ex), .Enable(id_ex_1_issyscallex), .clk(clk));  // open: Hex, Halt
  Multiplexer #(.width(32), .enable("false")) multiplexer_8 (.in0(undriven_3), .sel(not_2_out));  // open: in1, out
  not not_2 (not_2_out, IsJAL);
  Multiplexer #(.width(32), .enable("false")) multiplexer_9 (.in0(id_ex_1_r1ex), .in1(id_ex_1_r2ex));  // open: out, sel
  Multiplexer #(.width(32), .enable("false")) multiplexer_10 (.in1(id_ex_1_shamtex));  // open: in0, out, sel
  Hex_Digit_Display hex_digit_display_1 (.value(undriven_4));  // open: dp
  Hex_Digit_Display hex_digit_display_2 (.value(undriven_6));  // open: dp
  Hex_Digit_Display hex_digit_display_3 (.value(undriven_5));  // open: dp
  Adder #(.width(32)) adder_2 (.a(32'h4), .b(undriven_13), .out(adder_2_out));  // open: cin, cout
  Multiplexer #(.width(32), .enable("false")) multiplexer_11 (
    .in0(undriven_11), .in1(undriven_9), .out(multiplexer_11_out));  // open: sel
  Shifter #(.width(32)) shifter_1 (.in(id_ex_1_immex), .\dist (5'b00010), .out(shifter_1_out));
  Hex_Digit_Display hex_digit_display_4 (.value(undriven_7));  // open: dp
  Hex_Digit_Display hex_digit_display_5 (.value(undriven_15));  // open: dp
  Shifter #(.width(32)) shifter_2 (.in(undriven_14), .\dist (5'b00010), .out(shifter_2_out));
  xor xor_1 (xor_1_out, Equal, BneOrBeq);
  Multiplexer #(.width(32), .enable("false")) multiplexer_12 (
    .in0(undriven_10), .in1(undriven_11), .out(multiplexer_12_out), .sel(IsShamt));
  Multiplexer #(.width(32), .enable("false")) multiplexer_13 (
    .in0(multiplexer_11_out), .out(multiplexer_13_out), .sel(IsShamt));  // open: in1
  Adder #(.width(32)) adder_3 (.a(shifter_1_out), .b(id_ex_1_pcplusex));  // open: out, cin, cout
  Hex_Digit_Display hex_digit_display_6 (.value(undriven_16));  // open: dp
  Hex_Digit_Display hex_digit_display_7 (.value(undriven_8));  // open: dp
  ALU_Wrapper alu_wrapper_1 (
    .X(multiplexer_12_out), .Y(multiplexer_13_out), .Equal(Equal), .Result(alu_wrapper_1_result));  // open: AluOP, Result_2
  Hex_Digit_Display hex_digit_display_8 (.value(undriven_17));  // open: dp
  Adder #(.width(32)) adder_4 (.a(adder_2_out), .b(shifter_2_out), .out(adder_4_out));  // open: cin, cout
  and and_1 (and_1_out, Branch, xor_1_out);
  Multiplexer #(.width(32), .enable("false")) multiplexer_14 (
    .in0(adder_2_out), .in1(adder_4_out), .out(multiplexer_14_out), .sel(and_1_out));
  Multiplexer #(.width(32), .enable("false")) multiplexer_15 (
    .in0(undriven_12), .in1(multiplexer_14_out), .out(multiplexer_15_out), .sel(not_3_out));
  not not_3 (not_3_out, Jump);
  RAM #(.addrWidth(10), .dataWidth(32), .bus("separate")) ram_1 (
    .addr(alu_wrapper_1_result[11:2]), .din(undriven_11), .data(ram_1_data), .str(MemWrite), .clk(clk),
    .ld(MemRead));  // open: sel, clr
  Multiplexer #(.width(32), .enable("false")) multiplexer_16 (
    .in0(alu_wrapper_1_result), .in1(ram_1_data), .out(multiplexer_16_out), .sel(MemtoReg));
  Multiplexer #(.width(32), .enable("false")) multiplexer_17 (
    .in0(multiplexer_15_out), .in1(undriven_18), .out(multiplexer_17_out), .sel(IsJR));

  // Notes on the sheet:
  //   PC`
  //   PCIF
  //   PCPlus4IF
  //   contents of rom_1 (hex, n*v repeats v):
  //   20110001 8000c05 20110001 20120002 20130003 8000c09 20110001 20120002 20130003 8000c0d 20110001
  //   20120002 20130003 8000c11 20110001 20120002 20130003 c000cb8 20100001 20110001 118fc0 112020
  //   20020022 c 118882 12200001 8000c15 112020 20020022 c 20110001 118880 112020 20020022 c 12200001
  //   8000c1f 20110001 118fc0 112020 20020022 c 1188c3 112020 20020022 c 118903 112020 20020022 c 118903
  //   112020 20020022 c 118903 112020 20020022 c 118903 112020 20020022 c 118903 112020 20020022 c 118903
  //   112020 20020022 c 118903 112020 20020022 c 20100001 109fc0 139fc3 8021 2012000c 24160003 26100001
  //   3210000f 20080008 20090001 139900 2709825 132020 20020022 c 1094022 1500fff9 22100001 2018000f
  //   2188024 108700 20080008 20090001 139902 2709825 132021 20020022 c 1094022 1500fff9 108702 2c9b022
  //   12c00001 8000c50 4020 1084027 84400 3508ffff 82021 20020022 c 2010ffff 20110000 ae300000 22100001
  //   22310004 ae300000 22100001 22310004 ae300000 22100001 22310004 ae300000 22100001 22310004 ae300000
  //   22100001 22310004 ae300000 22100001 22310004 ae300000 22100001 22310004 ae300000 22100001 22310004
  //   ae300000 22100001 22310004 ae300000 22100001 22310004 ae300000 22100001 22310004 ae300000 22100001
  //   22310004 ae300000 22100001 22310004 ae300000 22100001 22310004 ae300000 22100001 22310004 ae300000
  //   22100001 22310004 22100001 8020 2011003c 8e130000 8e340000 274402a 11000002 ae330000 ae140000
  //   2231fffc 1611fff8 102020 20020022 c 22100004 2011003c 1611fff2 2002000a c 20100000 22100001 102020
  //   20020022 c 22100002 102020 20020022 c 22100003 102020 20020022 c 22100004 102020 20020022 c 22100005
  //   102020 20020022 c 22100006 102020 20020022 c 22100007 102020 20020022 c 22100008 102020 20020022
  //   20020022 c 3e00008
  //   Shamt
  //   Immediate
  //   JumpAddr
  //   JMP无条件跳转
  //   无条件跳转地址
  //   R2
  //   IMME
  //   IMME
  //   R1
  //   输入PC
  //   WB_DATA
endmodule

module Control (
  input  [5:0] op,
  input  [5:0] Funct,
  output IsJAL,
  output MemRead,
  output IsShamt,
  output MemWrite,
  output MemtoReg,
  output Jump,
  output RegWrite,
  output Branch,
  output BneOrBeq,
  output RegDst,
  output [3:0] ALUop,
  output ALUSrc,
  output IsJR,
  output IsSyscall,
  output IsException,
  output IsUnsigned
);

  wire funct_decoder_1_isjr, funct_decoder_1_isshamt, funct_decoder_1_issyscall, IsSpecial, not_1_out;
  wire [3:0] alu_decoder_1_aluop3, funct_decoder_1_alu3;

  Opcode_Decoder opcode_decoder_1 (
    .op0(op[5]), .MemRead(MemRead), .op1(op[4]), .op2(op[3]), .MemWrite(MemWrite), .op3(op[2]), .op4(op[1]),
    .op5(op[0]), .ALUSrc(ALUSrc), .Jump(Jump), .MemtoReg(MemtoReg), .Branch(Branch), .RegDst(RegDst),
    .RegWrite(RegWrite), .BneBeq(BneOrBeq), .IsJAL(IsJAL), .IsUnsigned(IsUnsigned));
  Funct_Decoder funct_decoder_1 (
    .Funct0(Funct[5]), .Funct1(Funct[4]), .Funct2(Funct[3]), .Funct3(Funct[2]),
    .ALU0(funct_decoder_1_alu3[3]), .Funct4(Funct[1]), .Funct5(Funct[0]), .ALU1(funct_decoder_1_alu3[2]),
    .ALU2(funct_decoder_1_alu3[1]), .ALU3(funct_decoder_1_alu3[0]), .IsJR(funct_decoder_1_isjr),
    .IsSyscall(funct_decoder_1_issyscall), .IsShamt(funct_decoder_1_isshamt));
  ALU_Decoder alu_decoder_1 (
    .op0(op[5]), .op1(op[4]), .op2(op[3]), .ALUop0(alu_decoder_1_aluop3[3]), .op3(op[2]), .op4(op[1]),
    .op5(op[0]), .ALUop1(alu_decoder_1_aluop3[2]), .ALUop2(alu_decoder_1_aluop3[1]),
    .ALUop3(alu_decoder_1_aluop3[0]));
  and and_1 (IsException, ~op[5], op[4], ~op[3], ~op[2], ~op[1], ~op[0]);  // AND_Gate
  Multiplexer #(.enable("false")) multiplexer_1 (
    .in0(1'b0), .in1(funct_decoder_1_issyscall), .out(IsSyscall), .sel(IsSpecial));
  Multiplexer #(.enable("false")) multiplexer_2 (.in0(1'b0), .in1(funct_decoder_1_isjr), .out(IsJR), .sel(IsSpecial));
  Multiplexer #(.enable("false")) multiplexer_3 (
    .in0(1'b0), .in1(funct_decoder_1_isshamt), .out(IsShamt), .sel(IsSpecial));
  not not_1 (not_1_out, IsSpecial);
  Multiplexer #(.width(4), .enable("false")) multiplexer_4 (
    .in0(funct_decoder_1_alu3), .in1(alu_decoder_1_aluop3), .out(ALUop), .sel(not_1_out));
  and and_2 (IsSpecial, ~op[5], ~op[4], ~op[3], ~op[2], ~op[1], ~op[0]);  // AND_Gate

  // Notes on the sheet:
  //   Input & Output
  //   OP Decoding Area
  //   ALU Decoding Area
  //   Exception Handler
endmodule

module Funct_Decoder (
  input  Funct0,
  input  Funct1,
  input  Funct2,
  input  Funct3,
  input  Funct4,
  input  Funct5,
  output ALU0,
  output ALU1,
  output ALU2,
  output ALU3,
  output IsJR,
  output IsSyscall,
  output IsShamt
);

  wire and_1_out, and_2_out, and_3_out, and_4_out, and_5_out, and_6_out, and_7_out, and_8_out, and_9_out,
       and_10_out, and_11_out, and_12_out, and_13_out, and_14_out, and_15_out, and_16_out, and_17_out,
       and_20_out, and_21_out, and_22_out, not_1_out, not_2_out, not_3_out, not_4_out, not_5_out, not_6_out,
       not_7_out, not_8_out, not_9_out, not_10_out, not_11_out, not_12_out, not_13_out, not_14_out,
       not_15_out, not_16_out, not_17_out, not_18_out, not_19_out, not_20_out, not_21_out, not_22_out,
       not_23_out, not_24_out, not_25_out, not_26_out, not_27_out, not_28_out, not_29_out, not_30_out,
       not_31_out, not_32_out, not_33_out, not_34_out, not_35_out, not_36_out, not_37_out, not_38_out,
       not_39_out, not_40_out, not_41_out, not_42_out, not_43_out, not_44_out, not_45_out, not_46_out,
       not_47_out, not_48_out, not_49_out, not_50_out, not_51_out, not_52_out, not_53_out, not_54_out,
       not_55_out, not_56_out, not_57_out, not_58_out, not_59_out, not_60_out, not_61_out, not_62_out,
       not_63_out, not_64_out, not_65_out, not_66_out, not_67_out, not_68_out, not_69_out, not_70_out,
       not_71_out, not_72_out, not_73_out, not_74_out, not_75_out, not_76_out, not_77_out, not_78_out,
       not_79_out, not_80_out, not_81_out;

  not not_1 (not_1_out, Funct1);
  not not_2 (not_2_out, Funct2);
  not not_3 (not_3_out, Funct4);
  not not_4 (not_4_out, Funct1);
  not not_5 (not_5_out, Funct2);
  not not_6 (not_6_out, Funct1);
  not not_7 (not_7_out, Funct3);
  not not_8 (not_8_out, Funct5);
  not not_9 (not_9_out, Funct1);
  not not_10 (not_10_out, Funct3);
  not not_11 (not_11_out, Funct1);
  not not_12 (not_12_out, Funct2);
  not not_13 (not_13_out, Funct3);
  not not_14 (not_14_out, Funct4);
  not not_15 (not_15_out, Funct1);
  not not_16 (not_16_out, Funct2);
  not not_17 (not_17_out, Funct3);
  not not_18 (not_18_out, Funct5);
  not not_19 (not_19_out, Funct1);
  not not_20 (not_20_out, Funct2);
  not not_21 (not_21_out, Funct4);
  not not_22 (not_22_out, Funct5);
  not not_23 (not_23_out, Funct1);
  not not_24 (not_24_out, Funct3);
  not not_25 (not_25_out, Funct1);
  not not_26 (not_26_out, Funct2);
  not not_27 (not_27_out, Funct3);
  not not_28 (not_28_out, Funct5);
  not not_29 (not_29_out, Funct1);
  not not_30 (not_30_out, Funct2);
  not not_31 (not_31_out, Funct4);
  not not_32 (not_32_out, Funct5);
  not not_33 (not_33_out, Funct0);
  not not_34 (not_34_out, Funct1);
  not not_35 (not_35_out, Funct2);
  not not_36 (not_36_out, Funct3);
  not not_37 (not_37_out, Funct5);
  not not_38 (not_38_out, Funct1);
  not not_39 (not_39_out, Funct2);
  not not_40 (not_40_out, Funct1);
  not not_41 (not_41_out, Funct3);
  not not_42 (not_42_out, Funct5);
  not not_43 (not_43_out, Funct0);
  not not_44 (not_44_out, Funct1);
  not not_45 (not_45_out, Funct2);
  not not_46 (not_46_out, Funct3);
  not not_47 (not_47_out, Funct1);
  not not_48 (not_48_out, Funct2);
  not not_49 (not_49_out, Funct3);
  not not_50 (not_50_out, Funct4);
  not not_51 (not_51_out, Funct1);
  not not_52 (not_52_out, Funct2);
  not not_53 (not_53_out, Funct4);
  not not_54 (not_54_out, Funct5);
  not not_55 (not_55_out, Funct1);
  not not_56 (not_56_out, Funct3);
  not not_57 (not_57_out, Funct5);
  not not_58 (not_58_out, Funct0);
  not not_59 (not_59_out, Funct1);
  not not_60 (not_60_out, Funct3);
  not not_61 (not_61_out, Funct4);
  not not_62 (not_62_out, Funct5);
  not not_63 (not_63_out, Funct0);
  not not_64 (not_64_out, Funct1);
  not not_65 (not_65_out, Funct4);
  not not_66 (not_66_out, Funct5);
  not not_67 (not_67_out, Funct0);
  not not_68 (not_68_out, Funct1);
  not not_69 (not_69_out, Funct2);
  not not_70 (not_70_out, Funct3);
  not not_71 (not_71_out, Funct0);
  not not_72 (not_72_out, Funct1);
  not not_73 (not_73_out, Funct2);
  not not_74 (not_74_out, Funct3);
  not not_75 (not_75_out, Funct5);
  not not_76 (not_76_out, Funct0);
  not not_77 (not_77_out, Funct1);
  not not_78 (not_78_out, Funct2);
  not not_79 (not_79_out, Funct3);
  not not_80 (not_80_out, Funct4);
  not not_81 (not_81_out, Funct5);
  and and_1 (and_1_out, Funct0, not_1_out, not_2_out, Funct3, not_3_out, Funct5);
  and and_2 (and_2_out, Funct0, not_4_out, not_5_out, Funct3, Funct4, Funct5);
  and and_3 (and_3_out, Funct0, not_6_out, Funct2, not_7_out, Funct4, not_8_out);
  and and_4 (and_4_out, Funct0, not_9_out, Funct2, not_10_out, Funct4, Funct5);
  and and_5 (and_5_out, Funct0, not_11_out, not_12_out, not_13_out, not_14_out);
  and and_6 (and_6_out, Funct0, not_15_out, not_16_out, not_17_out, not_18_out);
  and and_7 (and_7_out, Funct0, not_19_out, not_20_out, not_21_out, not_22_out);
  and and_8 (and_8_out, Funct0, not_23_out, Funct2, not_24_out, Funct4, Funct5);
  and and_9 (and_9_out, Funct0, not_25_out, not_26_out, not_27_out, Funct4, not_28_out);
  and and_10 (and_10_out, Funct0, not_29_out, not_30_out, Funct3, not_31_out, not_32_out);
  and and_11 (and_11_out, not_33_out, not_34_out, not_35_out, not_36_out, Funct4, not_37_out);
  and and_12 (and_12_out, Funct0, not_38_out, not_39_out, Funct3, Funct4, Funct5);
  and and_13 (and_13_out, Funct0, not_40_out, Funct2, not_41_out, Funct4, not_42_out);
  and and_14 (and_14_out, not_43_out, not_44_out, not_45_out, not_46_out, Funct4, Funct5);
  and and_15 (and_15_out, Funct0, not_47_out, not_48_out, not_49_out, not_50_out);
  and and_16 (and_16_out, Funct0, not_51_out, not_52_out, not_53_out, not_54_out);
  and and_17 (and_17_out, Funct0, not_55_out, Funct2, not_56_out, Funct4, not_57_out);
  and and_18 (IsJR, not_58_out, not_59_out, Funct2, not_60_out, not_61_out, not_62_out);
  and and_19 (IsSyscall, not_63_out, not_64_out, Funct2, Funct3, not_65_out, not_66_out);
  and and_20 (and_20_out, not_67_out, not_68_out, not_69_out, not_70_out, Funct4, Funct5);
  and and_21 (and_21_out, not_71_out, not_72_out, not_73_out, not_74_out, Funct4, not_75_out);
  and and_22 (and_22_out, not_76_out, not_77_out, not_78_out, not_79_out, not_80_out, not_81_out);
  or or_1 (ALU0, and_1_out, and_2_out, and_3_out, and_4_out);
  or or_2 (ALU1, and_5_out, and_6_out, and_7_out, and_8_out);
  or or_3 (ALU2, and_9_out, and_10_out, and_11_out, and_12_out, and_13_out);
  or or_4 (ALU3, and_14_out, and_15_out, and_16_out, and_17_out);
  or or_5 (IsShamt, and_20_out, and_21_out, and_22_out);
endmodule

module ALU_Decoder (
  input  op0,
  input  op1,
  input  op2,
  input  op3,
  input  op4,
  input  op5,
  output ALUop0,
  output ALUop1,
  output ALUop2,
  output ALUop3
);

  wire and_1_out, and_2_out, and_3_out, and_4_out, and_5_out, and_6_out, and_7_out, and_8_out, and_9_out,
       and_10_out, and_11_out, and_12_out, and_13_out, and_14_out, and_15_out, and_16_out, and_17_out,
       and_18_out, and_19_out, and_20_out, and_21_out, and_22_out, and_23_out, and_24_out, and_25_out,
       and_26_out, and_27_out, and_28_out, and_29_out, not_1_out, not_2_out, not_3_out, not_4_out, not_5_out,
       not_6_out, not_7_out, not_8_out, not_9_out, not_10_out, not_11_out, not_12_out, not_13_out,
       not_14_out, not_15_out, not_16_out, not_17_out, not_18_out, not_19_out, not_20_out, not_21_out,
       not_22_out, not_23_out, not_24_out, not_25_out, not_26_out, not_27_out, not_28_out, not_29_out,
       not_30_out, not_31_out, not_32_out, not_33_out, not_34_out, not_35_out, not_36_out, not_37_out,
       not_38_out, not_39_out, not_40_out, not_41_out, not_42_out, not_43_out, not_44_out, not_45_out,
       not_46_out, not_47_out, not_48_out, not_49_out, not_50_out, not_51_out, not_52_out, not_53_out,
       not_54_out, not_55_out, not_56_out, not_57_out, not_58_out, not_59_out, not_60_out, not_61_out,
       not_62_out, not_63_out, not_64_out, not_65_out, not_66_out, not_67_out, not_68_out, not_69_out,
       not_70_out, not_71_out, not_72_out, not_73_out, not_74_out, not_75_out, not_76_out, not_77_out,
       not_78_out, not_79_out, not_80_out, not_81_out, not_82_out, not_83_out, not_84_out, not_85_out,
       not_86_out, not_87_out, not_88_out, not_89_out, not_90_out, not_91_out, not_92_out, not_93_out,
       not_94_out, not_95_out, not_96_out, not_97_out, not_98_out, not_99_out, not_100_out, not_101_out,
       not_102_out, not_103_out, not_104_out, not_105_out, not_106_out, not_107_out, not_108_out,
       not_109_out, not_110_out, not_111_out, not_112_out, not_113_out, not_114_out, not_115_out,
       not_116_out, not_117_out, not_118_out, not_119_out, not_120_out, not_121_out, not_122_out, not_123_out;

  not not_1 (not_1_out, op0);
  not not_2 (not_2_out, op1);
  not not_3 (not_3_out, op4);
  not not_4 (not_4_out, op0);
  not not_5 (not_5_out, op1);
  not not_6 (not_6_out, op3);
  not not_7 (not_7_out, op5);
  not not_8 (not_8_out, op0);
  not not_9 (not_9_out, op1);
  not not_10 (not_10_out, op2);
  not not_11 (not_11_out, op3);
  not not_12 (not_12_out, op4);
  not not_13 (not_13_out, op5);
  not not_14 (not_14_out, op0);
  not not_15 (not_15_out, op1);
  not not_16 (not_16_out, op3);
  not not_17 (not_17_out, op4);
  not not_18 (not_18_out, op5);
  not not_19 (not_19_out, op1);
  not not_20 (not_20_out, op2);
  not not_21 (not_21_out, op3);
  not not_22 (not_22_out, op1);
  not not_23 (not_23_out, op3);
  not not_24 (not_24_out, op0);
  not not_25 (not_25_out, op1);
  not not_26 (not_26_out, op2);
  not not_27 (not_27_out, op4);
  not not_28 (not_28_out, op0);
  not not_29 (not_29_out, op1);
  not not_30 (not_30_out, op2);
  not not_31 (not_31_out, op4);
  not not_32 (not_32_out, op5);
  not not_33 (not_33_out, op0);
  not not_34 (not_34_out, op1);
  not not_35 (not_35_out, op4);
  not not_36 (not_36_out, op5);
  not not_37 (not_37_out, op0);
  not not_38 (not_38_out, op1);
  not not_39 (not_39_out, op3);
  not not_40 (not_40_out, op4);
  not not_41 (not_41_out, op0);
  not not_42 (not_42_out, op1);
  not not_43 (not_43_out, op3);
  not not_44 (not_44_out, op4);
  not not_45 (not_45_out, op5);
  not not_46 (not_46_out, op0);
  not not_47 (not_47_out, op1);
  not not_48 (not_48_out, op2);
  not not_49 (not_49_out, op3);
  not not_50 (not_50_out, op5);
  not not_51 (not_51_out, op0);
  not not_52 (not_52_out, op1);
  not not_53 (not_53_out, op2);
  not not_54 (not_54_out, op3);
  not not_55 (not_55_out, op0);
  not not_56 (not_56_out, op2);
  not not_57 (not_57_out, op3);
  not not_58 (not_58_out, op4);
  not not_59 (not_59_out, op5);
  not not_60 (not_60_out, op0);
  not not_61 (not_61_out, op1);
  not not_62 (not_62_out, op4);
  not not_63 (not_63_out, op5);
  not not_64 (not_64_out, op0);
  not not_65 (not_65_out, op1);
  not not_66 (not_66_out, op3);
  not not_67 (not_67_out, op5);
  not not_68 (not_68_out, op0);
  not not_69 (not_69_out, op1);
  not not_70 (not_70_out, op2);
  not not_71 (not_71_out, op3);
  not not_72 (not_72_out, op4);
  not not_73 (not_73_out, op5);
  not not_74 (not_74_out, op0);
  not not_75 (not_75_out, op1);
  not not_76 (not_76_out, op3);
  not not_77 (not_77_out, op4);
  not not_78 (not_78_out, op5);
  not not_79 (not_79_out, op1);
  not not_80 (not_80_out, op2);
  not not_81 (not_81_out, op3);
  not not_82 (not_82_out, op1);
  not not_83 (not_83_out, op3);
  not not_84 (not_84_out, op0);
  not not_85 (not_85_out, op1);
  not not_86 (not_86_out, op2);
  not not_87 (not_87_out, op4);
  not not_88 (not_88_out, op0);
  not not_89 (not_89_out, op1);
  not not_90 (not_90_out, op2);
  not not_91 (not_91_out, op4);
  not not_92 (not_92_out, op5);
  not not_93 (not_93_out, op0);
  not not_94 (not_94_out, op1);
  not not_95 (not_95_out, op4);
  not not_96 (not_96_out, op5);
  not not_97 (not_97_out, op0);
  not not_98 (not_98_out, op1);
  not not_99 (not_99_out, op3);
  not not_100 (not_100_out, op5);
  not not_101 (not_101_out, op0);
  not not_102 (not_102_out, op1);
  not not_103 (not_103_out, op3);
  not not_104 (not_104_out, op4);
  not not_105 (not_105_out, op0);
  not not_106 (not_106_out, op1);
  not not_107 (not_107_out, op3);
  not not_108 (not_108_out, op4);
  not not_109 (not_109_out, op5);
  not not_110 (not_110_out, op0);
  not not_111 (not_111_out, op1);
  not not_112 (not_112_out, op2);
  not not_113 (not_113_out, op3);
  not not_114 (not_114_out, op5);
  not not_115 (not_115_out, op0);
  not not_116 (not_116_out, op1);
  not not_117 (not_117_out, op2);
  not not_118 (not_118_out, op3);
  not not_119 (not_119_out, op0);
  not not_120 (not_120_out, op2);
  not not_121 (not_121_out, op3);
  not not_122 (not_122_out, op4);
  not not_123 (not_123_out, op5);
  and and_1 (and_1_out, not_1_out, not_2_out, op2, op3, not_3_out, op5);
  and and_2 (and_2_out, not_4_out, not_5_out, op2, not_6_out, op4, not_7_out);
  and and_3 (and_3_out, not_8_out, not_9_out, not_10_out, not_11_out, not_12_out, not_13_out);
  and and_4 (and_4_out, not_14_out, not_15_out, op2, not_16_out, not_17_out, not_18_out);
  and and_5 (and_5_out, op0, not_19_out, not_20_out, not_21_out, op4, op5);
  and and_6 (and_6_out, op0, not_22_out, op2, not_23_out, op4, op5);
  and and_7 (and_7_out, not_24_out, not_25_out, not_26_out, op3, not_27_out, op5);
  and and_8 (and_8_out, not_28_out, not_29_out, not_30_out, op3, not_31_out, not_32_out);
  and and_9 (and_9_out, not_33_out, not_34_out, op2, op3, not_35_out, not_36_out);
  and and_10 (and_10_out, not_37_out, not_38_out, op2, not_39_out, not_40_out, op5);
  and and_11 (and_11_out, not_41_out, not_42_out, op2, not_43_out, not_44_out, not_45_out);
  and and_12 (and_12_out, not_46_out, not_47_out, not_48_out, not_49_out, op4, not_50_out);
  and and_13 (and_13_out, not_51_out, not_52_out, not_53_out, not_54_out, op4, op5);
  and and_14 (and_14_out, not_55_out, op1, not_56_out, not_57_out, not_58_out, not_59_out);
  and and_15 (and_15_out, not_60_out, not_61_out, op2, op3, not_62_out, not_63_out);
  and and_16 (and_16_out, not_64_out, not_65_out, op2, not_66_out, op4, not_67_out);
  and and_17 (and_17_out, not_68_out, not_69_out, not_70_out, not_71_out, not_72_out, not_73_out);
  and and_18 (and_18_out, not_74_out, not_75_out, op2, not_76_out, not_77_out, not_78_out);
  and and_19 (and_19_out, op0, not_79_out, not_80_out, not_81_out, op4, op5);
  and and_20 (and_20_out, op0, not_82_out, op2, not_83_out, op4, op5);
  and and_21 (and_21_out, not_84_out, not_85_out, not_86_out, op3, not_87_out, op5);
  and and_22 (and_22_out, not_88_out, not_89_out, not_90_out, op3, not_91_out, not_92_out);
  and and_23 (and_23_out, not_93_out, not_94_out, op2, op3, not_95_out, not_96_out);
  and and_24 (and_24_out, not_97_out, not_98_out, op2, not_99_out, op4, not_100_out);
  and and_25 (and_25_out, not_101_out, not_102_out, op2, not_103_out, not_104_out, op5);
  and and_26 (and_26_out, not_105_out, not_106_out, op2, not_107_out, not_108_out, not_109_out);
  and and_27 (and_27_out, not_110_out, not_111_out, not_112_out, not_113_out, op4, not_114_out);
  and and_28 (and_28_out, not_115_out, not_116_out, not_117_out, not_118_out, op4, op5);
  and and_29 (and_29_out, not_119_out, op1, not_120_out, not_121_out, not_122_out, not_123_out);
  or or_1 (ALUop0, and_1_out, and_2_out);
  or or_2 (ALUop2, and_15_out, and_16_out);
  or or_3 (ALUop1, and_3_out, and_4_out, and_5_out, and_6_out, and_7_out, and_8_out, and_9_out, and_10_out, and_11_out, and_12_out, and_13_out, and_14_out);
  or or_4 (ALUop3, and_17_out, and_18_out, and_19_out, and_20_out, and_21_out, and_22_out, and_23_out, and_24_out, and_25_out, and_26_out, and_27_out, and_28_out, and_29_out);
endmodule

module Opcode_Decoder (
  input  op0,
  input  op1,
  input  op2,
  input  op3,
  input  op4,
  input  op5,
  output MemRead,
  output MemWrite,
  output ALUSrc,
  output Jump,
  output MemtoReg,
  output Branch,
  output RegDst,
  output RegWrite,
  output BneBeq,
  output IsJAL,
  output IsUnsigned
);

  wire and_3_out, and_4_out, and_5_out, and_6_out, and_7_out, and_8_out, and_9_out, and_10_out, and_11_out,
       and_12_out, and_14_out, and_15_out, and_17_out, and_18_out, and_19_out, and_20_out, and_21_out,
       and_22_out, and_23_out, and_24_out, and_25_out, and_26_out, not_1_out, not_2_out, not_3_out,
       not_4_out, not_5_out, not_6_out, not_7_out, not_8_out, not_9_out, not_10_out, not_11_out, not_12_out,
       not_13_out, not_14_out, not_15_out, not_16_out, not_17_out, not_18_out, not_19_out, not_20_out,
       not_21_out, not_22_out, not_23_out, not_24_out, not_25_out, not_26_out, not_27_out, not_28_out,
       not_29_out, not_30_out, not_31_out, not_32_out, not_33_out, not_34_out, not_35_out, not_36_out,
       not_37_out, not_38_out, not_39_out, not_40_out, not_41_out, not_42_out, not_43_out, not_44_out,
       not_45_out, not_46_out, not_47_out, not_48_out, not_49_out, not_50_out, not_51_out, not_52_out,
       not_53_out, not_54_out, not_55_out, not_56_out, not_57_out, not_58_out, not_59_out, not_60_out,
       not_61_out, not_62_out, not_63_out, not_64_out, not_65_out, not_66_out, not_67_out, not_68_out,
       not_69_out, not_70_out, not_71_out, not_72_out, not_73_out, not_74_out, not_75_out, not_76_out,
       not_77_out, not_78_out, not_79_out, not_80_out, not_81_out, not_82_out, not_83_out, not_84_out,
       not_85_out, not_86_out, not_87_out, not_88_out, not_89_out, not_90_out, not_91_out, not_92_out,
       not_93_out, not_94_out, not_95_out, not_96_out, not_97_out, not_98_out, not_99_out, not_100_out,
       not_101_out, not_102_out, not_103_out, not_104_out, not_105_out, not_106_out, not_107_out,
       not_108_out, not_109_out, not_110_out, not_111_out, not_112_out, not_113_out, not_114_out,
       not_115_out, not_116_out, not_117_out;

  not not_1 (not_1_out, op1);
  not not_2 (not_2_out, op2);
  not not_3 (not_3_out, op3);
  not not_4 (not_4_out, op1);
  not not_5 (not_5_out, op3);
  not not_6 (not_6_out, op0);
  not not_7 (not_7_out, op1);
  not not_8 (not_8_out, op3);
  not not_9 (not_9_out, op4);
  not not_10 (not_10_out, op5);
  not not_11 (not_11_out, op1);
  not not_12 (not_12_out, op2);
  not not_13 (not_13_out, op3);
  not not_14 (not_14_out, op1);
  not not_15 (not_15_out, op3);
  not not_16 (not_16_out, op0);
  not not_17 (not_17_out, op1);
  not not_18 (not_18_out, op4);
  not not_19 (not_19_out, op5);
  not not_20 (not_20_out, op0);
  not not_21 (not_21_out, op1);
  not not_22 (not_22_out, op4);
  not not_23 (not_23_out, op0);
  not not_24 (not_24_out, op1);
  not not_25 (not_25_out, op3);
  not not_26 (not_26_out, op5);
  not not_27 (not_27_out, op0);
  not not_28 (not_28_out, op1);
  not not_29 (not_29_out, op3);
  not not_30 (not_30_out, op4);
  not not_31 (not_31_out, op0);
  not not_32 (not_32_out, op1);
  not not_33 (not_33_out, op3);
  not not_34 (not_34_out, op4);
  not not_35 (not_35_out, op5);
  not not_36 (not_36_out, op0);
  not not_37 (not_37_out, op1);
  not not_38 (not_38_out, op2);
  not not_39 (not_39_out, op3);
  not not_40 (not_40_out, op5);
  not not_41 (not_41_out, op0);
  not not_42 (not_42_out, op1);
  not not_43 (not_43_out, op2);
  not not_44 (not_44_out, op3);
  not not_45 (not_45_out, op1);
  not not_46 (not_46_out, op2);
  not not_47 (not_47_out, op3);
  not not_48 (not_48_out, op0);
  not not_49 (not_49_out, op1);
  not not_50 (not_50_out, op2);
  not not_51 (not_51_out, op4);
  not not_52 (not_52_out, op0);
  not not_53 (not_53_out, op1);
  not not_54 (not_54_out, op2);
  not not_55 (not_55_out, op4);
  not not_56 (not_56_out, op5);
  not not_57 (not_57_out, op0);
  not not_58 (not_58_out, op1);
  not not_59 (not_59_out, op2);
  not not_60 (not_60_out, op3);
  not not_61 (not_61_out, op4);
  not not_62 (not_62_out, op5);
  not not_63 (not_63_out, op0);
  not not_64 (not_64_out, op1);
  not not_65 (not_65_out, op2);
  not not_66 (not_66_out, op3);
  not not_67 (not_67_out, op4);
  not not_68 (not_68_out, op5);
  not not_69 (not_69_out, op0);
  not not_70 (not_70_out, op1);
  not not_71 (not_71_out, op3);
  not not_72 (not_72_out, op4);
  not not_73 (not_73_out, op5);
  not not_74 (not_74_out, op1);
  not not_75 (not_75_out, op2);
  not not_76 (not_76_out, op3);
  not not_77 (not_77_out, op0);
  not not_78 (not_78_out, op1);
  not not_79 (not_79_out, op4);
  not not_80 (not_80_out, op5);
  not not_81 (not_81_out, op0);
  not not_82 (not_82_out, op1);
  not not_83 (not_83_out, op4);
  not not_84 (not_84_out, op0);
  not not_85 (not_85_out, op1);
  not not_86 (not_86_out, op3);
  not not_87 (not_87_out, op5);
  not not_88 (not_88_out, op0);
  not not_89 (not_89_out, op1);
  not not_90 (not_90_out, op3);
  not not_91 (not_91_out, op4);
  not not_92 (not_92_out, op0);
  not not_93 (not_93_out, op1);
  not not_94 (not_94_out, op3);
  not not_95 (not_95_out, op4);
  not not_96 (not_96_out, op5);
  not not_97 (not_97_out, op0);
  not not_98 (not_98_out, op1);
  not not_99 (not_99_out, op2);
  not not_100 (not_100_out, op3);
  not not_101 (not_101_out, op0);
  not not_102 (not_102_out, op2);
  not not_103 (not_103_out, op3);
  not not_104 (not_104_out, op4);
  not not_105 (not_105_out, op5);
  not not_106 (not_106_out, op0);
  not not_107 (not_107_out, op1);
  not not_108 (not_108_out, op2);
  not not_109 (not_109_out, op4);
  not not_110 (not_110_out, op0);
  not not_111 (not_111_out, op1);
  not not_112 (not_112_out, op2);
  not not_113 (not_113_out, op3);
  not not_114 (not_114_out, op0);
  not not_115 (not_115_out, op1);
  not not_116 (not_116_out, op3);
  not not_117 (not_117_out, op4);
  and and_1 (MemRead, op0, not_1_out, not_2_out, not_3_out, op4, op5);
  and and_2 (MemWrite, op0, not_4_out, op2, not_5_out, op4, op5);
  and and_3 (and_3_out, not_6_out, not_7_out, op2, not_8_out, not_9_out, not_10_out);
  and and_4 (and_4_out, op0, not_11_out, not_12_out, not_13_out, op4, op5);
  and and_5 (and_5_out, op0, not_14_out, op2, not_15_out, op4, op5);
  and and_6 (and_6_out, not_16_out, not_17_out, op2, op3, not_18_out, not_19_out);
  and and_7 (and_7_out, not_20_out, not_21_out, op2, op3, not_22_out, op5);
  and and_8 (and_8_out, not_23_out, not_24_out, op2, not_25_out, op4, not_26_out);
  and and_9 (and_9_out, not_27_out, not_28_out, op2, not_29_out, not_30_out, op5);
  and and_10 (and_10_out, not_31_out, not_32_out, op2, not_33_out, not_34_out, not_35_out);
  and and_11 (and_11_out, not_36_out, not_37_out, not_38_out, not_39_out, op4, not_40_out);
  and and_12 (and_12_out, not_41_out, not_42_out, not_43_out, not_44_out, op4, op5);
  and and_13 (MemtoReg, op0, not_45_out, not_46_out, not_47_out, op4, op5);
  and and_14 (and_14_out, not_48_out, not_49_out, not_50_out, op3, not_51_out, op5);
  and and_15 (and_15_out, not_52_out, not_53_out, not_54_out, op3, not_55_out, not_56_out);
  and and_16 (RegDst, not_57_out, not_58_out, not_59_out, not_60_out, not_61_out, not_62_out);
  and and_17 (and_17_out, not_63_out, not_64_out, not_65_out, not_66_out, not_67_out, not_68_out);
  and and_18 (and_18_out, not_69_out, not_70_out, op2, not_71_out, not_72_out, not_73_out);
  and and_19 (and_19_out, op0, not_74_out, not_75_out, not_76_out, op4, op5);
  and and_20 (and_20_out, not_77_out, not_78_out, op2, op3, not_79_out, not_80_out);
  and and_21 (and_21_out, not_81_out, not_82_out, op2, op3, not_83_out, op5);
  and and_22 (and_22_out, not_84_out, not_85_out, op2, not_86_out, op4, not_87_out);
  and and_23 (and_23_out, not_88_out, not_89_out, op2, not_90_out, not_91_out, op5);
  and and_24 (and_24_out, not_92_out, not_93_out, op2, not_94_out, not_95_out, not_96_out);
  and and_25 (and_25_out, not_97_out, not_98_out, not_99_out, not_100_out, op4, op5);
  and and_26 (and_26_out, not_101_out, op1, not_102_out, not_103_out, not_104_out, not_105_out);
  and and_27 (BneBeq, not_106_out, not_107_out, not_108_out, op3, not_109_out, op5);
  and and_28 (IsJAL, not_110_out, not_111_out, not_112_out, not_113_out, op4, op5);
  and and_29 (IsUnsigned, not_114_out, not_115_out, op2, not_116_out, not_117_out, op5);
  or or_1 (ALUSrc, and_3_out, and_4_out, and_5_out, and_6_out, and_7_out, and_8_out, and_9_out, and_10_out);
  or or_2 (Jump, and_11_out, and_12_out);
  or or_3 (Branch, and_14_out, and_15_out);
  or or_4 (RegWrite, and_17_out, and_18_out, and_19_out, and_20_out, and_21_out, and_22_out, and_23_out, and_24_out, and_25_out, and_26_out);
endmodule

module Syscall_Decoder (
  input  clk,
  input  Enable,
  input  [31:0] a0,
  input  [31:0] v0,
  output [31:0] Hex,
  output Halt
);

  wire comparator_1_eq, multiplexer_1_out;

  Comparator #(.width(32)) comparator_1 (.a(v0), .b(32'ha), .eq(comparator_1_eq));  // open: gt, lt
  Register #(.width(32)) register_1 (.D(a0), .en(Enable), .Q(Hex), .clk(clk));  // open: clr
  Multiplexer #(.enable("false")) multiplexer_1 (
    .in0(1'b0), .in1(comparator_1_eq), .out(multiplexer_1_out), .sel(Enable));
  D_Flip_Flop d_ff_1 (.clk(clk), .D(multiplexer_1_out), .Q(Halt));  // open: Qn, preset, en, reset
endmodule

module Statistics (
  input  op0,
  input  op1,
  input  op2,
  input  op3,
  input  op4,
  input  op5,
  output i,
  output r,
  output j
);

  wire and_1_out, and_2_out, and_3_out, and_4_out, and_5_out, and_6_out, and_7_out, and_8_out, and_9_out,
       and_10_out, and_12_out, and_13_out, not_1_out, not_2_out, not_3_out, not_4_out, not_5_out, not_6_out,
       not_7_out, not_8_out, not_9_out, not_10_out, not_11_out, not_12_out, not_13_out, not_14_out,
       not_15_out, not_16_out, not_17_out, not_18_out, not_19_out, not_20_out, not_21_out, not_22_out,
       not_23_out, not_24_out, not_25_out, not_26_out, not_27_out, not_28_out, not_29_out, not_30_out,
       not_31_out, not_32_out, not_33_out, not_34_out, not_35_out, not_36_out, not_37_out, not_38_out,
       not_39_out, not_40_out, not_41_out, not_42_out, not_43_out, not_44_out, not_45_out, not_46_out,
       not_47_out, not_48_out, not_49_out, not_50_out, not_51_out, not_52_out, not_53_out, not_54_out;

  not not_1 (not_1_out, op1);
  not not_2 (not_2_out, op2);
  not not_3 (not_3_out, op3);
  not not_4 (not_4_out, op1);
  not not_5 (not_5_out, op3);
  not not_6 (not_6_out, op0);
  not not_7 (not_7_out, op1);
  not not_8 (not_8_out, op2);
  not not_9 (not_9_out, op4);
  not not_10 (not_10_out, op0);
  not not_11 (not_11_out, op1);
  not not_12 (not_12_out, op2);
  not not_13 (not_13_out, op4);
  not not_14 (not_14_out, op5);
  not not_15 (not_15_out, op0);
  not not_16 (not_16_out, op1);
  not not_17 (not_17_out, op4);
  not not_18 (not_18_out, op5);
  not not_19 (not_19_out, op0);
  not not_20 (not_20_out, op1);
  not not_21 (not_21_out, op4);
  not not_22 (not_22_out, op0);
  not not_23 (not_23_out, op1);
  not not_24 (not_24_out, op3);
  not not_25 (not_25_out, op5);
  not not_26 (not_26_out, op0);
  not not_27 (not_27_out, op1);
  not not_28 (not_28_out, op3);
  not not_29 (not_29_out, op4);
  not not_30 (not_30_out, op5);
  not not_31 (not_31_out, op0);
  not not_32 (not_32_out, op1);
  not not_33 (not_33_out, op3);
  not not_34 (not_34_out, op4);
  not not_35 (not_35_out, op0);
  not not_36 (not_36_out, op1);
  not not_37 (not_37_out, op3);
  not not_38 (not_38_out, op4);
  not not_39 (not_39_out, op5);
  not not_40 (not_40_out, op0);
  not not_41 (not_41_out, op1);
  not not_42 (not_42_out, op2);
  not not_43 (not_43_out, op3);
  not not_44 (not_44_out, op4);
  not not_45 (not_45_out, op5);
  not not_46 (not_46_out, op0);
  not not_47 (not_47_out, op1);
  not not_48 (not_48_out, op2);
  not not_49 (not_49_out, op3);
  not not_50 (not_50_out, op5);
  not not_51 (not_51_out, op0);
  not not_52 (not_52_out, op1);
  not not_53 (not_53_out, op2);
  not not_54 (not_54_out, op3);
  and and_1 (and_1_out, op0, not_1_out, not_2_out, not_3_out, op4, op5);
  and and_2 (and_2_out, op0, not_4_out, op2, not_5_out, op4, op5);
  and and_3 (and_3_out, not_6_out, not_7_out, not_8_out, op3, not_9_out, op5);
  and and_4 (and_4_out, not_10_out, not_11_out, not_12_out, op3, not_13_out, not_14_out);
  and and_5 (and_5_out, not_15_out, not_16_out, op2, op3, not_17_out, not_18_out);
  and and_6 (and_6_out, not_19_out, not_20_out, op2, op3, not_21_out, op5);
  and and_7 (and_7_out, not_22_out, not_23_out, op2, not_24_out, op4, not_25_out);
  and and_8 (and_8_out, not_26_out, not_27_out, op2, not_28_out, not_29_out, not_30_out);
  and and_9 (and_9_out, not_31_out, not_32_out, op2, not_33_out, not_34_out, op5);
  and and_10 (and_10_out, not_35_out, not_36_out, op2, not_37_out, not_38_out, not_39_out);
  and and_11 (r, not_40_out, not_41_out, not_42_out, not_43_out, not_44_out, not_45_out);
  and and_12 (and_12_out, not_46_out, not_47_out, not_48_out, not_49_out, op4, not_50_out);
  and and_13 (and_13_out, not_51_out, not_52_out, not_53_out, not_54_out, op4, op5);
  or or_1 (j, and_12_out, and_13_out);
  or or_2 (i, and_1_out, and_2_out, and_3_out, and_4_out, and_5_out, and_6_out, and_7_out, and_8_out, and_9_out, and_10_out);
endmodule

module IF_ID (
  input  clk,
  input  [31:0] InstIF,
  input  [31:0] PCPlus4ID,
  output [31:0] InstID,
  output [31:0] PCPlus4IF
);
endmodule

module ID_EX (
  input  IsJALID,
  input  clk,
  input  IsShamtID,
  input  MemtoRegID,
  input  RegWriteID,
  input  BneOrBeqID,
  input  ALUSrcID,
  input  [4:0] WriteReg_ID,
  input  IsExceptionID,
  input  MemReadID,
  input  [31:0] ImmID,
  input  MemWriteID,
  input  JumpID,
  input  BranchID,
  input  [31:0] R1ID,
  input  IsJRID,
  input  IsSyscallID,
  input  [31:0] R2ID,
  input  [3:0] ALUopID,
  input  [31:0] ShamtID,
  input  [31:0] PCPlus4ID,
  input  [31:0] JumpAddr,
  output IsJALEX,
  output IsShamtEX,
  output MemtoRegEX,
  output RegWriteEX,
  output BneOrBeqEX,
  output ALUSrcEX,
  output [4:0] WriteReg_EX,
  output IsExceptionEX,
  output MemReadEX,
  output [31:0] ImmEX,
  output MemWriteEX,
  output JumpEX,
  output BranchEX,
  output [31:0] R1EX,
  output IsJREX,
  output IsSyscallEX,
  output [31:0] R2EX,
  output [3:0] ALUopEX,
  output [31:0] ShamtEX,
  output [31:0] PCPlusEX,
  output [31:0] JumpAddr_2
);
endmodule

module Regfile_Wrapper (
  input  [4:0] R1_num,
  input  [4:0] R2_num,
  input  [4:0] RW,
  input  WE,
  input  clk,
  input  [31:0] Din,
  output [31:0] R1,
  output [31:0] R2
);

  regfile_main main_1 (
    .Reg1_num(R1_num), .Reg2(R2_num), .Write_Reg_num(RW), .Din(Din), .Write_Enable(WE), .Clock(clk),
    .Reg1(R1), .Reg2_2(R2));  // open: v0_Value, s2_Value, ra_Value, a0_Value
endmodule

module ALU_Wrapper (
  input  [31:0] X,
  input  [31:0] Y,
  input  [3:0] AluOP,
  output [31:0] Result,
  output Equal,
  output [31:0] Result_2
);

  ALU alu_1 (
    .AluOP(AluOP), .X(X), .Equal(Equal), .Result(Result), .Y(Y), .Result_2(Result_2));  // open: Signed_Overflow, UnSigned_Overflow
endmodule
