// Logisim project Pipeline_CPU.circ as structural Verilog: 19 circuits, main circuit main
module main (
);

  wire alu_wrapper_1_equal, and_1_out, BranchSuccess, clk, clock_1_out, control_1_alusrc, control_1_bneorbeq,
       control_1_branch, control_1_isjal, control_1_isjr, control_1_isshamt, control_1_issyscall,
       control_1_jump, control_1_memread, control_1_memtoreg, control_1_memwrite, control_1_regwrite,
       cp0_1_iseret, ex_mem_1_isjalmem, ex_mem_1_issyscallmem, ex_mem_1_memreadmem, ex_mem_1_memwritemem,
       ExpBlock, ExpSrc0, ExpSrc1, ExpSrc2, ExRegWrite, Halt, HasExp, hazard_unit_1_flushid,
       hazard_unit_1_flushif, hazard_unit_1_stallid, hazard_unit_1_stallif, id_ex_1_alusrcex,
       id_ex_1_bneorbeqex, id_ex_1_branchex, id_ex_1_isshamtex, id_ex_1_issyscallex, id_ex_1_memtoregex,
       id_ex_1_memwriteex, IsCOP0, IsCOP0EX, IsCOP0MEM, IsEretEX, IsJALEX, IsJREX, JumpEX,
       mem_wb_1_isexceptionwb, mem_wb_1_isjalwb, mem_wb_1_issyscallwb, mem_wb_1_memtoregwb,
       mem_wb_1_regwritewb, MemReadEX, MemtoRegMEM, multiplexer_7_out, not_1_out, not_2_out, not_3_out,
       not_4_out, or_1_out, or_2_out, ReadRs, ReadRt, RegDstID, regwrite_decider_1_finalregwrite, RegWriteEX,
       RegWriteMEM, statistics_1_i, statistics_1_j, statistics_1_r, xor_1_out, ZeroExtendID;
  wire [1:0] RsOutput, RtOutput;
  wire [3:0] control_1_aluop, id_ex_1_aluopex, syscall_decoder_1_hex_2, syscall_decoder_1_hex_3,
       syscall_decoder_1_hex_4, syscall_decoder_1_hex_5, syscall_decoder_1_hex_6;
  wire [4:0] ex_mem_1_writereg_mem, id_ex_1_writereg_ex, mem_wb_1_writereg_wb, multiplexer_9_out,
       multiplexer_10_out, Rs, Rt;
  wire [5:0] multiplexer_8_out_2;
  wire [8:0] demultiplexer_1_out0, demultiplexer_1_out1;
  wire [11:0] syscall_decoder_1_hex;
  wire [25:0] multiplexer_8_out;
  wire [27:0] if_id_1_pcplus4if;
  wire [31:0] a0, adder_1_out, adder_2_out, alu_wrapper_1_result, bit_extender_1_out, counter_1_q,
       counter_2_q, counter_3_q, counter_4_q, cp0_1_dout, cp0_1_pcout, Cycle_q, ex_mem_1_aluresultmem,
       ex_mem_1_cp0dout_2, ex_mem_1_jumpaddrmem, ex_mem_1_writedatamem, hazard_unit_1_bubblenum,
       id_ex_1_cp0dout_2, id_ex_1_immex, id_ex_1_jumpaddr_2, id_ex_1_pcplusex, id_ex_1_r1ex, id_ex_1_r2ex,
       id_ex_1_shamtex, immediate_extend_1_output, mem_wb_1_aluresultwb, mem_wb_1_jumpaddrwb,
       mem_wb_1_jumpaddrwb_2, mem_wb_1_readdatawb, multiplexer_1_out, multiplexer_2_out, multiplexer_4_out,
       multiplexer_5_out, multiplexer_6_out, multiplexer_11_out, multiplexer_12_out, multiplexer_13_out,
       multiplexer_14_out, multiplexer_15_out, multiplexer_16_out, multiplexer_17_out, multiplexer_18_out,
       multiplexer_19_out, multiplexer_20_out, multiplexer_21_out, PC_q, ram_1_data, regfile_wrapper_1_r1,
       regfile_wrapper_1_r2, rom_1_data, rom_2_data, shifter_1_out, v0;
  wire [31:2] if_id_1_instid_2;
  wire [31:26] if_id_1_instid;

  Multiplexer #(.width(32), .enable("false")) multiplexer_1 (
    .in0(adder_1_out), .in1(adder_2_out), .out(multiplexer_1_out), .sel(BranchSuccess));
  Multiplexer #(.width(32), .enable("false")) multiplexer_2 (
    .in0(multiplexer_1_out), .in1(id_ex_1_jumpaddr_2), .out(multiplexer_2_out), .sel(JumpEX));
  Multiplexer #(.enable("false")) multiplexer_3 (.in0(clock_1_out), .in1(1'b0), .out(clk), .sel(Halt));
  Clock clock_1 (.out(clock_1_out));
  Multiplexer #(.width(32), .enable("false")) multiplexer_4 (
    .in0(multiplexer_2_out), .in1(id_ex_1_r1ex), .out(multiplexer_4_out), .sel(IsJREX));
  Multiplexer #(.width(32), .enable("false")) multiplexer_5 (
    .in0(multiplexer_4_out), .in1(cp0_1_pcout), .out(multiplexer_5_out), .sel(and_1_out));
  and and_1 (and_1_out, IsEretEX, IsCOP0EX);
  Counter #(.width(32), .max('hffffffff)) Cycle (.Q(Cycle_q), .clk(clk));  // open: load, D, count, carry, clr
  Multiplexer #(.width(32), .enable("false")) multiplexer_6 (
    .in0(multiplexer_5_out), .in1(32'h800), .out(multiplexer_6_out), .sel(HasExp));
  or or_1 (or_1_out, HasExp, and_1_out);
  not not_1 (not_1_out, hazard_unit_1_stallif);
  Hazard_Unit hazard_unit_1 (
    .clk(clk), .FlushIF(hazard_unit_1_flushif), .FlushID(hazard_unit_1_flushid), .IsToBranchOrJump(or_2_out),
    .WriteReg_MEM(ex_mem_1_writereg_mem), .RT(Rt), .RegWriteMEM(RegWriteMEM), .RS(Rs),
    .StallIF(hazard_unit_1_stallif), .StallID(hazard_unit_1_stallid), .WriteReg_EX(id_ex_1_writereg_ex),
    .RegWriteEX(RegWriteEX), .ReadRs(ReadRs), .ReadRt(ReadRt), .BubbleNum(hazard_unit_1_bubblenum),
    .RsOutput(RsOutput), .RtOutput(RtOutput), .IsLW(MemReadEX));
  Hex_Digit_Display hex_digit_display_1 (.value(syscall_decoder_1_hex_6));  // open: dp
  Hex_Digit_Display hex_digit_display_2 (.value(syscall_decoder_1_hex_5));  // open: dp
  Counter #(.width(32), .max('hffffffff)) counter_1 (
    .count(statistics_1_j), .Q(counter_1_q), .clk(clk));  // open: load, D, carry, clr
  // Probe on Cycle_q
  Register #(.width(32)) PC (.D(multiplexer_6_out), .en(not_1_out), .Q(PC_q), .clk(multiplexer_7_out));  // open: clr
  Multiplexer #(.enable("false")) multiplexer_7 (.in0(clk), .in1(not_2_out), .out(multiplexer_7_out), .sel(or_1_out));
  not not_2 (not_2_out, clk);
  Hex_Digit_Display hex_digit_display_3 (.value(syscall_decoder_1_hex_3));  // open: dp
  Hex_Digit_Display hex_digit_display_4 (.value(syscall_decoder_1_hex_4));  // open: dp
  Counter #(.width(32), .max('hffffffff)) counter_2 (
    .count(statistics_1_r), .Q(counter_2_q), .clk(clk));  // open: load, D, carry, clr
  // Probe on counter_1_q
  // Probe on counter_2_q
  Demultiplexer #(.width(9), .enable("false")) demultiplexer_1 (
    .out0(demultiplexer_1_out0), .out1(demultiplexer_1_out1), .in(PC_q[10:2]), .sel(PC_q[11]));
  Button button_1 (.out(ExpSrc0));
  Counter #(.width(32), .max('hffffffff)) counter_3 (
    .count(BranchSuccess), .Q(counter_3_q), .clk(clk));  // open: load, D, carry, clr
  // Probe on counter_3_q
  Hex_Digit_Display hex_digit_display_5 (.value(syscall_decoder_1_hex[11:8]));  // open: dp
  Hex_Digit_Display hex_digit_display_6 (.value(syscall_decoder_1_hex_2));  // open: dp
  Counter #(.width(32), .max('hffffffff)) counter_4 (
    .count(statistics_1_i), .Q(counter_4_q), .clk(clk));  // open: load, D, carry, clr
  // Probe on counter_4_q
  Button button_2 (.out(ExpSrc1));
  Hex_Digit_Display hex_digit_display_7 (.value(syscall_decoder_1_hex[7:4]));  // open: dp
  Hex_Digit_Display hex_digit_display_8 (.value(syscall_decoder_1_hex[3:0]));  // open: dp
  Statistics statistics_1 (
    .op0(multiplexer_8_out_2[5]), .op1(multiplexer_8_out_2[4]), .op2(multiplexer_8_out_2[3]),
    .op3(multiplexer_8_out_2[2]), .op4(multiplexer_8_out_2[1]), .op5(multiplexer_8_out_2[0]),
    .i(statistics_1_i), .r(statistics_1_r), .j(statistics_1_j));
  ROM #(.addrWidth(9), .dataWidth(32)) rom_1 (.addr(demultiplexer_1_out0), .data(rom_1_data));  // open: sel
  ROM #(.addrWidth(9), .dataWidth(32)) rom_2 (.addr(demultiplexer_1_out1), .data(rom_2_data));  // open: sel
  Button button_3 (.out(ExpSrc2));
  Adder #(.width(32)) adder_1 (.a(PC_q), .b(32'h4), .out(adder_1_out));  // open: cin, cout
  // Probe on hazard_unit_1_bubblenum
  IF_ID if_id_1 (
    .InstIF({multiplexer_8_out_2, multiplexer_8_out}),
    .InstID({if_id_1_instid, Rs, Rt, if_id_1_instid_2[17:2]}), .clk(clk), .En(not_3_out),
    .clr(hazard_unit_1_flushif), .PCPlus4ID(adder_1_out),
    .PCPlus4IF({if_id_1_instid_2[31:28], if_id_1_pcplus4if}));
  Multiplexer #(.width(32), .enable("false")) multiplexer_8 (
    .in0(rom_1_data), .in1(rom_2_data), .out({multiplexer_8_out_2, multiplexer_8_out}), .sel(PC_q[11]));
  not not_3 (not_3_out, hazard_unit_1_stallid);
  Control control_1 (
    .op(if_id_1_instid), .Funct(if_id_1_instid_2[7:2]), .ALUop(control_1_aluop), .IsJAL(control_1_isjal),
    .IsShamt(control_1_isshamt), .MemtoReg(control_1_memtoreg), .RegWrite(control_1_regwrite),
    .MemRead(control_1_memread), .MemWrite(control_1_memwrite), .Jump(control_1_jump),
    .Branch(control_1_branch), .RegDst(RegDstID), .BneOrBeq(control_1_bneorbeq), .ALUSrc(control_1_alusrc),
    .IsJR(control_1_isjr), .IsSyscall(control_1_issyscall), .IsCOP0(IsCOP0), .ZeroExtend(ZeroExtendID),
    .ReadRs(ReadRs), .ReadRt(ReadRt));
  Immediate_Extend immediate_extend_1 (
    .Input(if_id_1_instid_2[17:2]), .Output(immediate_extend_1_output), .ZeroExtend(ZeroExtendID));
  Multiplexer #(.width(5), .enable("false")) multiplexer_9 (
    .in0(Rt), .in1(if_id_1_instid_2[17:13]), .out(multiplexer_9_out), .sel(RegDstID));
  CP0 cp0_1 (
    .ExpSrc0(ExpSrc0), .clk(clk), .ExpSrc1(ExpSrc1), .enable(IsCOP0), .ExpSrc2(ExpSrc2),
    .Inst({if_id_1_instid, Rs, Rt, if_id_1_instid_2[17:2]}), .PCin(PC_q), .Din(multiplexer_12_out),
    .ExRegWrite(ExRegWrite), .IsEret(cp0_1_iseret), .ExpBlock(ExpBlock), .HasExp(HasExp),
    .PCout(cp0_1_pcout), .Dout(cp0_1_dout));
  Multiplexer #(.width(5), .enable("false")) multiplexer_10 (
    .in0(multiplexer_9_out), .in1({5{1'b1}}), .out(multiplexer_10_out), .sel(control_1_isjal));
  not not_4 (not_4_out, clk);
  Regfile_Wrapper regfile_wrapper_1 (
    .R1_num(Rs), .R2_num(Rt), .RW(mem_wb_1_writereg_wb), .R1(regfile_wrapper_1_r1),
    .R2(regfile_wrapper_1_r2), .Din(multiplexer_21_out), .WE(mem_wb_1_regwritewb), .clk(not_4_out), .v0(v0),
    .a0(a0));
  assign bit_extender_1_out = {{27{1'b0}}, if_id_1_instid_2[12:8]};  // Bit_Extender bit_extender_1
  RegWrite_Decider regwrite_decider_1 (
    .RegWrite(control_1_regwrite), .ExRegWrite(ExRegWrite), .FinalRegWrite(regwrite_decider_1_finalregwrite),
    .IsException(IsCOP0));
  Multiplexer #(.select(2), .width(32), .enable("false")) multiplexer_11 (
    .in0(regfile_wrapper_1_r1), .in1(multiplexer_16_out), .in2(multiplexer_18_out), .out(multiplexer_11_out),
    .sel(RsOutput));  // open: in3
  Multiplexer #(.select(2), .width(32), .enable("false")) multiplexer_12 (
    .in0(regfile_wrapper_1_r2), .in1(multiplexer_16_out), .in2(multiplexer_18_out), .out(multiplexer_12_out),
    .sel(RtOutput));  // open: in3
  ID_EX id_ex_1 (
    .clk(clk), .IsJALID(control_1_isjal), .MemReadID(control_1_memread), .IsShamtID(control_1_isshamt),
    .MemWriteID(control_1_memwrite), .MemtoRegID(control_1_memtoreg), .JumpID(control_1_jump),
    .RegWriteID(regwrite_decider_1_finalregwrite), .BranchID(control_1_branch),
    .BneOrBeqID(control_1_bneorbeq), .ALUSrcID(control_1_alusrc), .IsJRID(control_1_isjr),
    .IsExceptionID(IsCOP0), .IsJALEX(IsJALEX), .MemReadEX(MemReadEX), .IsShamtEX(id_ex_1_isshamtex),
    .MemWriteEX(id_ex_1_memwriteex), .MemtoRegEX(id_ex_1_memtoregex), .JumpEX(JumpEX),
    .RegWriteEX(RegWriteEX), .BranchEX(id_ex_1_branchex), .BneOrBeqEX(id_ex_1_bneorbeqex),
    .ALUSrcEX(id_ex_1_alusrcex), .IsJREX(IsJREX), .IsExceptionEX(IsCOP0EX), .ALUopID(control_1_aluop),
    .ALUopEX(id_ex_1_aluopex), .WriteReg_ID(multiplexer_10_out), .WriteReg_EX(id_ex_1_writereg_ex),
    .ImmID(immediate_extend_1_output), .ImmEX(id_ex_1_immex), .R1ID(multiplexer_11_out), .R1EX(id_ex_1_r1ex),
    .R2ID(multiplexer_12_out), .R2EX(id_ex_1_r2ex), .PCPlus4ID({if_id_1_instid_2[31:28], if_id_1_pcplus4if}),
    .PCPlusEX(id_ex_1_pcplusex), .ShamtID(bit_extender_1_out), .ShamtEX(id_ex_1_shamtex),
    .JumpAddr({if_id_1_instid_2[31:28], Rs, Rt, if_id_1_instid_2[17:2], 2'b00}),
    .JumpAddr_2(id_ex_1_jumpaddr_2), .IsSyscallID(control_1_issyscall), .IsSyscallEX(id_ex_1_issyscallex),
    .clr(hazard_unit_1_flushid), .En(1'b1), .CP0Dout(cp0_1_dout), .CP0Dout_2(id_ex_1_cp0dout_2),
    .IsEret(cp0_1_iseret), .IsEret_2(IsEretEX));
  Multiplexer #(.width(32), .enable("false")) multiplexer_13 (
    .in0(id_ex_1_r1ex), .in1(id_ex_1_r2ex), .out(multiplexer_13_out), .sel(id_ex_1_isshamtex));
  Multiplexer #(.width(32), .enable("false")) multiplexer_14 (
    .in0(id_ex_1_r2ex), .in1(id_ex_1_shamtex), .out(multiplexer_14_out), .sel(id_ex_1_isshamtex));
  Adder #(.width(32)) adder_2 (.a(id_ex_1_pcplusex), .b(shifter_1_out), .out(adder_2_out));  // open: cin, cout
  Shifter #(.width(32)) shifter_1 (.in(id_ex_1_immex), .\dist (5'b00010), .out(shifter_1_out));
  ALU_Wrapper alu_wrapper_1 (
    .X(multiplexer_13_out), .Y(multiplexer_15_out), .AluOP(id_ex_1_aluopex), .Equal(alu_wrapper_1_equal),
    .Result(alu_wrapper_1_result));
  Multiplexer #(.width(32), .enable("false")) multiplexer_15 (
    .in0(multiplexer_14_out), .in1(id_ex_1_immex), .out(multiplexer_15_out), .sel(id_ex_1_alusrcex));
  or or_2 (or_2_out, JumpEX, IsEretEX, BranchSuccess, IsJREX, IsJALEX);
  and and_2 (BranchSuccess, id_ex_1_branchex, xor_1_out);
  xor xor_1 (xor_1_out, id_ex_1_bneorbeqex, alu_wrapper_1_equal);
  Multiplexer #(.width(32), .enable("false")) multiplexer_16 (
    .in0(alu_wrapper_1_result), .in1(id_ex_1_cp0dout_2), .out(multiplexer_16_out), .sel(IsCOP0EX));
  EX_MEM ex_mem_1 (
    .MemReadEX(MemReadEX), .MemReadMEM(ex_mem_1_memreadmem), .MemWriteEX(id_ex_1_memwriteex),
    .MemWriteMEM(ex_mem_1_memwritemem), .IsExceptionEX(IsCOP0EX), .IsExceptionMEM(IsCOP0MEM),
    .IsJALEX(IsJALEX), .IsJALMEM(ex_mem_1_isjalmem), .RegWriteEX(RegWriteEX), .RegWriteMEM(RegWriteMEM),
    .MemtoRegEX(id_ex_1_memtoregex), .MemtoRegMEM(MemtoRegMEM), .clk(clk), .IsSyscallEX(id_ex_1_issyscallex),
    .IsSyscallMEM(ex_mem_1_issyscallmem), .ALUResultEX(alu_wrapper_1_result),
    .ALUResultMEM(ex_mem_1_aluresultmem), .WriteDataEX(id_ex_1_r2ex), .WriteDataMEM(ex_mem_1_writedatamem),
    .JumpAddrEX(id_ex_1_pcplusex), .JumpAddrMEM(ex_mem_1_jumpaddrmem), .WriteReg_EX(id_ex_1_writereg_ex),
    .WriteReg_MEM(ex_mem_1_writereg_mem), .clr(1'b0), .En(1'b1), .CP0Dout(id_ex_1_cp0dout_2),
    .CP0Dout_2(ex_mem_1_cp0dout_2));
  Multiplexer #(.width(32), .enable("false")) multiplexer_17 (
    .in0(ex_mem_1_aluresultmem), .in1(ram_1_data), .out(multiplexer_17_out), .sel(MemtoRegMEM));
  Multiplexer #(.width(32), .enable("false")) multiplexer_18 (
    .in0(multiplexer_17_out), .in1(ex_mem_1_cp0dout_2), .out(multiplexer_18_out), .sel(IsCOP0MEM));
  RAM #(.addrWidth(10), .dataWidth(32), .bus("separate")) ram_1 (
    .addr(ex_mem_1_aluresultmem[11:2]), .din(ex_mem_1_writedatamem), .data(ram_1_data),
    .str(ex_mem_1_memwritemem), .clk(clk), .ld(ex_mem_1_memreadmem));  // open: sel, clr
  MEM_WB mem_wb_1 (
    .IsJALMEM(ex_mem_1_isjalmem), .clk(clk), .MemtoRegMEM(MemtoRegMEM), .RegWriteMEM(RegWriteMEM),
    .IsExceptionMEM(IsCOP0MEM), .IsJALWB(mem_wb_1_isjalwb), .MemtoRegWB(mem_wb_1_memtoregwb),
    .RegWriteWB(mem_wb_1_regwritewb), .IsExceptionWB(mem_wb_1_isexceptionwb),
    .ALUResultMEM(ex_mem_1_aluresultmem), .ALUResultWB(mem_wb_1_aluresultwb), .JumpAddrMEM(ram_1_data),
    .JumpAddrWB(mem_wb_1_jumpaddrwb), .ReadDataMEM(ex_mem_1_jumpaddrmem), .ReadDataWB(mem_wb_1_readdatawb),
    .WriteReg_MEM(ex_mem_1_writereg_mem), .WriteReg_WB(mem_wb_1_writereg_wb),
    .IsSyscallMEM(ex_mem_1_issyscallmem), .IsSyscallWB(mem_wb_1_issyscallwb), .clr(1'b0), .En(1'b1),
    .JumpAddrMEM_2(ex_mem_1_cp0dout_2), .JumpAddrWB_2(mem_wb_1_jumpaddrwb_2));
  Syscall_Decoder syscall_decoder_1 (
    .v0(v0), .a0(a0), .Enable(mem_wb_1_issyscallwb),
    .Hex({syscall_decoder_1_hex_6, syscall_decoder_1_hex_5, syscall_decoder_1_hex_4, syscall_decoder_1_hex_3, syscall_decoder_1_hex_2, syscall_decoder_1_hex}),
    .Halt(Halt), .clk(clk));
  Multiplexer #(.width(32), .enable("false")) multiplexer_19 (
    .in0(mem_wb_1_aluresultwb), .in1(mem_wb_1_jumpaddrwb_2), .out(multiplexer_19_out),
    .sel(mem_wb_1_isexceptionwb));
  Multiplexer #(.width(32), .enable("false")) multiplexer_20 (
    .in0(multiplexer_19_out), .in1(mem_wb_1_jumpaddrwb), .out(multiplexer_20_out), .sel(mem_wb_1_memtoregwb));
  Multiplexer #(.width(32), .enable("false")) multiplexer_21 (
    .in0(multiplexer_20_out), .in1(mem_wb_1_readdatawb), .out(multiplexer_21_out), .sel(mem_wb_1_isjalwb));

  // Notes on the sheet:
  //   Screen
  //   contents of rom_1 (hex, n*v repeats v):
  //   20110001 8000c05 20110001 20120002 20130003 8000c09 20110001 20120002 20130003 8000c0d 20110001
  //   20120002 20130003 8000c11 20110001 20120002 20130003 c000d2e 20100001 20110001 118fc0 112020
  //   20020022 c 118882 12200001 8000c15 112020 20020022 c 20110001 118880 112020 20020022 c 12200001
  //   8000c1f 20110001 118fc0 112020 20020022 c 1188c3 112020 20020022 c 118903 112020 20020022 c 118903
  //   112020 20020022 c 118903 112020 20020022 c 118903 112020 20020022 c 118903 112020 20020022 c 118903
  //   112020 20020022 c 118903 112020 20020022 c 20100001 109fc0 139fc3 8021 2012000c 24160003 26100001
  //   3210000f 20080008 20090001 139900 2709825 132020 20020022 c 1094022 1500fff9 22100001 2018000f
  //   2188024 108700 20080008 20090001 139902 2709825 132021 20020022 c 1094022 1500fff9 108702 2c9b022
  //   12c00001 8000c50 4020 1084027 84400 3508ffff 82021 20020022 c 20110004 ae310000 8e320000 2252fffc
  //   20100000 22110001 2118020 22520004 ae500000 22310001 2118020 22520004 ae500000 22310001 2118020
  //   22520004 ae500000 22310001 2118020 22520004 ae500000 22310001 2118020 22520004 ae500000 22310001
  //   2118020 22520004 ae500000 22310001 2118020 22520004 ae500000 20090001 8c080004 1509008f ac000004
  //   20090003 8c080008 1509008b ac000008 20090006 8c08000c 15090087 ac00000c 2009000a 8c080010 15090083
  //   ac000010 2009000f 8c080014 1509007f ac000014 20090015 8c080018 1509007b ac000018 2009001c 8c08001c
  //   15090077 ac00001c 2010ffff 20110000 ae300000 22100001 22310004 ae300000 22100001 22310004 ae300000
  //   22100001 22310004 ae300000 22100001 22310004 ae300000 22100001 22310004 ae300000 22100001 22310004
  //   ae300000 22100001 22310004 ae300000 22100001 22310004 ae300000 22100001 22310004 ae300000 22100001
  //   22310004 ae300000 22100001 22310004 ae300000 22100001 22310004 ae300000 22100001 22310004 ae300000
  //   22100001 22310004 ae300000 22100001 22310004 ae300000 22100001 22310004 22100001 8020 2011003c
  //   8e130000 8e340000 274402a 11000002 ae330000 ae140000 2231fffc 1611fff8 102020 20020022 c 22100004
  //   2011003c 1611fff2 20100001 201200ff 20110001 20130003 12120005 12100004 20110001 20120002 20130003
  //   8000d26 102020 20020001 c 16310005 16320004 20110001 20120002 20130003 8000d26 132020 20020001 c
  //   2011ffff 118c00 2020 24840064 2484ff9c 14800017 2020 2484ff9c 24840064 14800013 2020 34847fff 912024
  //   1480000f 2020 34848000 912024 1480000b 24040000 8000d20 8000d26 2002000a c 20041ced 42400 3484cafe
  //   20020022 c 8000d1e 3c010000 3421baad 12020 42400 3484c0de 20020022 c 8000d1e 20100000 22100001
  //   102020 20020022 c 22100002 102020 20020022 c 22100003 102020 20020022 c 22100004 102020 20020022 c
  //   22100005 102020 20020022 c 22100006 102020 20020022 c 22100007 102020 20020022 c 22100008 102020
  //   20020022 c 3e00008
  //   contents of rom_2 (hex, n*v repeats v):
  //   201a0001 409a0800 201c0400 39df020 401a0000 afda0000 23de0004 23bd0004 401b1000 401a1800 409a1000
  //   afd00000 23bd0004 23de0004 afd40000 23bd0004 23de0004 afd50000 23bd0004 23de0004 afd60000 23bd0004
  //   23de0004 afc40000 23bd0004 23de0004 afc20000 23bd0004 23de0004 afdb0000 23bd0004 23de0004 1ab020
  //   22d60001 201a0000 409a0800 20140005 20150001 168020 102020 20020022 c 108100 1600fffb 295a022
  //   1680fff8 201a0001 409a0800 23defffc 23bdfffc 8fdb0000 23defffc 23bdfffc 8fc20000 23defffc 23bdfffc
  //   8fc40000 23defffc 23bdfffc 8fd60000 23defffc 23bdfffc 8fd50000 23defffc 23bdfffc 8fd40000 23defffc
  //   23bdfffc 8fd00000 409b1000 23defffc 23bdfffc 8fda0000 409a0000 201a0000 409a0800 42000018
  //   PCPlus4IF
  //   OP
  //   Funct
  //   RS
  //   RT
  //   RD
  //   JR Addr
  //   Jump Addr
  //   Branch Addr
  //   Shamt
  //   WriteReg#
  //   JumpAddr
  //   Immediate
  //   PCPlus4ID
  //   IsEret
  //   ALU Result
  //   Memory Result
  //   IsToBranchOrJump
  //   WriteDataEX
  //   WriteReg#MEM
  //   WriteReg#WB
  //   WB_DATA
endmodule

module Control (
  input  [5:0] op,
  input  [5:0] Funct,
  output IsJAL,
  output MemRead,
  output IsShamt,
  output MemWrite,
  output MemtoReg,
  output Jump,
  output RegWrite,
  output Branch,
  output BneOrBeq,
  output RegDst,
  output [3:0] ALUop,
  output ALUSrc,
  output IsJR,
  output IsSyscall,
  output IsCOP0,
  output ReadRs,
  output ZeroExtend,
  output ReadRt
);

  wire funct_decoder_1_isjr, funct_decoder_1_isshamt, funct_decoder_1_issyscall, IsSpecial, not_1_out;
  wire [3:0] alu_decoder_1_aluop3, funct_decoder_1_alu3;

  Opcode_Decoder opcode_decoder_1 (
    .op0(op[5]), .MemRead(MemRead), .op1(op[4]), .op2(op[3]), .MemWrite(MemWrite), .op3(op[2]), .op4(op[1]),
    .op5(op[0]), .ALUSrc(ALUSrc), .Jump(Jump), .MemtoReg(MemtoReg), .Branch(Branch), .RegDst(RegDst),
    .RegWrite(RegWrite), .BneBeq(BneOrBeq), .IsJAL(IsJAL), .ZeroExtend(ZeroExtend));
  RegisterRead_Detector registerread_detector_1 (
    .op0(op[5]), .op1(op[4]), .op2(op[3]), .op3(op[2]), .op4(op[1]), .op5(op[0]), .Funct0(Funct[5]),
    .Funct1(Funct[4]), .Funct2(Funct[3]), .Funct3(Funct[2]), .Funct4(Funct[1]), .Funct5(Funct[0]),
    .ReadRs(ReadRs), .ReadRt(ReadRt));
  Funct_Decoder funct_decoder_1 (
    .Funct0(Funct[5]), .Funct1(Funct[4]), .Funct2(Funct[3]), .Funct3(Funct[2]),
    .ALU0(funct_decoder_1_alu3[3]), .Funct4(Funct[1]), .Funct5(Funct[0]), .ALU1(funct_decoder_1_alu3[2]),
    .ALU2(funct_decoder_1_alu3[1]), .ALU3(funct_decoder_1_alu3[0]), .IsJR(funct_decoder_1_isjr),
    .IsSyscall(funct_decoder_1_issyscall), .IsShamt(funct_decoder_1_isshamt));
  ALU_Decoder alu_decoder_1 (
    .op0(op[5]), .op1(op[4]), .op2(op[3]), .ALUop0(alu_decoder_1_aluop3[3]), .op3(op[2]), .op4(op[1]),
    .op5(op[0]), .ALUop1(alu_decoder_1_aluop3[2]), .ALUop2(alu_decoder_1_aluop3[1]),
    .ALUop3(alu_decoder_1_aluop3[0]));
  Multiplexer #(.enable("false")) multiplexer_1 (
    .in0(1'b0), .in1(funct_decoder_1_issyscall), .out(IsSyscall), .sel(IsSpecial));
  Multiplexer #(.enable("false")) multiplexer_2 (.in0(1'b0), .in1(funct_decoder_1_isjr), .out(IsJR), .sel(IsSpecial));
  Multiplexer #(.enable("false")) multiplexer_3 (
    .in0(1'b0), .in1(funct_decoder_1_isshamt), .out(IsShamt), .sel(IsSpecial));
  not not_1 (not_1_out, IsSpecial);
  Multiplexer #(.width(4), .enable("false")) multiplexer_4 (
    .in0(funct_decoder_1_alu3), .in1(alu_decoder_1_aluop3), .out(ALUop), .sel(not_1_out));
  and and_1 (IsCOP0, ~op[5], op[4], ~op[3], ~op[2], ~op[1], ~op[0]);  // AND_Gate
  and and_2 (IsSpecial, ~op[5], ~op[4], ~op[3], ~op[2], ~op[1], ~op[0]);  // AND_Gate

  // Notes on the sheet:
  //   Input & Output
  //   OP Decoding Area
  //   ALU Decoding Area
  //   Exception Handler
endmodule

module Funct_Decoder (
  input  Funct0,
  input  Funct1,
  input  Funct2,
  input  Funct3,
  input  Funct4,
  input  Funct5,
  output ALU0,
  output ALU1,
  output ALU2,
  output ALU3,
  output IsJR,
  output IsSyscall,
  output IsShamt
);

  wire and_1_out, and_2_out, and_3_out, and_4_out, and_5_out, and_6_out, and_7_out, and_8_out, and_9_out,
       and_10_out, and_11_out, and_12_out, and_13_out, and_14_out, and_15_out, and_16_out, and_17_out,
       and_20_out, and_21_out, and_22_out, not_1_out, not_2_out, not_3_out, not_4_out, not_5_out, not_6_out,
       not_7_out, not_8_out, not_9_out, not_10_out, not_11_out, not_12_out, not_13_out, not_14_out,
       not_15_out, not_16_out, not_17_out, not_18_out, not_19_out, not_20_out, not_21_out, not_22_out,
       not_23_out, not_24_out, not_25_out, not_26_out, not_27_out, not_28_out, not_29_out, not_30_out,
       not_31_out, not_32_out, not_33_out, not_34_out, not_35_out, not_36_out, not_37_out, not_38_out,
       not_39_out, not_40_out, not_41_out, not_42_out, not_43_out, not_44_out, not_45_out, not_46_out,
       not_47_out, not_48_out, not_49_out, not_50_out, not_51_out, not_52_out, not_53_out, not_54_out,
       not_55_out, not_56_out, not_57_out, not_58_out, not_59_out, not_60_out, not_61_out, not_62_out,
       not_63_out, not_64_out, not_65_out, not_66_out, not_67_out, not_68_out, not_69_out, not_70_out,
       not_71_out, not_72_out, not_73_out, not_74_out, not_75_out, not_76_out, not_77_out, not_78_out,
       not_79_out, not_80_out, not_81_out;

  not not_1 (not_1_out, Funct1);
  not not_2 (not_2_out, Funct2);
  not not_3 (not_3_out, Funct4);
  not not_4 (not_4_out, Funct1);
  not not_5 (not_5_out, Funct2);
  not not_6 (not_6_out, Funct1);
  not not_7 (not_7_out, Funct3);
  not not_8 (not_8_out, Funct5);
  not not_9 (not_9_out, Funct1);
  not not_10 (not_10_out, Funct3);
  not not_11 (not_11_out, Funct1);
  not not_12 (not_12_out, Funct2);
  not not_13 (not_13_out, Funct3);
  not not_14 (not_14_out, Funct4);
  not not_15 (not_15_out, Funct1);
  not not_16 (not_16_out, Funct2);
  not not_17 (not_17_out, Funct3);
  not not_18 (not_18_out, Funct5);
  not not_19 (not_19_out, Funct1);
  not not_20 (not_20_out, Funct2);
  not not_21 (not_21_out, Funct4);
  not not_22 (not_22_out, Funct5);
  not not_23 (not_23_out, Funct1);
  not not_24 (not_24_out, Funct3);
  not not_25 (not_25_out, Funct1);
  not not_26 (not_26_out, Funct2);
  not not_27 (not_27_out, Funct3);
  not not_28 (not_28_out, Funct5);
  not not_29 (not_29_out, Funct1);
  not not_30 (not_30_out, Funct2);
  not not_31 (not_31_out, Funct4);
  not not_32 (not_32_out, Funct5);
  not not_33 (not_33_out, Funct0);
  not not_34 (not_34_out, Funct1);
  not not_35 (not_35_out, Funct2);
  not not_36 (not_36_out, Funct3);
  not not_37 (not_37_out, Funct5);
  not not_38 (not_38_out, Funct1);
  not not_39 (not_39_out, Funct2);
  not not_40 (not_40_out, Funct1);
  not not_41 (not_41_out, Funct3);
  not not_42 (not_42_out, Funct5);
  not not_43 (not_43_out, Funct0);
  not not_44 (not_44_out, Funct1);
  not not_45 (not_45_out, Funct2);
  not not_46 (not_46_out, Funct3);
  not not_47 (not_47_out, Funct1);
  not not_48 (not_48_out, Funct2);
  not not_49 (not_49_out, Funct3);
  not not_50 (not_50_out, Funct4);
  not not_51 (not_51_out, Funct1);
  not not_52 (not_52_out, Funct2);
  not not_53 (not_53_out, Funct4);
  not not_54 (not_54_out, Funct5);
  not not_55 (not_55_out, Funct1);
  not not_56 (not_56_out, Funct3);
  not not_57 (not_57_out, Funct5);
  not not_58 (not_58_out, Funct0);
  not not_59 (not_59_out, Funct1);
  not not_60 (not_60_out, Funct3);
  not not_61 (not_61_out, Funct4);
  not not_62 (not_62_out, Funct5);
  not not_63 (not_63_out, Funct0);
  not not_64 (not_64_out, Funct1);
  not not_65 (not_65_out, Funct4);
  not not_66 (not_66_out, Funct5);
  not not_67 (not_67_out, Funct0);
  not not_68 (not_68_out, Funct1);
  not not_69 (not_69_out, Funct2);
  not not_70 (not_70_out, Funct3);
  not not_71 (not_71_out, Funct0);
  not not_72 (not_72_out, Funct1);
  not not_73 (not_73_out, Funct2);
  not not_74 (not_74_out, Funct3);
  not not_75 (not_75_out, Funct5);
  not not_76 (not_76_out, Funct0);
  not not_77 (not_77_out, Funct1);
  not not_78 (not_78_out, Funct2);
  not not_79 (not_79_out, Funct3);
  not not_80 (not_80_out, Funct4);
  not not_81 (not_81_out, Funct5);
  and and_1 (and_1_out, Funct0, not_1_out, not_2_out, Funct3, not_3_out, Funct5);
  and and_2 (and_2_out, Funct0, not_4_out, not_5_out, Funct3, Funct4, Funct5);
  and and_3 (and_3_out, Funct0, not_6_out, Funct2, not_7_out, Funct4, not_8_out);
  and and_4 (and_4_out, Funct0, not_9_out, Funct2, not_10_out, Funct4, Funct5);
  and and_5 (and_5_out, Funct0, not_11_out, not_12_out, not_13_out, not_14_out);
  and and_6 (and_6_out, Funct0, not_15_out, not_16_out, not_17_out, not_18_out);
  and and_7 (and_7_out, Funct0, not_19_out, not_20_out, not_21_out, not_22_out);
  and and_8 (and_8_out, Funct0, not_23_out, Funct2, not_24_out, Funct4, Funct5);
  and and_9 (and_9_out, Funct0, not_25_out, not_26_out, not_27_out, Funct4, not_28_out);
  and and_10 (and_10_out, Funct0, not_29_out, not_30_out, Funct3, not_31_out, not_32_out);
  and and_11 (and_11_out, not_33_out, not_34_out, not_35_out, not_36_out, Funct4, not_37_out);
  and and_12 (and_12_out, Funct0, not_38_out, not_39_out, Funct3, Funct4, Funct5);
  and and_13 (and_13_out, Funct0, not_40_out, Funct2, not_41_out, Funct4, not_42_out);
  and and_14 (and_14_out, not_43_out, not_44_out, not_45_out, not_46_out, Funct4, Funct5);
  and and_15 (and_15_out, Funct0, not_47_out, not_48_out, not_49_out, not_50_out);
  and and_16 (and_16_out, Funct0, not_51_out, not_52_out, not_53_out, not_54_out);
  and and_17 (and_17_out, Funct0, not_55_out, Funct2, not_56_out, Funct4, not_57_out);
  and and_18 (IsJR, not_58_out, not_59_out, Funct2, not_60_out, not_61_out, not_62_out);
  and and_19 (IsSyscall, not_63_out, not_64_out, Funct2, Funct3, not_65_out, not_66_out);
  and and_20 (and_20_out, not_67_out, not_68_out, not_69_out, not_70_out, Funct4, Funct5);
  and and_21 (and_21_out, not_71_out, not_72_out, not_73_out, not_74_out, Funct4, not_75_out);
  and and_22 (and_22_out, not_76_out, not_77_out, not_78_out, not_79_out, not_80_out, not_81_out);
  or or_1 (ALU0, and_1_out, and_2_out, and_3_out, and_4_out);
  or or_2 (ALU1, and_5_out, and_6_out, and_7_out, and_8_out);
  or or_3 (ALU2, and_9_out, and_10_out, and_11_out, and_12_out, and_13_out);
  or or_4 (ALU3, and_14_out, and_15_out, and_16_out, and_17_out);
  or or_5 (IsShamt, and_20_out, and_21_out, and_22_out);
endmodule

module ALU_Decoder (
  input  op0,
  input  op1,
  input  op2,
  input  op3,
  input  op4,
  input  op5,
  output ALUop0,
  output ALUop1,
  output ALUop2,
  output ALUop3
);

  wire and_1_out, and_2_out, and_3_out, and_4_out, and_5_out, and_6_out, and_7_out, and_8_out, and_9_out,
       and_10_out, and_11_out, and_12_out, and_13_out, and_14_out, and_15_out, and_16_out, and_17_out,
       and_18_out, and_19_out, and_20_out, and_21_out, and_22_out, and_23_out, and_24_out, and_25_out,
       and_26_out, and_27_out, and_28_out, and_29_out, not_1_out, not_2_out, not_3_out, not_4_out, not_5_out,
       not_6_out, not_7_out, not_8_out, not_9_out, not_10_out, not_11_out, not_12_out, not_13_out,
       not_14_out, not_15_out, not_16_out, not_17_out, not_18_out, not_19_out, not_20_out, not_21_out,
       not_22_out, not_23_out, not_24_out, not_25_out, not_26_out, not_27_out, not_28_out, not_29_out,
       not_30_out, not_31_out, not_32_out, not_33_out, not_34_out, not_35_out, not_36_out, not_37_out,
       not_38_out, not_39_out, not_40_out, not_41_out, not_42_out, not_43_out, not_44_out, not_45_out,
       not_46_out, not_47_out, not_48_out, not_49_out, not_50_out, not_51_out, not_52_out, not_53_out,
       not_54_out, not_55_out, not_56_out, not_57_out, not_58_out, not_59_out, not_60_out, not_61_out,
       not_62_out, not_63_out, not_64_out, not_65_out, not_66_out, not_67_out, not_68_out, not_69_out,
       not_70_out, not_71_out, not_72_out, not_73_out, not_74_out, not_75_out, not_76_out, not_77_out,
       not_78_out, not_79_out, not_80_out, not_81_out, not_82_out, not_83_out, not_84_out, not_85_out,
       not_86_out, not_87_out, not_88_out, not_89_out, not_90_out, not_91_out, not_92_out, not_93_out,
       not_94_out, not_95_out, not_96_out, not_97_out, not_98_out, not_99_out, not_100_out, not_101_out,
       not_102_out, not_103_out, not_104_out, not_105_out, not_106_out, not_107_out, not_108_out,
       not_109_out, not_110_out, not_111_out, not_112_out, not_113_out, not_114_out, not_115_out,
       not_116_out, not_117_out, not_118_out, not_119_out, not_120_out, not_121_out, not_122_out, not_123_out;

  not not_1 (not_1_out, op0);
  not not_2 (not_2_out, op1);
  not not_3 (not_3_out, op4);
  not not_4 (not_4_out, op0);
  not not_5 (not_5_out, op1);
  not not_6 (not_6_out, op3);
  not not_7 (not_7_out, op5);
  not not_8 (not_8_out, op0);
  not not_9 (not_9_out, op1);
  not not_10 (not_10_out, op2);
  not not_11 (not_11_out, op3);
  not not_12 (not_12_out, op4);
  not not_13 (not_13_out, op5);
  not not_14 (not_14_out, op0);
  not not_15 (not_15_out, op1);
  not not_16 (not_16_out, op3);
  not not_17 (not_17_out, op4);
  not not_18 (not_18_out, op5);
  not not_19 (not_19_out, op1);
  not not_20 (not_20_out, op2);
  not not_21 (not_21_out, op3);
  not not_22 (not_22_out, op1);
  not not_23 (not_23_out, op3);
  not not_24 (not_24_out, op0);
  not not_25 (not_25_out, op1);
  not not_26 (not_26_out, op2);
  not not_27 (not_27_out, op4);
  not not_28 (not_28_out, op0);
  not not_29 (not_29_out, op1);
  not not_30 (not_30_out, op2);
  not not_31 (not_31_out, op4);
  not not_32 (not_32_out, op5);
  not not_33 (not_33_out, op0);
  not not_34 (not_34_out, op1);
  not not_35 (not_35_out, op4);
  not not_36 (not_36_out, op5);
  not not_37 (not_37_out, op0);
  not not_38 (not_38_out, op1);
  not not_39 (not_39_out, op3);
  not not_40 (not_40_out, op4);
  not not_41 (not_41_out, op0);
  not not_42 (not_42_out, op1);
  not not_43 (not_43_out, op3);
  not not_44 (not_44_out, op4);
  not not_45 (not_45_out, op5);
  not not_46 (not_46_out, op0);
  not not_47 (not_47_out, op1);
  not not_48 (not_48_out, op2);
  not not_49 (not_49_out, op3);
  not not_50 (not_50_out, op5);
  not not_51 (not_51_out, op0);
  not not_52 (not_52_out, op1);
  not not_53 (not_53_out, op2);
  not not_54 (not_54_out, op3);
  not not_55 (not_55_out, op0);
  not not_56 (not_56_out, op2);
  not not_57 (not_57_out, op3);
  not not_58 (not_58_out, op4);
  not not_59 (not_59_out, op5);
  not not_60 (not_60_out, op0);
  not not_61 (not_61_out, op1);
  not not_62 (not_62_out, op4);
  not not_63 (not_63_out, op5);
  not not_64 (not_64_out, op0);
  not not_65 (not_65_out, op1);
  not not_66 (not_66_out, op3);
  not not_67 (not_67_out, op5);
  not not_68 (not_68_out, op0);
  not not_69 (not_69_out, op1);
  not not_70 (not_70_out, op2);
  not not_71 (not_71_out, op3);
  not not_72 (not_72_out, op4);
  not not_73 (not_73_out, op5);
  not not_74 (not_74_out, op0);
  not not_75 (not_75_out, op1);
  not not_76 (not_76_out, op3);
  not not_77 (not_77_out, op4);
  not not_78 (not_78_out, op5);
  not not_79 (not_79_out, op1);
  not not_80 (not_80_out, op2);
  not not_81 (not_81_out, op3);
  not not_82 (not_82_out, op1);
  not not_83 (not_83_out, op3);
  not not_84 (not_84_out, op0);
  not not_85 (not_85_out, op1);
  not not_86 (not_86_out, op2);
  not not_87 (not_87_out, op4);
  not not_88 (not_88_out, op0);
  not not_89 (not_89_out, op1);
  not not_90 (not_90_out, op2);
  not not_91 (not_91_out, op4);
  not not_92 (not_92_out, op5);
  not not_93 (not_93_out, op0);
  not not_94 (not_94_out, op1);
  not not_95 (not_95_out, op4);
  not not_96 (not_96_out, op5);
  not not_97 (not_97_out, op0);
  not not_98 (not_98_out, op1);
  not not_99 (not_99_out, op3);
  not not_100 (not_100_out, op5);
  not not_101 (not_101_out, op0);
  not not_102 (not_102_out, op1);
  not not_103 (not_103_out, op3);
  not not_104 (not_104_out, op4);
  not not_105 (not_105_out, op0);
  not not_106 (not_106_out, op1);
  not not_107 (not_107_out, op3);
  not not_108 (not_108_out, op4);
  not not_109 (not_109_out, op5);
  not not_110 (not_110_out, op0);
  not not_111 (not_111_out, op1);
  not not_112 (not_112_out, op2);
  not not_113 (not_113_out, op3);
  not not_114 (not_114_out, op5);
  not not_115 (not_115_out, op0);
  not not_116 (not_116_out, op1);
  not not_117 (not_117_out, op2);
  not not_118 (not_118_out, op3);
  not not_119 (not_119_out, op0);
  not not_120 (not_120_out, op2);
  not not_121 (not_121_out, op3);
  not not_122 (not_122_out, op4);
  not not_123 (not_123_out, op5);
  and and_1 (and_1_out, not_1_out, not_2_out, op2, op3, not_3_out, op5);
  and and_2 (and_2_out, not_4_out, not_5_out, op2, not_6_out, op4, not_7_out);
  and and_3 (and_3_out, not_8_out, not_9_out, not_10_out, not_11_out, not_12_out, not_13_out);
  and and_4 (and_4_out, not_14_out, not_15_out, op2, not_16_out, not_17_out, not_18_out);
  and and_5 (and_5_out, op0, not_19_out, not_20_out, not_21_out, op4, op5);
  and and_6 (and_6_out, op0, not_22_out, op2, not_23_out, op4, op5);
  and and_7 (and_7_out, not_24_out, not_25_out, not_26_out, op3, not_27_out, op5);
  and and_8 (and_8_out, not_28_out, not_29_out, not_30_out, op3, not_31_out, not_32_out);
  and and_9 (and_9_out, not_33_out, not_34_out, op2, op3, not_35_out, not_36_out);
  and and_10 (and_10_out, not_37_out, not_38_out, op2, not_39_out, not_40_out, op5);
  and and_11 (and_11_out, not_41_out, not_42_out, op2, not_43_out, not_44_out, not_45_out);
  and and_12 (and_12_out, not_46_out, not_47_out, not_48_out, not_49_out, op4, not_50_out);
  and and_13 (and_13_out, not_51_out, not_52_out, not_53_out, not_54_out, op4, op5);
  and and_14 (and_14_out, not_55_out, op1, not_56_out, not_57_out, not_58_out, not_59_out);
  and and_15 (and_15_out, not_60_out, not_61_out, op2, op3, not_62_out, not_63_out);
  and and_16 (and_16_out, not_64_out, not_65_out, op2, not_66_out, op4, not_67_out);
  and and_17 (and_17_out, not_68_out, not_69_out, not_70_out, not_71_out, not_72_out, not_73_out);
  and and_18 (and_18_out, not_74_out, not_75_out, op2, not_76_out, not_77_out, not_78_out);
  and and_19 (and_19_out, op0, not_79_out, not_80_out, not_81_out, op4, op5);
  and and_20 (and_20_out, op0, not_82_out, op2, not_83_out, op4, op5);
  and and_21 (and_21_out, not_84_out, not_85_out, not_86_out, op3, not_87_out, op5);
  and and_22 (and_22_out, not_88_out, not_89_out, not_90_out, op3, not_91_out, not_92_out);
  and and_23 (and_23_out, not_93_out, not_94_out, op2, op3, not_95_out, not_96_out);
  and and_24 (and_24_out, not_97_out, not_98_out, op2, not_99_out, op4, not_100_out);
  and and_25 (and_25_out, not_101_out, not_102_out, op2, not_103_out, not_104_out, op5);
  and and_26 (and_26_out, not_105_out, not_106_out, op2, not_107_out, not_108_out, not_109_out);
  and and_27 (and_27_out, not_110_out, not_111_out, not_112_out, not_113_out, op4, not_114_out);
  and and_28 (and_28_out, not_115_out, not_116_out, not_117_out, not_118_out, op4, op5);
  and and_29 (and_29_out, not_119_out, op1, not_120_out, not_121_out, not_122_out, not_123_out);
  or or_1 (ALUop0, and_1_out, and_2_out);
  or or_2 (ALUop2, and_15_out, and_16_out);
  or or_3 (ALUop1, and_3_out, and_4_out, and_5_out, and_6_out, and_7_out, and_8_out, and_9_out, and_10_out, and_11_out, and_12_out, and_13_out, and_14_out);
  or or_4 (ALUop3, and_17_out, and_18_out, and_19_out, and_20_out, and_21_out, and_22_out, and_23_out, and_24_out, and_25_out, and_26_out, and_27_out, and_28_out, and_29_out);
endmodule

module Opcode_Decoder (
  input  op0,
  input  op1,
  input  op2,
  input  op3,
  input  op4,
  input  op5,
  output MemRead,
  output MemWrite,
  output ALUSrc,
  output Jump,
  output MemtoReg,
  output Branch,
  output RegDst,
  output RegWrite,
  output BneBeq,
  output IsJAL,
  output ZeroExtend
);

  wire and_3_out, and_4_out, and_5_out, and_6_out, and_7_out, and_8_out, and_9_out, and_10_out, and_11_out,
       and_12_out, and_14_out, and_15_out, and_17_out, and_18_out, and_19_out, and_20_out, and_21_out,
       and_22_out, and_23_out, and_24_out, and_25_out, and_26_out, and_29_out, and_30_out, not_1_out,
       not_2_out, not_3_out, not_4_out, not_5_out, not_6_out, not_7_out, not_8_out, not_9_out, not_10_out,
       not_11_out, not_12_out, not_13_out, not_14_out, not_15_out, not_16_out, not_17_out, not_18_out,
       not_19_out, not_20_out, not_21_out, not_22_out, not_23_out, not_24_out, not_25_out, not_26_out,
       not_27_out, not_28_out, not_29_out, not_30_out, not_31_out, not_32_out, not_33_out, not_34_out,
       not_35_out, not_36_out, not_37_out, not_38_out, not_39_out, not_40_out, not_41_out, not_42_out,
       not_43_out, not_44_out, not_45_out, not_46_out, not_47_out, not_48_out, not_49_out, not_50_out,
       not_51_out, not_52_out, not_53_out, not_54_out, not_55_out, not_56_out, not_57_out, not_58_out,
       not_59_out, not_60_out, not_61_out, not_62_out, not_63_out, not_64_out, not_65_out, not_66_out,
       not_67_out, not_68_out, not_69_out, not_70_out, not_71_out, not_72_out, not_73_out, not_74_out,
       not_75_out, not_76_out, not_77_out, not_78_out, not_79_out, not_80_out, not_81_out, not_82_out,
       not_83_out, not_84_out, not_85_out, not_86_out, not_87_out, not_88_out, not_89_out, not_90_out,
       not_91_out, not_92_out, not_93_out, not_94_out, not_95_out, not_96_out, not_97_out, not_98_out,
       not_99_out, not_100_out, not_101_out, not_102_out, not_103_out, not_104_out, not_105_out, not_106_out,
       not_107_out, not_108_out, not_109_out, not_110_out, not_111_out, not_112_out, not_113_out,
       not_114_out, not_115_out, not_116_out, not_117_out, not_118_out, not_119_out;

  not not_1 (not_1_out, op1);
  not not_2 (not_2_out, op2);
  not not_3 (not_3_out, op3);
  not not_4 (not_4_out, op1);
  not not_5 (not_5_out, op3);
  not not_6 (not_6_out, op0);
  not not_7 (not_7_out, op1);
  not not_8 (not_8_out, op3);
  not not_9 (not_9_out, op4);
  not not_10 (not_10_out, op5);
  not not_11 (not_11_out, op1);
  not not_12 (not_12_out, op2);
  not not_13 (not_13_out, op3);
  not not_14 (not_14_out, op1);
  not not_15 (not_15_out, op3);
  not not_16 (not_16_out, op0);
  not not_17 (not_17_out, op1);
  not not_18 (not_18_out, op4);
  not not_19 (not_19_out, op5);
  not not_20 (not_20_out, op0);
  not not_21 (not_21_out, op1);
  not not_22 (not_22_out, op4);
  not not_23 (not_23_out, op0);
  not not_24 (not_24_out, op1);
  not not_25 (not_25_out, op3);
  not not_26 (not_26_out, op5);
  not not_27 (not_27_out, op0);
  not not_28 (not_28_out, op1);
  not not_29 (not_29_out, op3);
  not not_30 (not_30_out, op4);
  not not_31 (not_31_out, op0);
  not not_32 (not_32_out, op1);
  not not_33 (not_33_out, op3);
  not not_34 (not_34_out, op4);
  not not_35 (not_35_out, op5);
  not not_36 (not_36_out, op0);
  not not_37 (not_37_out, op1);
  not not_38 (not_38_out, op2);
  not not_39 (not_39_out, op3);
  not not_40 (not_40_out, op5);
  not not_41 (not_41_out, op0);
  not not_42 (not_42_out, op1);
  not not_43 (not_43_out, op2);
  not not_44 (not_44_out, op3);
  not not_45 (not_45_out, op1);
  not not_46 (not_46_out, op2);
  not not_47 (not_47_out, op3);
  not not_48 (not_48_out, op0);
  not not_49 (not_49_out, op1);
  not not_50 (not_50_out, op2);
  not not_51 (not_51_out, op4);
  not not_52 (not_52_out, op0);
  not not_53 (not_53_out, op1);
  not not_54 (not_54_out, op2);
  not not_55 (not_55_out, op4);
  not not_56 (not_56_out, op5);
  not not_57 (not_57_out, op0);
  not not_58 (not_58_out, op1);
  not not_59 (not_59_out, op2);
  not not_60 (not_60_out, op3);
  not not_61 (not_61_out, op4);
  not not_62 (not_62_out, op5);
  not not_63 (not_63_out, op0);
  not not_64 (not_64_out, op1);
  not not_65 (not_65_out, op2);
  not not_66 (not_66_out, op3);
  not not_67 (not_67_out, op4);
  not not_68 (not_68_out, op5);
  not not_69 (not_69_out, op0);
  not not_70 (not_70_out, op1);
  not not_71 (not_71_out, op3);
  not not_72 (not_72_out, op4);
  not not_73 (not_73_out, op5);
  not not_74 (not_74_out, op1);
  not not_75 (not_75_out, op2);
  not not_76 (not_76_out, op3);
  not not_77 (not_77_out, op0);
  not not_78 (not_78_out, op1);
  not not_79 (not_79_out, op4);
  not not_80 (not_80_out, op5);
  not not_81 (not_81_out, op0);
  not not_82 (not_82_out, op1);
  not not_83 (not_83_out, op4);
  not not_84 (not_84_out, op0);
  not not_85 (not_85_out, op1);
  not not_86 (not_86_out, op3);
  not not_87 (not_87_out, op5);
  not not_88 (not_88_out, op0);
  not not_89 (not_89_out, op1);
  not not_90 (not_90_out, op3);
  not not_91 (not_91_out, op4);
  not not_92 (not_92_out, op0);
  not not_93 (not_93_out, op1);
  not not_94 (not_94_out, op3);
  not not_95 (not_95_out, op4);
  not not_96 (not_96_out, op5);
  not not_97 (not_97_out, op0);
  not not_98 (not_98_out, op1);
  not not_99 (not_99_out, op2);
  not not_100 (not_100_out, op3);
  not not_101 (not_101_out, op0);
  not not_102 (not_102_out, op2);
  not not_103 (not_103_out, op3);
  not not_104 (not_104_out, op4);
  not not_105 (not_105_out, op5);
  not not_106 (not_106_out, op0);
  not not_107 (not_107_out, op1);
  not not_108 (not_108_out, op2);
  not not_109 (not_109_out, op4);
  not not_110 (not_110_out, op0);
  not not_111 (not_111_out, op1);
  not not_112 (not_112_out, op2);
  not not_113 (not_113_out, op3);
  not not_114 (not_114_out, op0);
  not not_115 (not_115_out, op1);
  not not_116 (not_116_out, op4);
  not not_117 (not_117_out, op0);
  not not_118 (not_118_out, op1);
  not not_119 (not_119_out, op5);
  and and_1 (MemRead, op0, not_1_out, not_2_out, not_3_out, op4, op5);
  and and_2 (MemWrite, op0, not_4_out, op2, not_5_out, op4, op5);
  and and_3 (and_3_out, not_6_out, not_7_out, op2, not_8_out, not_9_out, not_10_out);
  and and_4 (and_4_out, op0, not_11_out, not_12_out, not_13_out, op4, op5);
  and and_5 (and_5_out, op0, not_14_out, op2, not_15_out, op4, op5);
  and and_6 (and_6_out, not_16_out, not_17_out, op2, op3, not_18_out, not_19_out);
  and and_7 (and_7_out, not_20_out, not_21_out, op2, op3, not_22_out, op5);
  and and_8 (and_8_out, not_23_out, not_24_out, op2, not_25_out, op4, not_26_out);
  and and_9 (and_9_out, not_27_out, not_28_out, op2, not_29_out, not_30_out, op5);
  and and_10 (and_10_out, not_31_out, not_32_out, op2, not_33_out, not_34_out, not_35_out);
  and and_11 (and_11_out, not_36_out, not_37_out, not_38_out, not_39_out, op4, not_40_out);
  and and_12 (and_12_out, not_41_out, not_42_out, not_43_out, not_44_out, op4, op5);
  and and_13 (MemtoReg, op0, not_45_out, not_46_out, not_47_out, op4, op5);
  and and_14 (and_14_out, not_48_out, not_49_out, not_50_out, op3, not_51_out, op5);
  and and_15 (and_15_out, not_52_out, not_53_out, not_54_out, op3, not_55_out, not_56_out);
  and and_16 (RegDst, not_57_out, not_58_out, not_59_out, not_60_out, not_61_out, not_62_out);
  and and_17 (and_17_out, not_63_out, not_64_out, not_65_out, not_66_out, not_67_out, not_68_out);
  and and_18 (and_18_out, not_69_out, not_70_out, op2, not_71_out, not_72_out, not_73_out);
  and and_19 (and_19_out, op0, not_74_out, not_75_out, not_76_out, op4, op5);
  and and_20 (and_20_out, not_77_out, not_78_out, op2, op3, not_79_out, not_80_out);
  and and_21 (and_21_out, not_81_out, not_82_out, op2, op3, not_83_out, op5);
  and and_22 (and_22_out, not_84_out, not_85_out, op2, not_86_out, op4, not_87_out);
  and and_23 (and_23_out, not_88_out, not_89_out, op2, not_90_out, not_91_out, op5);
  and and_24 (and_24_out, not_92_out, not_93_out, op2, not_94_out, not_95_out, not_96_out);
  and and_25 (and_25_out, not_97_out, not_98_out, not_99_out, not_100_out, op4, op5);
  and and_26 (and_26_out, not_101_out, op1, not_102_out, not_103_out, not_104_out, not_105_out);
  and and_27 (BneBeq, not_106_out, not_107_out, not_108_out, op3, not_109_out, op5);
  and and_28 (IsJAL, not_110_out, not_111_out, not_112_out, not_113_out, op4, op5);
  and and_29 (and_29_out, not_114_out, not_115_out, op2, op3, not_116_out);
  and and_30 (and_30_out, not_117_out, not_118_out, op2, op3, op4, not_119_out);
  or or_1 (ALUSrc, and_3_out, and_4_out, and_5_out, and_6_out, and_7_out, and_8_out, and_9_out, and_10_out);
  or or_2 (Jump, and_11_out, and_12_out);
  or or_3 (Branch, and_14_out, and_15_out);
  or or_4 (ZeroExtend, and_29_out, and_30_out);
  or or_5 (RegWrite, and_17_out, and_18_out, and_19_out, and_20_out, and_21_out, and_22_out, and_23_out, and_24_out, and_25_out, and_26_out);
endmodule

module Syscall_Decoder (
  input  clk,
  input  Enable,
  input  [31:0] a0,
  input  [31:0] v0,
  output [31:0] Hex,
  output Halt
);

  wire comparator_1_eq;

  Comparator #(.width(32)) comparator_1 (.a(v0), .b(32'ha), .eq(comparator_1_eq));  // open: gt, lt
  Register #(.width(32)) register_1 (.D(a0), .en(Enable), .Q(Hex), .clk(clk));  // open: clr
  Multiplexer #(.enable("false")) multiplexer_1 (.in0(1'b0), .in1(comparator_1_eq), .out(Halt), .sel(Enable));
  D_Flip_Flop d_ff_1 (.clk(clk));  // open: D, Q, Qn, preset, en, reset
endmodule

module Statistics (
  input  op0,
  input  op1,
  input  op2,
  input  op3,
  input  op4,
  input  op5,
  output i,
  output r,
  output j
);

  wire and_1_out, and_2_out, and_3_out, and_4_out, and_5_out, and_6_out, and_7_out, and_8_out, and_9_out,
       and_10_out, and_12_out, and_13_out, not_1_out, not_2_out, not_3_out, not_4_out, not_5_out, not_6_out,
       not_7_out, not_8_out, not_9_out, not_10_out, not_11_out, not_12_out, not_13_out, not_14_out,
       not_15_out, not_16_out, not_17_out, not_18_out, not_19_out, not_20_out, not_21_out, not_22_out,
       not_23_out, not_24_out, not_25_out, not_26_out, not_27_out, not_28_out, not_29_out, not_30_out,
       not_31_out, not_32_out, not_33_out, not_34_out, not_35_out, not_36_out, not_37_out, not_38_out,
       not_39_out, not_40_out, not_41_out, not_42_out, not_43_out, not_44_out, not_45_out, not_46_out,
       not_47_out, not_48_out, not_49_out, not_50_out, not_51_out, not_52_out, not_53_out, not_54_out;

  not not_1 (not_1_out, op1);
  not not_2 (not_2_out, op2);
  not not_3 (not_3_out, op3);
  not not_4 (not_4_out, op1);
  not not_5 (not_5_out, op3);
  not not_6 (not_6_out, op0);
  not not_7 (not_7_out, op1);
  not not_8 (not_8_out, op2);
  not not_9 (not_9_out, op4);
  not not_10 (not_10_out, op0);
  not not_11 (not_11_out, op1);
  not not_12 (not_12_out, op2);
  not not_13 (not_13_out, op4);
  not not_14 (not_14_out, op5);
  not not_15 (not_15_out, op0);
  not not_16 (not_16_out, op1);
  not not_17 (not_17_out, op4);
  not not_18 (not_18_out, op5);
  not not_19 (not_19_out, op0);
  not not_20 (not_20_out, op1);
  not not_21 (not_21_out, op4);
  not not_22 (not_22_out, op0);
  not not_23 (not_23_out, op1);
  not not_24 (not_24_out, op3);
  not not_25 (not_25_out, op5);
  not not_26 (not_26_out, op0);
  not not_27 (not_27_out, op1);
  not not_28 (not_28_out, op3);
  not not_29 (not_29_out, op4);
  not not_30 (not_30_out, op5);
  not not_31 (not_31_out, op0);
  not not_32 (not_32_out, op1);
  not not_33 (not_33_out, op3);
  not not_34 (not_34_out, op4);
  not not_35 (not_35_out, op0);
  not not_36 (not_36_out, op1);
  not not_37 (not_37_out, op3);
  not not_38 (not_38_out, op4);
  not not_39 (not_39_out, op5);
  not not_40 (not_40_out, op0);
  not not_41 (not_41_out, op1);
  not not_42 (not_42_out, op2);
  not not_43 (not_43_out, op3);
  not not_44 (not_44_out, op4);
  not not_45 (not_45_out, op5);
  not not_46 (not_46_out, op0);
  not not_47 (not_47_out, op1);
  not not_48 (not_48_out, op2);
  not not_49 (not_49_out, op3);
  not not_50 (not_50_out, op5);
  not not_51 (not_51_out, op0);
  not not_52 (not_52_out, op1);
  not not_53 (not_53_out, op2);
  not not_54 (not_54_out, op3);
  and and_1 (and_1_out, op0, not_1_out, not_2_out, not_3_out, op4, op5);
  and and_2 (and_2_out, op0, not_4_out, op2, not_5_out, op4, op5);
  and and_3 (and_3_out, not_6_out, not_7_out, not_8_out, op3, not_9_out, op5);
  and and_4 (and_4_out, not_10_out, not_11_out, not_12_out, op3, not_13_out, not_14_out);
  and and_5 (and_5_out, not_15_out, not_16_out, op2, op3, not_17_out, not_18_out);
  and and_6 (and_6_out, not_19_out, not_20_out, op2, op3, not_21_out, op5);
  and and_7 (and_7_out, not_22_out, not_23_out, op2, not_24_out, op4, not_25_out);
  and and_8 (and_8_out, not_26_out, not_27_out, op2, not_28_out, not_29_out, not_30_out);
  and and_9 (and_9_out, not_31_out, not_32_out, op2, not_33_out, not_34_out, op5);
  and and_10 (and_10_out, not_35_out, not_36_out, op2, not_37_out, not_38_out, not_39_out);
  and and_11 (r, not_40_out, not_41_out, not_42_out, not_43_out, not_44_out, not_45_out);
  and and_12 (and_12_out, not_46_out, not_47_out, not_48_out, not_49_out, op4, not_50_out);
  and and_13 (and_13_out, not_51_out, not_52_out, not_53_out, not_54_out, op4, op5);
  or or_1 (j, and_12_out, and_13_out);
  or or_2 (i, and_1_out, and_2_out, and_3_out, and_4_out, and_5_out, and_6_out, and_7_out, and_8_out, and_9_out, and_10_out);
endmodule

module IF_ID (
  input  clk,
  input  clr,
  input  [31:0] InstIF,
  input  [31:0] PCPlus4ID,
  input  En,
  output [31:0] InstID,
  output [31:0] PCPlus4IF
);

  Register #(.width(32)) register_1 (.D(InstIF), .en(En), .Q(InstID), .clk(clk), .clr(clr));
  Register #(.width(32)) register_2 (.D(PCPlus4ID), .en(En), .Q(PCPlus4IF), .clk(clk), .clr(clr));
endmodule

module ID_EX (
  input  clk,
  input  clr,
  input  MemWriteID,
  input  [31:0] ImmID,
  input  [31:0] ShamtID,
  input  IsJALID,
  input  JumpID,
  input  IsShamtID,
  input  [31:0] R1ID,
  input  [31:0] JumpAddr,
  input  BranchID,
  input  MemtoRegID,
  input  IsJRID,
  input  RegWriteID,
  input  [31:0] R2ID,
  input  [31:0] PCPlus4ID,
  input  IsSyscallID,
  input  BneOrBeqID,
  input  [3:0] ALUopID,
  input  ALUSrcID,
  input  [31:0] CP0Dout,
  input  [4:0] WriteReg_ID,
  input  IsExceptionID,
  input  MemReadID,
  input  IsEret,
  input  En,
  output MemWriteEX,
  output [31:0] ImmEX,
  output [31:0] ShamtEX,
  output IsJALEX,
  output JumpEX,
  output IsShamtEX,
  output [31:0] R1EX,
  output [31:0] JumpAddr_2,
  output BranchEX,
  output MemtoRegEX,
  output IsJREX,
  output RegWriteEX,
  output [31:0] R2EX,
  output [31:0] PCPlusEX,
  output IsSyscallEX,
  output BneOrBeqEX,
  output [3:0] ALUopEX,
  output ALUSrcEX,
  output [31:0] CP0Dout_2,
  output [4:0] WriteReg_EX,
  output IsExceptionEX,
  output MemReadEX,
  output IsEret_2
);

  Register #(.width(32)) register_1 (.D(ImmID), .en(En), .Q(ImmEX), .clk(clk), .clr(clr));
  Register #(.width(32)) register_2 (.D(R1ID), .en(En), .Q(R1EX), .clk(clk), .clr(clr));
  Register #(.width(32)) register_3 (.D(R2ID), .en(En), .Q(R2EX), .clk(clk), .clr(clr));
  Register #(.width(32)) register_4 (.D(CP0Dout), .en(En), .Q(CP0Dout_2), .clk(clk), .clr(clr));
  Register #(.width(32)) register_5 (.D(ShamtID), .en(En), .Q(ShamtEX), .clk(clk), .clr(clr));
  Register #(.width(32)) register_6 (.D(JumpAddr), .en(En), .Q(JumpAddr_2), .clk(clk), .clr(clr));
  Register #(.width(32)) register_7 (.D(PCPlus4ID), .en(En), .Q(PCPlusEX), .clk(clk), .clr(clr));
  Register #(.width(1)) register_8 (.D(IsJALID), .en(En), .Q(IsJALEX), .clk(clk), .clr(clr));
  Register #(.width(1)) register_9 (.D(IsShamtID), .en(En), .Q(IsShamtEX), .clk(clk), .clr(clr));
  Register #(.width(1)) register_10 (.D(MemtoRegID), .en(En), .Q(MemtoRegEX), .clk(clk), .clr(clr));
  Register #(.width(1)) register_11 (.D(RegWriteID), .en(En), .Q(RegWriteEX), .clk(clk), .clr(clr));
  Register #(.width(1)) register_12 (.D(BneOrBeqID), .en(En), .Q(BneOrBeqEX), .clk(clk), .clr(clr));
  Register #(.width(1)) register_13 (.D(ALUSrcID), .en(En), .Q(ALUSrcEX), .clk(clk), .clr(clr));
  Register #(.width(1)) register_14 (.D(IsExceptionID), .en(En), .Q(IsExceptionEX), .clk(clk), .clr(clr));
  Register #(.width(1)) register_15 (.D(MemReadID), .en(En), .Q(MemReadEX), .clk(clk), .clr(clr));
  Register #(.width(1)) register_16 (.D(MemWriteID), .en(En), .Q(MemWriteEX), .clk(clk), .clr(clr));
  Register #(.width(1)) register_17 (.D(JumpID), .en(En), .Q(JumpEX), .clk(clk), .clr(clr));
  Register #(.width(1)) register_18 (.D(BranchID), .en(En), .Q(BranchEX), .clk(clk), .clr(clr));
  Register #(.width(1)) register_19 (.D(IsJRID), .en(En), .Q(IsJREX), .clk(clk), .clr(clr));
  Register #(.width(1)) register_20 (.D(IsSyscallID), .en(En), .Q(IsSyscallEX), .clk(clk), .clr(clr));
  Register #(.width(4)) register_21 (.D(ALUopID), .en(En), .Q(ALUopEX), .clk(clk), .clr(clr));
  Register #(.width(5)) register_22 (.D(WriteReg_ID), .en(En), .Q(WriteReg_EX), .clk(clk), .clr(clr));
  Register #(.width(1)) register_23 (.D(IsEret), .en(En), .Q(IsEret_2), .clk(clk), .clr(clr));
endmodule

module EX_MEM (
  input  clk,
  input  clr,
  input  IsJALEX,
  input  [31:0] ALUResultEX,
  input  MemtoRegEX,
  input  RegWriteEX,
  input  [31:0] WriteDataEX,
  input  IsExceptionEX,
  input  [31:0] JumpAddrEX,
  input  MemReadEX,
  input  MemWriteEX,
  input  [31:0] CP0Dout,
  input  IsSyscallEX,
  input  [4:0] WriteReg_EX,
  input  En,
  output IsJALMEM,
  output [31:0] ALUResultMEM,
  output MemtoRegMEM,
  output RegWriteMEM,
  output [31:0] WriteDataMEM,
  output IsExceptionMEM,
  output [31:0] JumpAddrMEM,
  output MemReadMEM,
  output MemWriteMEM,
  output [31:0] CP0Dout_2,
  output IsSyscallMEM,
  output [4:0] WriteReg_MEM
);

  Register #(.width(1)) register_1 (.D(IsJALEX), .en(En), .Q(IsJALMEM), .clk(clk), .clr(clr));
  Register #(.width(1)) register_2 (.D(MemtoRegEX), .en(En), .Q(MemtoRegMEM), .clk(clk), .clr(clr));
  Register #(.width(1)) register_3 (.D(RegWriteEX), .en(En), .Q(RegWriteMEM), .clk(clk), .clr(clr));
  Register #(.width(1)) register_4 (.D(IsExceptionEX), .en(En), .Q(IsExceptionMEM), .clk(clk), .clr(clr));
  Register #(.width(1)) register_5 (.D(MemReadEX), .en(En), .Q(MemReadMEM), .clk(clk), .clr(clr));
  Register #(.width(1)) register_6 (.D(MemWriteEX), .en(En), .Q(MemWriteMEM), .clk(clk), .clr(clr));
  Register #(.width(1)) register_7 (.D(IsSyscallEX), .en(En), .Q(IsSyscallMEM), .clk(clk), .clr(clr));
  Register #(.width(5)) register_8 (.D(WriteReg_EX), .en(En), .Q(WriteReg_MEM), .clk(clk), .clr(clr));
  Register #(.width(32)) register_9 (.D(ALUResultEX), .en(En), .Q(ALUResultMEM), .clk(clk), .clr(clr));
  Register #(.width(32)) register_10 (.D(WriteDataEX), .en(En), .Q(WriteDataMEM), .clk(clk), .clr(clr));
  Register #(.width(32)) register_11 (.D(JumpAddrEX), .en(En), .Q(JumpAddrMEM), .clk(clk), .clr(clr));
  Register #(.width(32)) register_12 (.D(CP0Dout), .en(En), .Q(CP0Dout_2), .clk(clk), .clr(clr));
endmodule

// MEM/WBN
module MEM_WB (
  input  clk,
  input  clr,
  input  IsJALMEM,
  input  [31:0] ALUResultMEM,
  input  MemtoRegMEM,
  input  RegWriteMEM,
  input  [31:0] ReadDataMEM,
  input  IsExceptionMEM,
  input  IsSyscallMEM,
  input  [31:0] JumpAddrMEM,
  input  [4:0] WriteReg_MEM,
  input  [31:0] JumpAddrMEM_2,
  input  En,
  output IsJALWB,
  output [31:0] ALUResultWB,
  output MemtoRegWB,
  output RegWriteWB,
  output [31:0] ReadDataWB,
  output IsExceptionWB,
  output IsSyscallWB,
  output [31:0] JumpAddrWB,
  output [4:0] WriteReg_WB,
  output [31:0] JumpAddrWB_2
);

  Register #(.width(1)) register_1 (.D(IsJALMEM), .en(En), .Q(IsJALWB), .clk(clk), .clr(clr));
  Register #(.width(1)) register_2 (.D(MemtoRegMEM), .en(En), .Q(MemtoRegWB), .clk(clk), .clr(clr));
  Register #(.width(1)) register_3 (.D(RegWriteMEM), .en(En), .Q(RegWriteWB), .clk(clk), .clr(clr));
  Register #(.width(1)) register_4 (.D(IsExceptionMEM), .en(En), .Q(IsExceptionWB), .clk(clk), .clr(clr));
  Register #(.width(1)) register_5 (.D(IsSyscallMEM), .en(En), .Q(IsSyscallWB), .clk(clk), .clr(clr));
  Register #(.width(5)) register_6 (.D(WriteReg_MEM), .en(En), .Q(WriteReg_WB), .clk(clk), .clr(clr));
  Register #(.width(32)) register_7 (.D(ALUResultMEM), .en(En), .Q(ALUResultWB), .clk(clk), .clr(clr));
  Register #(.width(32)) register_8 (.D(ReadDataMEM), .en(En), .Q(ReadDataWB), .clk(clk), .clr(clr));
  Register #(.width(32)) register_9 (.D(JumpAddrMEM), .en(En), .Q(JumpAddrWB), .clk(clk), .clr(clr));
  Register #(.width(32)) register_10 (.D(JumpAddrMEM_2), .en(En), .Q(JumpAddrWB_2), .clk(clk), .clr(clr));
endmodule

module Regfile_Wrapper (
  input  [4:0] R1_num,
  input  [4:0] R2_num,
  input  [4:0] RW,
  input  WE,
  input  clk,
  input  [31:0] Din,
  output [31:0] v0,
  output [31:0] a0,
  output [31:0] R1,
  output [31:0] R2
);

  regfile_main main_1 (
    .Reg1_num(R1_num), .Reg2(R2_num), .Write_Reg_num(RW), .Din(Din), .Write_Enable(WE), .Clock(clk),
    .Reg1(R1), .Reg2_2(R2), .s0_Value(v0), .s1_Value(a0));  // open: s2_Value, ra_Value
endmodule

module ALU_Wrapper (
  input  [31:0] X,
  input  [31:0] Y,
  input  [3:0] AluOP,
  output [31:0] Result,
  output Equal
);

  ALU alu_1 (
    .AluOP(AluOP), .X(X), .Equal(Equal), .Result(Result), .Y(Y));  // open: Signed_Overflow, Result_2, UnSigned_Overflow
endmodule

module Immediate_Extend (
  input  ZeroExtend,
  input  [15:0] Input,
  output [31:0] Output
);

  wire [31:0] bit_extender_1_out, bit_extender_2_out;

  assign bit_extender_1_out = {{16{Input[15]}}, Input};  // Bit_Extender bit_extender_1
  assign bit_extender_2_out = {{16{1'b0}}, Input};  // Bit_Extender bit_extender_2
  Multiplexer #(.width(32), .enable("false")) multiplexer_1 (
    .in0(bit_extender_1_out), .in1(bit_extender_2_out), .out(Output), .sel(ZeroExtend));
endmodule

module Hazard_Unit (
  input  clk,
  input  ReadRs,
  input  RegWriteMEM,
  input  IsToBranchOrJump,
  input  ReadRt,
  input  [4:0] RS,
  input  RegWriteEX,
  input  [4:0] WriteReg_MEM,
  input  [4:0] WriteReg_EX,
  input  [4:0] RT,
  input  IsLW,
  output FlushIF,
  output [1:0] RsOutput,
  output FlushID,
  output StallIF,
  output StallID,
  output [31:0] BubbleNum,
  output [1:0] RtOutput
);

  wire d_ff_1_q, d_ff_2_q, hazard_detector_1_hazard, hazard_detector_2_hazard, hazard_detector_3_hazard,
       hazard_detector_4_hazard, or_1_out;
  wire [1:0] multiplexer_1_out, multiplexer_2_out;

  Hazard_Detector hazard_detector_1 (
    .Read(ReadRs), .RegWrite(RegWriteMEM), .WriteReg(WriteReg_MEM), .Register_num(RS),
    .Hazard(hazard_detector_1_hazard));
  Hazard_Detector hazard_detector_2 (
    .Read(ReadRs), .RegWrite(RegWriteEX), .WriteReg(WriteReg_EX), .Register_num(RS),
    .Hazard(hazard_detector_2_hazard));
  Hazard_Detector hazard_detector_3 (
    .Read(ReadRt), .RegWrite(RegWriteMEM), .WriteReg(WriteReg_MEM), .Register_num(RT),
    .Hazard(hazard_detector_3_hazard));
  Hazard_Detector hazard_detector_4 (
    .Read(ReadRt), .RegWrite(RegWriteEX), .WriteReg(WriteReg_EX), .Register_num(RT),
    .Hazard(hazard_detector_4_hazard));
  Multiplexer #(.width(2), .enable("false")) multiplexer_1 (
    .in0(2'b00), .in1(2'b10), .out(multiplexer_1_out), .sel(hazard_detector_1_hazard));
  Multiplexer #(.width(2), .enable("false")) multiplexer_2 (
    .in0(2'b00), .in1(2'b10), .out(multiplexer_2_out), .sel(hazard_detector_3_hazard));
  Multiplexer #(.width(2), .enable("false")) multiplexer_3 (
    .in0(multiplexer_1_out), .in1(2'b01), .out(RsOutput), .sel(hazard_detector_2_hazard));
  Multiplexer #(.width(2), .enable("false")) multiplexer_4 (
    .in0(multiplexer_2_out), .in1(2'b01), .out(RtOutput), .sel(hazard_detector_4_hazard));
  or or_1 (or_1_out, hazard_detector_2_hazard, hazard_detector_4_hazard);
  and and_1 (StallID, IsLW, or_1_out);
  D_Flip_Flop #(.trigger("falling")) d_ff_1 (
    .clk(clk), .D(IsToBranchOrJump), .Q(d_ff_1_q));  // open: Qn, preset, en, reset
  D_Flip_Flop #(.trigger("falling")) d_ff_2 (.clk(clk), .D(StallID), .Q(d_ff_2_q));  // open: Qn, preset, en, reset
  Counter #(.width(32), .max('hffffffff)) counter_1 (
    .count(StallID), .Q(BubbleNum), .clk(clk));  // open: load, D, carry, clr
  and and_2 (FlushIF, ~clk, d_ff_1_q);  // AND_Gate
  and and_3 (FlushID, clk, d_ff_2_q);

  assign StallIF = StallID;

  // Other names for the same wires on the sheet: ReadWriteEX = RegWriteEX; ReadWriteMEM = RegWriteMEM

  // Notes on the sheet:
  //   Rs Hazard in MEM
  //   Rs Hazard in EX
  //   Rt Hazard in MEM
  //   Rt Hazard in EX
  //   hasHazard
endmodule

module RegisterRead_Detector (
  input  op0,
  input  op1,
  input  op2,
  input  op3,
  input  op4,
  input  op5,
  input  Funct0,
  input  Funct1,
  input  Funct2,
  input  Funct3,
  input  Funct4,
  input  Funct5,
  output ReadRs,
  output ReadRt
);

  wire and_1_out, and_2_out, and_3_out, and_4_out, and_5_out, and_6_out, and_7_out, and_8_out, and_9_out,
       and_10_out, and_11_out, and_12_out, and_13_out, and_14_out, and_15_out, and_16_out, and_17_out,
       and_18_out, and_19_out, and_20_out, and_21_out, and_22_out, and_23_out, and_24_out, and_25_out,
       and_26_out, and_27_out, and_28_out, and_29_out, and_30_out, and_31_out, and_32_out, and_33_out,
       and_34_out, and_35_out, not_1_out, not_2_out, not_3_out, not_4_out, not_5_out, not_6_out, not_7_out,
       not_8_out, not_9_out, not_10_out, not_11_out, not_12_out, not_13_out, not_14_out, not_15_out,
       not_16_out, not_17_out, not_18_out, not_19_out, not_20_out, not_21_out, not_22_out, not_23_out,
       not_24_out, not_25_out, not_26_out, not_27_out, not_28_out, not_29_out, not_30_out, not_31_out,
       not_32_out, not_33_out, not_34_out, not_35_out, not_36_out, not_37_out, not_38_out, not_39_out,
       not_40_out, not_41_out, not_42_out, not_43_out, not_44_out, not_45_out, not_46_out, not_47_out,
       not_48_out, not_49_out, not_50_out, not_51_out, not_52_out, not_53_out, not_54_out, not_55_out,
       not_56_out, not_57_out, not_58_out, not_59_out, not_60_out, not_61_out, not_62_out, not_63_out,
       not_64_out, not_65_out, not_66_out, not_67_out, not_68_out, not_69_out, not_70_out, not_71_out,
       not_72_out, not_73_out, not_74_out, not_75_out, not_76_out, not_77_out, not_78_out, not_79_out,
       not_80_out, not_81_out, not_82_out, not_83_out, not_84_out, not_85_out, not_86_out, not_87_out,
       not_88_out, not_89_out, not_90_out, not_91_out, not_92_out, not_93_out, not_94_out, not_95_out,
       not_96_out, not_97_out, not_98_out, not_99_out, not_100_out, not_101_out, not_102_out, not_103_out,
       not_104_out, not_105_out, not_106_out, not_107_out, not_108_out, not_109_out, not_110_out,
       not_111_out, not_112_out, not_113_out, not_114_out, not_115_out, not_116_out, not_117_out,
       not_118_out, not_119_out, not_120_out, not_121_out, not_122_out, not_123_out, not_124_out,
       not_125_out, not_126_out, not_127_out, not_128_out, not_129_out, not_130_out, not_131_out,
       not_132_out, not_133_out, not_134_out, not_135_out, not_136_out, or_1_out, or_2_out;

  not not_1 (not_1_out, Funct1);
  not not_2 (not_2_out, Funct2);
  not not_3 (not_3_out, Funct3);
  not not_4 (not_4_out, Funct4);
  not not_5 (not_5_out, Funct5);
  not not_6 (not_6_out, Funct1);
  not not_7 (not_7_out, Funct2);
  not not_8 (not_8_out, Funct4);
  not not_9 (not_9_out, Funct5);
  not not_10 (not_10_out, Funct1);
  not not_11 (not_11_out, Funct2);
  not not_12 (not_12_out, Funct3);
  not not_13 (not_13_out, Funct4);
  not not_14 (not_14_out, Funct1);
  not not_15 (not_15_out, Funct2);
  not not_16 (not_16_out, Funct3);
  not not_17 (not_17_out, Funct5);
  not not_18 (not_18_out, Funct1);
  not not_19 (not_19_out, Funct2);
  not not_20 (not_20_out, Funct4);
  not not_21 (not_21_out, Funct1);
  not not_22 (not_22_out, Funct2);
  not not_23 (not_23_out, Funct1);
  not not_24 (not_24_out, Funct3);
  not not_25 (not_25_out, Funct5);
  not not_26 (not_26_out, Funct1);
  not not_27 (not_27_out, Funct3);
  not not_28 (not_28_out, Funct0);
  not not_29 (not_29_out, Funct1);
  not not_30 (not_30_out, Funct3);
  not not_31 (not_31_out, Funct4);
  not not_32 (not_32_out, Funct5);
  not not_33 (not_33_out, Funct1);
  not not_34 (not_34_out, Funct2);
  not not_35 (not_35_out, Funct3);
  not not_36 (not_36_out, Funct4);
  not not_37 (not_37_out, Funct5);
  not not_38 (not_38_out, Funct1);
  not not_39 (not_39_out, Funct2);
  not not_40 (not_40_out, Funct3);
  not not_41 (not_41_out, Funct4);
  not not_42 (not_42_out, Funct1);
  not not_43 (not_43_out, Funct2);
  not not_44 (not_44_out, Funct4);
  not not_45 (not_45_out, Funct5);
  not not_46 (not_46_out, Funct0);
  not not_47 (not_47_out, Funct1);
  not not_48 (not_48_out, Funct2);
  not not_49 (not_49_out, Funct3);
  not not_50 (not_50_out, Funct4);
  not not_51 (not_51_out, Funct5);
  not not_52 (not_52_out, Funct0);
  not not_53 (not_53_out, Funct1);
  not not_54 (not_54_out, Funct2);
  not not_55 (not_55_out, Funct3);
  not not_56 (not_56_out, Funct0);
  not not_57 (not_57_out, Funct1);
  not not_58 (not_58_out, Funct2);
  not not_59 (not_59_out, Funct3);
  not not_60 (not_60_out, Funct5);
  not not_61 (not_61_out, Funct1);
  not not_62 (not_62_out, Funct2);
  not not_63 (not_63_out, Funct3);
  not not_64 (not_64_out, Funct5);
  not not_65 (not_65_out, Funct1);
  not not_66 (not_66_out, Funct2);
  not not_67 (not_67_out, Funct4);
  not not_68 (not_68_out, Funct1);
  not not_69 (not_69_out, Funct2);
  not not_70 (not_70_out, Funct1);
  not not_71 (not_71_out, Funct3);
  not not_72 (not_72_out, Funct5);
  not not_73 (not_73_out, Funct1);
  not not_74 (not_74_out, Funct3);
  and and_1 (and_1_out, Funct0, not_1_out, not_2_out, not_3_out, not_4_out, not_5_out);
  and and_2 (and_2_out, Funct0, not_6_out, not_7_out, Funct3, not_8_out, not_9_out);
  and and_3 (and_3_out, Funct0, not_10_out, not_11_out, not_12_out, not_13_out, Funct5);
  and and_4 (and_4_out, Funct0, not_14_out, not_15_out, not_16_out, Funct4, not_17_out);
  and and_5 (and_5_out, Funct0, not_18_out, not_19_out, Funct3, not_20_out, Funct5);
  and and_6 (and_6_out, Funct0, not_21_out, not_22_out, Funct3, Funct4, Funct5);
  and and_7 (and_7_out, Funct0, not_23_out, Funct2, not_24_out, Funct4, not_25_out);
  and and_8 (and_8_out, Funct0, not_26_out, Funct2, not_27_out, Funct4, Funct5);
  and and_9 (and_9_out, not_28_out, not_29_out, Funct2, not_30_out, not_31_out, not_32_out);
  and and_10 (and_10_out, Funct0, not_33_out, not_34_out, not_35_out, not_36_out, not_37_out);
  and and_11 (and_11_out, Funct0, not_38_out, not_39_out, not_40_out, not_41_out, Funct5);
  and and_12 (and_12_out, Funct0, not_42_out, not_43_out, Funct3, not_44_out, not_45_out);
  and and_13 (and_13_out, not_46_out, not_47_out, not_48_out, not_49_out, not_50_out, not_51_out);
  and and_14 (and_14_out, not_52_out, not_53_out, not_54_out, not_55_out, Funct4, Funct5);
  and and_15 (and_15_out, not_56_out, not_57_out, not_58_out, not_59_out, Funct4, not_60_out);
  and and_16 (and_16_out, Funct0, not_61_out, not_62_out, not_63_out, Funct4, not_64_out);
  and and_17 (and_17_out, Funct0, not_65_out, not_66_out, Funct3, not_67_out, Funct5);
  and and_18 (and_18_out, Funct0, not_68_out, not_69_out, Funct3, Funct4, Funct5);
  and and_19 (and_19_out, Funct0, not_70_out, Funct2, not_71_out, Funct4, not_72_out);
  and and_20 (and_20_out, Funct0, not_73_out, Funct2, not_74_out, Funct4, Funct5);
  not not_75 (not_75_out, op0);
  not not_76 (not_76_out, op1);
  not not_77 (not_77_out, op2);
  not not_78 (not_78_out, op3);
  not not_79 (not_79_out, op4);
  not not_80 (not_80_out, op5);
  or or_1 (or_1_out, and_1_out, and_2_out, and_3_out, and_4_out, and_5_out, and_6_out, and_7_out, and_8_out, and_9_out);
  not not_81 (not_81_out, op0);
  not not_82 (not_82_out, op1);
  not not_83 (not_83_out, op3);
  not not_84 (not_84_out, op4);
  not not_85 (not_85_out, op5);
  not not_86 (not_86_out, op0);
  not not_87 (not_87_out, op1);
  not not_88 (not_88_out, op3);
  not not_89 (not_89_out, op4);
  not not_90 (not_90_out, op0);
  not not_91 (not_91_out, op1);
  not not_92 (not_92_out, op4);
  not not_93 (not_93_out, op5);
  not not_94 (not_94_out, op0);
  not not_95 (not_95_out, op1);
  not not_96 (not_96_out, op4);
  not not_97 (not_97_out, op1);
  not not_98 (not_98_out, op2);
  not not_99 (not_99_out, op3);
  not not_100 (not_100_out, op0);
  not not_101 (not_101_out, op1);
  not not_102 (not_102_out, op2);
  not not_103 (not_103_out, op4);
  not not_104 (not_104_out, op5);
  not not_105 (not_105_out, op0);
  not not_106 (not_106_out, op1);
  not not_107 (not_107_out, op2);
  not not_108 (not_108_out, op4);
  not not_109 (not_109_out, op0);
  not not_110 (not_110_out, op1);
  not not_111 (not_111_out, op3);
  not not_112 (not_112_out, op5);
  not not_113 (not_113_out, op1);
  not not_114 (not_114_out, op3);
  not not_115 (not_115_out, op0);
  not not_116 (not_116_out, op1);
  not not_117 (not_117_out, op2);
  not not_118 (not_118_out, op3);
  not not_119 (not_119_out, op4);
  not not_120 (not_120_out, op5);
  or or_2 (or_2_out, and_10_out, and_11_out, and_12_out, and_13_out, and_14_out, and_15_out, and_16_out, and_17_out, and_18_out, and_19_out, and_20_out);
  not not_121 (not_121_out, op0);
  not not_122 (not_122_out, op1);
  not not_123 (not_123_out, op2);
  not not_124 (not_124_out, op4);
  not not_125 (not_125_out, op5);
  not not_126 (not_126_out, op0);
  not not_127 (not_127_out, op1);
  not not_128 (not_128_out, op2);
  not not_129 (not_129_out, op4);
  not not_130 (not_130_out, op0);
  not not_131 (not_131_out, op2);
  not not_132 (not_132_out, op3);
  not not_133 (not_133_out, op4);
  not not_134 (not_134_out, op5);
  not not_135 (not_135_out, op1);
  not not_136 (not_136_out, op3);
  and and_21 (and_21_out, not_75_out, not_76_out, not_77_out, not_78_out, not_79_out, not_80_out, or_1_out);
  and and_22 (and_22_out, not_81_out, not_82_out, op2, not_83_out, not_84_out, not_85_out);
  and and_23 (and_23_out, not_86_out, not_87_out, op2, not_88_out, not_89_out, op5);
  and and_24 (and_24_out, not_90_out, not_91_out, op2, op3, not_92_out, not_93_out);
  and and_25 (and_25_out, not_94_out, not_95_out, op2, op3, not_96_out, op5);
  and and_26 (and_26_out, op0, not_97_out, not_98_out, not_99_out, op4, op5);
  and and_27 (and_27_out, not_100_out, not_101_out, not_102_out, op3, not_103_out, not_104_out);
  and and_28 (and_28_out, not_105_out, not_106_out, not_107_out, op3, not_108_out, op5);
  and and_29 (and_29_out, not_109_out, not_110_out, op2, not_111_out, op4, not_112_out);
  and and_30 (and_30_out, op0, not_113_out, op2, not_114_out, op4, op5);
  and and_31 (and_31_out, not_115_out, not_116_out, not_117_out, not_118_out, not_119_out, not_120_out, or_2_out);
  and and_32 (and_32_out, not_121_out, not_122_out, not_123_out, op3, not_124_out, not_125_out);
  and and_33 (and_33_out, not_126_out, not_127_out, not_128_out, op3, not_129_out, op5);
  and and_34 (and_34_out, not_130_out, op1, not_131_out, not_132_out, not_133_out, not_134_out);
  and and_35 (and_35_out, op0, not_135_out, op2, not_136_out, op4, op5);
  or or_3 (ReadRs, and_21_out, and_22_out, and_23_out, and_24_out, and_25_out, and_26_out, and_27_out, and_28_out, and_29_out, and_30_out);
  or or_4 (ReadRt, and_31_out, and_32_out, and_33_out, and_34_out, and_35_out);
endmodule

module Hazard_Detector (
  input  Read,
  input  RegWrite,
  input  [4:0] WriteReg,
  input  [4:0] Register_num,
  output Hazard
);

  wire comparator_1_eq, comparator_2_eq, not_1_out;

  not not_1 (not_1_out, comparator_1_eq);
  Comparator #(.width(5)) comparator_1 (.a({5{1'b0}}), .b(WriteReg), .eq(comparator_1_eq));  // open: gt, lt
  Comparator #(.width(5)) comparator_2 (.a(WriteReg), .b(Register_num), .eq(comparator_2_eq));  // open: gt, lt
  and and_1 (Hazard, Read, RegWrite, not_1_out, comparator_2_eq);
endmodule

module CP0 (
  input  ExpSrc0,
  input  clk,
  input  ExpSrc1,
  input  enable,
  input  ExpSrc2,
  input  [31:0] Inst,
  input  [31:0] PCin,
  input  [31:0] Din,
  output ExRegWrite,
  output IsEret,
  output ExpBlock,
  output HasExp,
  output [31:0] PCout,
  output [31:0] Dout
);

  wire and_4_out, and_5_out, and_6_out, and_7_out, BlockSrc0, BlockSrc1, BlockSrc2, counter_1_q, counter_2_q,
       demultiplexer_1_out0, demultiplexer_1_out1, demultiplexer_2_out0, demultiplexer_2_out1,
       demultiplexer_3_out0, demultiplexer_3_out1, demultiplexer_4_out0, demultiplexer_4_out1,
       demultiplexer_4_out2, ExpClick, not_2_out, not_3_out, or_1_out, or_2_out;
  wire [31:0] Cause_q, controlled_buffer_1_out, multiplexer_1_out;
  wire [31:1] Status_q;
  wire [31:3] Block_q;

  Demultiplexer #(.enable("false")) demultiplexer_1 (
    .out0(demultiplexer_1_out0), .out1(demultiplexer_1_out1), .in(ExpSrc0), .sel(BlockSrc0));
  or or_1 (or_1_out, demultiplexer_1_out0, demultiplexer_2_out0, demultiplexer_3_out0);
  Demultiplexer #(.enable("false")) demultiplexer_2 (
    .out0(demultiplexer_2_out0), .out1(demultiplexer_2_out1), .in(ExpSrc1), .sel(BlockSrc1));
  and and_1 (ExpClick, or_1_out, ~ExpBlock);  // AND_Gate
  Demultiplexer #(.enable("false")) demultiplexer_3 (
    .out0(demultiplexer_3_out0), .out1(demultiplexer_3_out1), .in(ExpSrc2), .sel(BlockSrc2));
  not not_1 (ExRegWrite, Inst[23]);
  and and_2 (IsEret, ~Inst[5], Inst[4], Inst[3], ~Inst[2], ~Inst[1], ~Inst[0]);  // AND_Gate
  Counter #(.width(1), .max('h1), .ongoal("stay")) counter_1 (
    .Q(counter_1_q), .clk(ExpClick), .clr(counter_2_q));  // open: load, D, count, carry
  and and_3 (HasExp, clk, counter_1_q);
  Counter #(.width(1), .max('h1), .ongoal("stay"), .trigger("falling")) counter_2 (
    .Q(counter_2_q), .clk(HasExp), .clr(not_2_out));  // open: load, D, count, carry
  not not_2 (not_2_out, counter_1_q);
  not not_3 (not_3_out, HasExp);
  Multiplexer #(.width(32), .enable("false")) multiplexer_1 (
    .in0(PCin), .in1(Din), .out(multiplexer_1_out), .sel(not_3_out));
  and and_4 (and_4_out, enable, ~ExRegWrite);  // AND_Gate
  Demultiplexer #(.select(2), .disabled(0), .enable("false")) demultiplexer_4 (
    .out0(demultiplexer_4_out0), .out1(demultiplexer_4_out1), .out2(demultiplexer_4_out2), .in(1'b1),
    .sel(Inst[12:11]));  // open: out3
  assign controlled_buffer_1_out = ExpSrc0 ? 32'h1 : 32'bz;  // Controlled_Buffer controlled_buffer_1
  assign controlled_buffer_1_out = ExpSrc1 ? 32'h3 : 32'bz;  // Controlled_Buffer controlled_buffer_2
  assign controlled_buffer_1_out = ExpSrc2 ? 32'h7 : 32'bz;  // Controlled_Buffer controlled_buffer_3
  or or_2 (or_2_out, HasExp, and_5_out);
  and and_5 (and_5_out, demultiplexer_4_out0, and_4_out);
  and and_6 (and_6_out, demultiplexer_4_out1, and_4_out);
  and and_7 (and_7_out, demultiplexer_4_out2, and_4_out);
  Register #(.width(32), .trigger("low")) EPC (
    .D(multiplexer_1_out), .en(or_2_out), .Q(PCout), .clk(clk));  // open: clr
  Register #(.width(32)) Status (.D(Din), .en(and_6_out), .Q({Status_q, ExpBlock}), .clk(clk));  // open: clr
  Register #(.width(32)) Block (
    .D(Din), .en(and_7_out), .Q({Block_q, BlockSrc2, BlockSrc1, BlockSrc0}), .clk(clk));  // open: clr
  Register #(.width(32)) Cause (.D(controlled_buffer_1_out), .Q(Cause_q), .clk(ExpClick));  // open: en, clr
  Multiplexer #(.select(2), .width(32), .enable("false")) multiplexer_2 (
    .in0(PCout), .in1({Status_q, ExpBlock}), .in2({Block_q, BlockSrc2, BlockSrc1, BlockSrc0}), .in3(Cause_q),
    .out(Dout), .sel(Inst[12:11]));
  // also tied to GND on the sheet: {demultiplexer_1_out1, demultiplexer_2_out1, demultiplexer_3_out1}

  // Other names for the same wires on the sheet: Sel[1:0] = Inst[12:11]

  // Notes on the sheet:
  //   Exception Signals
  //   Signal Decoding
  //   Input & Output
  //   Registers
endmodule

module RegWrite_Decider (
  input  RegWrite,
  input  ExRegWrite,
  input  IsException,
  output FinalRegWrite
);

  Multiplexer #(.enable("false")) multiplexer_1 (
    .in0(RegWrite), .in1(ExRegWrite), .out(FinalRegWrite), .sel(IsException));
endmodule
