// Logisim project Single_Cycle_CPU.circ as structural Verilog: 4 circuits, main circuit main
module main (
);

  wire ALUop, ALUSrc, and_1_out, BneOrBeq, Branch, buffer_1_out, clk, clock_1_out, Halt, Jump, MemRead,
       MemtoReg, MemWrite, not_1_out, not_2_out, RegDst, RegWrite, xor_1_out, Zero;
  wire [3:0] alu_control_1_alu;
  wire [4:0] multiplexer_2_out, Rs, Rt;
  wire [5:0] Funct, OP;
  wire [15:6] Immediate;
  wire [25:0] shifter_1_out;
  wire [31:0] adder_1_out, adder_2_out, alu_1_result, bit_extender_1_out, Cycle_q, main_1_reg1,
       main_1_reg2_2, multiplexer_3_out, multiplexer_4_out, multiplexer_5_out, multiplexer_6_out, PC_q, ra,
       ram_1_data, s0, s1, s2, shifter_2_out;

  Multiplexer #(.enable("false")) multiplexer_1 (.in0(clock_1_out), .in1(1'b1), .out(clk), .sel(Halt));
  Clock clock_1 (.out(clock_1_out));
  Register #(.width(32), .trigger("falling")) PC (.D(multiplexer_5_out), .Q(PC_q), .clk(clk));  // open: en, clr
  Adder #(.width(32)) adder_1 (.a(32'h4), .b(PC_q), .out(adder_1_out));  // open: cin, cout
  // Probe on s0
  // Probe on s1
  // Probe on s2
  // Probe on ra
  Counter #(.width(32), .max('hffffffff)) Cycle (.Q(Cycle_q), .clk(clk));  // open: load, D, count, carry, clr
  // Probe on {OP, Rs, Rt, Immediate, Funct}
  ROM #(.addrWidth(10), .dataWidth(32)) rom_1 (.addr(PC_q[11:2]), .data({OP, Rs, Rt, Immediate, Funct}));  // open: sel
  // Probe on Cycle_q
  Shifter #(.width(26)) shifter_1 (.in({Rs, Rt, Immediate, Funct}), .\dist (5'b00010), .out(shifter_1_out));
  Control control_1 (
    .op(OP), .MemRead(MemRead), .MemWrite(MemWrite), .ALUSrc(ALUSrc), .ALUop(ALUop), .Jump(Jump),
    .MemtoReg(MemtoReg), .Branch(Branch), .RegDst(RegDst), .RegWrite(RegWrite), .BneOrBeq(BneOrBeq));
  Multiplexer #(.width(5), .enable("false")) multiplexer_2 (
    .in0(Rt), .in1(Immediate[15:11]), .out(multiplexer_2_out), .sel(RegDst));
  regfile_main main_1 (
    .Reg1_num(Rs), .Reg2(Rt), .Write_Reg_num(multiplexer_2_out), .Din(multiplexer_6_out),
    .Write_Enable(RegWrite), .Clock(clk), .Reg1(main_1_reg1), .Reg2_2(main_1_reg2_2), .s0_Value(s0),
    .s1_Value(s1), .s2_Value(s2), .ra_Value(ra));
  assign bit_extender_1_out = {{16{Immediate[15]}}, {Immediate, Funct}};  // Bit_Extender bit_extender_1
  Shifter #(.width(32)) shifter_2 (.in(bit_extender_1_out), .\dist (5'b00010), .out(shifter_2_out));
  // Probe on OP
  // Probe on Rs
  ALU alu_1 (
    .AluOP(alu_control_1_alu), .X(main_1_reg1), .Equal(Zero), .Result(alu_1_result), .Y(multiplexer_3_out));  // open: Signed_Overflow, Result_2, UnSigned_Overflow
  Multiplexer #(.width(32), .enable("false")) multiplexer_3 (
    .in0(main_1_reg2_2), .in1(bit_extender_1_out), .out(multiplexer_3_out), .sel(ALUSrc));
  ALU_Control alu_control_1 (.ALU(alu_control_1_alu), .ALUop(ALUop), .Funct(Funct), .Halt(Halt));
  // Probe on Rt
  Adder #(.width(32)) adder_2 (.a(adder_1_out), .b(shifter_2_out), .out(adder_2_out));  // open: cin, cout
  xor xor_1 (xor_1_out, Zero, BneOrBeq);
  // Probe on Immediate[15:11]
  buf buffer_1 (buffer_1_out, MemWrite);
  Multiplexer #(.width(32), .enable("false")) multiplexer_4 (
    .in0(adder_1_out), .in1(adder_2_out), .out(multiplexer_4_out), .sel(and_1_out));
  not not_1 (not_1_out, Jump);
  and and_1 (and_1_out, Branch, xor_1_out);
  // Probe on Funct
  RAM #(.addrWidth(10), .dataWidth(32), .bus("separate")) ram_1 (
    .addr(alu_1_result[11:2]), .din(main_1_reg2_2), .data(ram_1_data), .str(buffer_1_out), .clk(clk),
    .ld(MemRead));  // open: sel, clr
  Multiplexer #(.width(32), .enable("false")) multiplexer_5 (
    .in0({adder_1_out[31:28], shifter_1_out, 2'b00}), .in1(multiplexer_4_out), .out(multiplexer_5_out),
    .sel(not_1_out));
  // Probe on {Immediate, Funct}
  Multiplexer #(.width(32), .enable("false")) multiplexer_6 (
    .in0(ram_1_data), .in1(alu_1_result), .out(multiplexer_6_out), .sel(not_2_out));
  not not_2 (not_2_out, MemtoReg);

  // Other names for the same wires on the sheet: Immediate[5:0] = Funct; Rd[4:0] = Immediate[15:11]

  // Notes on the sheet:
  //   contents of rom_1 (hex, n*v repeats v):
  //   2010ffff 20110000 ae300000 22100001 22310004 ae300000 22100001 22310004 ae300000 22100001 22310004
  //   ae300000 22100001 22310004 ae300000 22100001 22310004 ae300000 22100001 22310004 ae300000 22100001
  //   22310004 ae300000 22100001 22310004 ae300000 22100001 22310004 ae300000 22100001 22310004 ae300000
  //   22100001 22310004 ae300000 22100001 22310004 ae300000 22100001 22310004 ae300000 22100001 22310004
  //   ae300000 22100001 22310004 ae300000 22100001 22310004 22100001 8020 2011003c 8e130000 8e340000
  //   274402a 11000002 ae330000 ae140000 2231fffc 1611fff8 22100004 2011003c 1611fff5 2002000a c
endmodule

module ALU_Control (
  input  [5:0] Funct,
  input  ALUop,
  output Halt,
  output [3:0] ALU
);

  wire comparator_1_eq;
  wire [3:0] multiplexer_1_out, multiplexer_2_out, multiplexer_3_out;

  Multiplexer #(.select(5), .width(4), .enable("false")) multiplexer_1 (
    .in12(4'b0000), .out(multiplexer_1_out), .sel(Funct[4:0]));  // open: in0, in1, in2, in3, in4, in5, in6, in7, in8, in9, in10, in11, in13, in14, in15, in16, in17, in18, in19, in20, in21, in22, in23, in24, in25, in26, in27, in28, in29, in30, in31
  Multiplexer #(.select(5), .width(4), .enable("false")) multiplexer_2 (
    .in0(4'b0101), .in10(4'b1011), .out(multiplexer_2_out), .sel(Funct[4:0]));  // open: in1, in2, in3, in4, in5, in6, in7, in8, in9, in11, in12, in13, in14, in15, in16, in17, in18, in19, in20, in21, in22, in23, in24, in25, in26, in27, in28, in29, in30, in31
  Multiplexer #(.width(4), .enable("false")) multiplexer_3 (
    .in0(multiplexer_1_out), .in1(multiplexer_2_out), .out(multiplexer_3_out), .sel(Funct[5]));
  Comparator #(.width(6)) comparator_1 (.a(6'b001100), .b(Funct), .eq(comparator_1_eq));  // open: gt, lt
  Multiplexer #(.width(4), .enable("false")) multiplexer_4 (
    .in0(4'b0101), .in1(multiplexer_3_out), .out(ALU), .sel(ALUop));
  and and_1 (Halt, comparator_1_eq, ALUop);
endmodule

module Control (
  input  [5:0] op,
  output MemRead,
  output MemWrite,
  output ALUSrc,
  output ALUop,
  output Jump,
  output MemtoReg,
  output Branch,
  output RegDst,
  output RegWrite,
  output BneOrBeq
);

  wire and_6_out, and_7_out, not_1_out, not_2_out, not_3_out, not_4_out, not_5_out, not_6_out, not_7_out,
       not_8_out, not_9_out, not_10_out, not_11_out, not_12_out, not_13_out;

  not not_1 (not_1_out, op[3]);
  and and_1 (MemWrite, op[5], op[3]);
  or or_1 (ALUSrc, op[1], op[3]);
  not not_2 (not_2_out, op[3]);
  not not_3 (not_3_out, op[2]);
  not not_4 (not_4_out, op[1]);
  not not_5 (not_5_out, op[3]);
  not not_6 (not_6_out, op[3]);
  not not_7 (not_7_out, op[2]);
  not not_8 (not_8_out, op[1]);
  not not_9 (not_9_out, op[3]);
  not not_10 (not_10_out, op[2]);
  not not_11 (not_11_out, op[2]);
  not not_12 (not_12_out, op[1]);
  not not_13 (not_13_out, op[1]);
  and and_2 (MemRead, not_1_out, op[1]);
  and and_3 (ALUop, not_2_out, not_3_out, not_4_out);
  and and_4 (MemtoReg, op[5], not_5_out);
  and and_5 (RegDst, not_6_out, not_7_out, not_8_out);
  and and_6 (and_6_out, not_9_out, not_10_out);
  or or_2 (RegWrite, and_6_out, and_7_out);
  and and_7 (and_7_out, not_11_out, not_12_out);
  and and_8 (BneOrBeq, not_13_out, op[0]);

  assign Branch = op[2];
  assign Jump = 1'b0;
endmodule

module _333 (
  input  op1,
  input  op2,
  input  op3,
  input  op4,
  input  op5,
  input  op6,
  output MemRead,
  output MemWrite,
  output ALUSrc,
  output ALUop,
  output Jump,
  output MemtoReg,
  output Branch,
  output RegDst,
  output RegWrite,
  output BneOrBeq
);

  wire and_6_out, and_7_out, not_1_out, not_2_out, not_3_out, not_4_out, not_5_out, not_6_out, not_7_out,
       not_8_out, not_9_out, not_10_out, not_11_out, not_12_out, not_13_out;

  not not_1 (not_1_out, op3);
  and and_1 (MemWrite, op1, op3);
  or or_1 (ALUSrc, op5, op3);
  not not_2 (not_2_out, op3);
  not not_3 (not_3_out, op4);
  not not_4 (not_4_out, op5);
  not not_5 (not_5_out, op3);
  not not_6 (not_6_out, op3);
  not not_7 (not_7_out, op4);
  not not_8 (not_8_out, op5);
  not not_9 (not_9_out, op3);
  not not_10 (not_10_out, op4);
  not not_11 (not_11_out, op4);
  not not_12 (not_12_out, op5);
  not not_13 (not_13_out, op5);
  and and_2 (MemRead, not_1_out, op5);
  and and_3 (ALUop, not_2_out, not_3_out, not_4_out);
  and and_4 (MemtoReg, op1, not_5_out);
  and and_5 (RegDst, not_6_out, not_7_out, not_8_out);
  and and_6 (and_6_out, not_9_out, not_10_out);
  and and_7 (and_7_out, not_11_out, not_12_out);
  and and_8 (BneOrBeq, not_13_out, op6);
  or or_2 (RegWrite, and_6_out, and_7_out);

  assign Branch = op4;
  assign Jump = 1'b0;
endmodule
