// Logisim project alu.circ as structural Verilog: 8 circuits, main circuit ALU
module ALU (
  input  [31:0] X,
  input  [31:0] Y,
  input  [3:0] AluOP,
  output Signed_Overflow,
  output UnSigned_Overflow,
  output Equal,
  output [31:0] Result,
  output [31:0] Result_2
);

  wire comparator_1_lt, comparator_2_lt;
  wire [1:0] \n32位溢出检测减法_1_cf , \n32位溢出检测加法_1_cf ;
  wire [31:0] and_1_out, bit_extender_1_out, bit_extender_2_out, divider_1_out, divider_1_rem,
       multiplier_1_cout, multiplier_1_out, \n32位左移_1_result_of_the_operation ,
       \n32位溢出检测减法_1_result_of_the_operation , \n32位溢出检测加法_1_result_of_the_operation ,
       \n32位运算右移_1_result_of_the_operation , \n32位逻辑右移_1_result_of_the_operation , not_1_out, or_1_out,
       or_2_out, xor_1_out;

  // Probe on X
  // Probe on X
  // Probe on Y
  // Probe on Y
  // Probe on AluOP
  \_32位左移  \u_32位左移_1  (.X(X), .Y(Y), .Result_of_the_operation(\n32位左移_1_result_of_the_operation ));
  \_32位运算右移  \u_32位运算右移_1  (.X(X), .Y(Y), .Result_of_the_operation(\n32位运算右移_1_result_of_the_operation ));
  \_32位逻辑右移  \u_32位逻辑右移_1  (.X(X), .Y(Y), .Result_of_the_operation(\n32位逻辑右移_1_result_of_the_operation ));
  \_32位溢出检测加法  \u_32位溢出检测加法_1  (
    .X(X), .Y(Y), .Result_of_the_operation(\n32位溢出检测加法_1_result_of_the_operation ),
    .CF(\n32位溢出检测加法_1_cf [0]), .OF(\n32位溢出检测加法_1_cf [1]));  // open: in_3
  \_32位溢出检测减法  \u_32位溢出检测减法_1  (
    .X(X), .Y(Y), .Result_of_the_operation(\n32位溢出检测减法_1_result_of_the_operation ),
    .CF(\n32位溢出检测减法_1_cf [0]), .OF(\n32位溢出检测减法_1_cf [1]));  // open: in_3
  // Probe on Result
  // Probe on Result
  Multiplier #(.width(32)) multiplier_1 (.a(X), .b(Y), .out(multiplier_1_out), .cout(multiplier_1_cout));  // open: cin
  Divider #(.width(32)) divider_1 (.a(X), .b(Y), .out(divider_1_out), .rem(divider_1_rem));  // open: upper
  assign and_1_out = X & Y;  // AND_Gate and_1, 32 bits wide
  assign or_1_out = X | Y;  // OR_Gate or_1, 32 bits wide
  assign xor_1_out = X ^ Y;  // XOR_Gate xor_1, 32 bits wide
  assign not_1_out = ~or_2_out;  // NOT_Gate not_1, 32 bits wide
  assign or_2_out = X | Y;  // OR_Gate or_2, 32 bits wide
  Comparator #(.width(32)) comparator_1 (.a(X), .b(Y), .lt(comparator_1_lt));  // open: gt, eq
  Comparator #(.width(32), .mode("unsigned")) comparator_2 (
    .a(X), .b(Y), .eq(Equal), .lt(comparator_2_lt));  // open: gt
  Multiplexer #(.select(4), .width(2), .enable("false")) multiplexer_1 (
    .in0(2'b00), .in1(2'b00), .in2(2'b00), .in3(2'b00), .in4(2'b00), .in5(\n32位溢出检测加法_1_cf ),
    .in6(\n32位溢出检测减法_1_cf ), .in7(2'b00), .in8(2'b00), .in9(2'b00), .in10(2'b00), .in11(2'b00), .in12(2'b00),
    .in13(2'b00), .in14(2'b00), .in15(2'b00), .out({Signed_Overflow, UnSigned_Overflow}), .sel(AluOP));
  // Probe on Result_2
  Multiplexer #(.select(4), .width(32), .enable("false")) multiplexer_2 (
    .in0({32{1'b0}}), .in1({32{1'b0}}), .in2({32{1'b0}}), .in3(multiplier_1_cout), .in4(divider_1_rem),
    .in5({32{1'b0}}), .in6({32{1'b0}}), .in7({32{1'b0}}), .in8({32{1'b0}}), .in9({32{1'b0}}),
    .in10({32{1'b0}}), .in11({32{1'b0}}), .in12({32{1'b0}}), .in13({32{1'b0}}), .in14({32{1'b0}}),
    .in15({32{1'b0}}), .out(Result_2), .sel(AluOP));
  assign bit_extender_1_out = {{31{1'b0}}, comparator_1_lt};  // Bit_Extender bit_extender_1
  assign bit_extender_2_out = {{31{1'b0}}, comparator_2_lt};  // Bit_Extender bit_extender_2
  Multiplexer #(.select(4), .width(32), .enable("false")) multiplexer_3 (
    .in0(\n32位左移_1_result_of_the_operation ), .in1(\n32位运算右移_1_result_of_the_operation ),
    .in2(\n32位逻辑右移_1_result_of_the_operation ), .in3(multiplier_1_out), .in4(divider_1_out),
    .in5(\n32位溢出检测加法_1_result_of_the_operation ), .in6(\n32位溢出检测减法_1_result_of_the_operation ),
    .in7(and_1_out), .in8(or_1_out), .in9(xor_1_out), .in10(not_1_out), .in11(bit_extender_1_out),
    .in12(bit_extender_2_out), .in13({32{1'b0}}), .in14({32{1'b0}}), .in15({32{1'b0}}), .out(Result),
    .sel(AluOP));

  // Other names for the same wires on the sheet: CF = UnSigned_Overflow; OF = Signed_Overflow;
  //   Result2[31:0] = Result_2; S[3:0] = AluOP

  // Notes on the sheet:
  //   不要改变此引脚区域内容，也不要改变ALU封装形式
  //   输入引脚
  //   请在下方利用上方输入输出引脚的隧道信号构建ALU电路，ctrl+d复制选择部件
  //   华中科技大学计算机学院 计算机组成原理，鸣谢加州大学伯克利CS61C课程
  //   输出引脚
  //   探测区域
endmodule

// 加法器
module \_32位溢出检测加法  (
  input  [31:0] X,
  input  [31:0] Y,
  input  in_3,
  output [31:0] Result_of_the_operation,
  output CF,
  output OF
);

  wire adder_1_cout;

  // Probe on X
  Adder #(.width(31)) adder_1 (
    .a(X[30:0]), .b(Y[30:0]), .out(Result_of_the_operation[30:0]), .cin(in_3), .cout(adder_1_cout));
  Adder #(.width(1)) adder_2 (.a(X[31]), .b(Y[31]), .out(Result_of_the_operation[31]), .cin(adder_1_cout), .cout(CF));
  // Probe on Y
  xor xor_1 (OF, adder_1_cout, CF);
  // Probe on Result_of_the_operation

  // Other names for the same wires on the sheet: cin = in_3; Result[31:0] = Result_of_the_operation
endmodule

// 减法器
module \_32位溢出检测减法  (
  input  [31:0] X,
  input  [31:0] Y,
  input  in_3,
  output [31:0] Result_of_the_operation,
  output CF,
  output OF
);

  wire subtractor_1_bout;

  // Probe on X
  Subtractor #(.width(31)) subtractor_1 (
    .a(X[30:0]), .b(Y[30:0]), .out(Result_of_the_operation[30:0]), .bin(in_3), .bout(subtractor_1_bout));
  Subtractor #(.width(1)) subtractor_2 (
    .a(X[31]), .b(Y[31]), .out(Result_of_the_operation[31]), .bin(subtractor_1_bout), .bout(CF));
  // Probe on Y
  xor xor_1 (OF, subtractor_1_bout, CF);
  // Probe on Result_of_the_operation

  // Other names for the same wires on the sheet: bin = in_3; Result[31:0] = Result_of_the_operation
endmodule

module \_32位左移  (
  input  [31:0] X,
  input  [31:0] Y,
  output [31:0] Result_of_the_operation
);

  wire comparator_1_gt;
  wire [31:0] shifter_1_out;

  // Probe on X
  Comparator #(.width(32), .mode("unsigned")) comparator_1 (.a(Y), .b(32'h31), .gt(comparator_1_gt));  // open: eq, lt
  // Probe on Y
  Shifter #(.width(32)) shifter_1 (.in(X), .\dist (Y[4:0]), .out(shifter_1_out));
  Multiplexer #(.width(32), .enable("false")) multiplexer_1 (
    .in0(shifter_1_out), .in1({32{1'b0}}), .out(Result_of_the_operation), .sel(comparator_1_gt));
  // Probe on Result_of_the_operation

  // Other names for the same wires on the sheet: Result[31:0] = Result_of_the_operation
endmodule

module \_32位逻辑右移  (
  input  [31:0] X,
  input  [31:0] Y,
  output [31:0] Result_of_the_operation
);

  wire comparator_1_gt;
  wire [31:0] shifter_1_out;

  // Probe on X
  Comparator #(.width(32), .mode("unsigned")) comparator_1 (.a(Y), .b(32'h31), .gt(comparator_1_gt));  // open: eq, lt
  // Probe on Y
  Shifter #(.width(32), .shift("lr")) shifter_1 (.in(X), .\dist (Y[4:0]), .out(shifter_1_out));
  Multiplexer #(.width(32), .enable("false")) multiplexer_1 (
    .in0(shifter_1_out), .in1({32{1'b0}}), .out(Result_of_the_operation), .sel(comparator_1_gt));
  // Probe on Result_of_the_operation

  // Other names for the same wires on the sheet: Result[31:0] = Result_of_the_operation
endmodule

module \_32位运算右移  (
  input  [31:0] X,
  input  [31:0] Y,
  output [31:0] Result_of_the_operation
);

  wire comparator_1_gt;
  wire [31:0] bit_extender_1_out, shifter_1_out;

  // Probe on X
  Comparator #(.width(32), .mode("unsigned")) comparator_1 (.a(Y), .b(32'h31), .gt(comparator_1_gt));  // open: eq, lt
  // Probe on Y
  Shifter #(.width(32), .shift("ar")) shifter_1 (.in(X), .\dist (Y[4:0]), .out(shifter_1_out));
  assign bit_extender_1_out = {{31{X[31]}}, X[31]};  // Bit_Extender bit_extender_1
  Multiplexer #(.width(32), .enable("false")) multiplexer_1 (
    .in0(shifter_1_out), .in1(bit_extender_1_out), .out(Result_of_the_operation), .sel(comparator_1_gt));
  // Probe on Result_of_the_operation

  // Other names for the same wires on the sheet: Result[31:0] = Result_of_the_operation
endmodule

module \演示电路  (
  input  [31:0] X,
  input  [31:0] Y,
  input  [3:0] ALUOP,
  output Signed_Overflow,
  output Unsigned_overflow,
  output [31:0] Result,
  output [31:0] Result_2,
  output Equal
);

  // Probe on X
  // Probe on X
  ALU alu_1 (
    .AluOP(ALUOP), .X(X), .Equal(Equal), .Result(Result), .Signed_Overflow(Signed_Overflow), .Y(Y),
    .Result_2(Result_2), .UnSigned_Overflow(Unsigned_overflow));
  // Probe on ALUOP
  // Probe on Y
  // Probe on Y
  // Probe on Result
  // Probe on Result
  // Probe on Result_2
endmodule

module \等差数列求和  (
  input  [31:0] Difference_Value,
  input  [31:0] Initial_Value,
  input  in_3
);

  wire clock_1_out, comparator_1_eq, comparator_2_eq, not_1_out, not_2_out, or_1_out;
  wire [31:0] alu_1_result, alu_2_result, Count_q, Current_Number_2_q, multiplexer_1_out, multiplexer_2_out,
       Sum_2_q;

  Counter #(.width(32), .max('hffffffff), .trigger("falling")) Count (
    .Q(Count_q), .clk(clock_1_out), .clr(in_3));  // open: load, D, count, carry
  // Probe on Difference_Value
  Comparator #(.width(32)) comparator_1 (.a(Count_q), .b(32'h1), .eq(comparator_1_eq));  // open: gt, lt
  Comparator #(.width(32)) comparator_2 (.a(Count_q), .b({32{1'b0}}), .eq(comparator_2_eq));  // open: gt, lt
  Multiplexer #(.width(32), .enable("false")) multiplexer_1 (
    .in0({32{1'b0}}), .in1(Difference_Value), .out(multiplexer_1_out), .sel(not_1_out));
  not not_1 (not_1_out, or_1_out);
  or or_1 (or_1_out, comparator_1_eq, comparator_2_eq);
  // Probe on multiplexer_1_out
  Multiplexer #(.width(32), .enable("false")) multiplexer_2 (
    .in0(Initial_Value), .in1(alu_1_result), .out(multiplexer_2_out), .sel(not_2_out));
  not not_2 (not_2_out, comparator_2_eq);
  // Probe on Current_Number_2_q
  ALU alu_1 (
    .AluOP(4'b0101), .X(multiplexer_1_out), .Result(alu_1_result), .Y(Current_Number_2_q));  // open: Equal, Signed_Overflow, Result_2, UnSigned_Overflow
  Register #(.width(32)) Current_Number_2 (
    .D(multiplexer_2_out), .Q(Current_Number_2_q), .clk(clock_1_out), .clr(in_3));  // open: en
  Clock clock_1 (.out(clock_1_out));
  // Probe on Sum_2_q
  Hex_Digit_Display hex_digit_display_1 (.value(Sum_2_q[27:24]));  // open: dp
  Hex_Digit_Display hex_digit_display_2 (.value(Sum_2_q[31:28]));  // open: dp
  Hex_Digit_Display hex_digit_display_3 (.value(Sum_2_q[11:8]));  // open: dp
  Hex_Digit_Display hex_digit_display_4 (.value(Sum_2_q[15:12]));  // open: dp
  ALU alu_2 (
    .AluOP(4'b0101), .X(alu_1_result), .Result(alu_2_result), .Y(Sum_2_q));  // open: Equal, Signed_Overflow, Result_2, UnSigned_Overflow
  Register #(.width(32)) Sum_2 (.D(alu_2_result), .Q(Sum_2_q), .clk(clock_1_out), .clr(in_3));  // open: en
  Hex_Digit_Display hex_digit_display_5 (.value(Sum_2_q[19:16]));  // open: dp
  Hex_Digit_Display hex_digit_display_6 (.value(Sum_2_q[23:20]));  // open: dp
  Hex_Digit_Display hex_digit_display_7 (.value(Sum_2_q[3:0]));  // open: dp
  Hex_Digit_Display hex_digit_display_8 (.value(Sum_2_q[7:4]));  // open: dp
endmodule
