// Logisim project cp0.circ as structural Verilog: 1 circuit, main circuit CP0
module CP0 (
  input  ExpSrc0,
  input  clk,
  input  ExpSrc1,
  input  enable,
  input  ExpSrc2,
  input  [31:0] Inst,
  input  [31:0] PCin,
  input  [31:0] Din,
  output ExRegWrite,
  output IsEret,
  output ExpBlock,
  output HasExp,
  output [31:0] PCout,
  output [31:0] Dout
);

  wire and_4_out, and_5_out, and_6_out, and_7_out, BlockSrc0, BlockSrc1, BlockSrc2, counter_1_q, counter_2_q,
       demultiplexer_1_out0, demultiplexer_1_out1, demultiplexer_2_out0, demultiplexer_2_out1,
       demultiplexer_3_out0, demultiplexer_3_out1, demultiplexer_4_out0, demultiplexer_4_out1,
       demultiplexer_4_out2, ExpClick, not_2_out, not_3_out, or_1_out, or_2_out;
  wire [31:0] Cause_q, controlled_buffer_1_out, multiplexer_1_out;
  wire [31:1] Status_q;
  wire [31:3] Block_q;

  Demultiplexer #(.enable("false")) demultiplexer_1 (
    .out0(demultiplexer_1_out0), .out1(demultiplexer_1_out1), .in(ExpSrc0), .sel(BlockSrc0));
  or or_1 (or_1_out, demultiplexer_1_out0, demultiplexer_2_out0, demultiplexer_3_out0);
  Demultiplexer #(.enable("false")) demultiplexer_2 (
    .out0(demultiplexer_2_out0), .out1(demultiplexer_2_out1), .in(ExpSrc1), .sel(BlockSrc1));
  and and_1 (ExpClick, or_1_out, ~ExpBlock);  // AND_Gate
  Demultiplexer #(.enable("false")) demultiplexer_3 (
    .out0(demultiplexer_3_out0), .out1(demultiplexer_3_out1), .in(ExpSrc2), .sel(BlockSrc2));
  not not_1 (ExRegWrite, Inst[23]);
  and and_2 (IsEret, ~Inst[5], Inst[4], Inst[3], ~Inst[2], ~Inst[1], ~Inst[0]);  // AND_Gate
  Counter #(.width(1), .max('h1), .ongoal("stay")) counter_1 (
    .Q(counter_1_q), .clk(ExpClick), .clr(counter_2_q));  // open: load, D, count, carry
  and and_3 (HasExp, clk, counter_1_q);
  Counter #(.width(1), .max('h1), .ongoal("stay"), .trigger("falling")) counter_2 (
    .Q(counter_2_q), .clk(HasExp), .clr(not_2_out));  // open: load, D, count, carry
  not not_2 (not_2_out, counter_1_q);
  not not_3 (not_3_out, HasExp);
  Multiplexer #(.width(32), .enable("false")) multiplexer_1 (
    .in0(PCin), .in1(Din), .out(multiplexer_1_out), .sel(not_3_out));
  and and_4 (and_4_out, enable, ~ExRegWrite);  // AND_Gate
  Demultiplexer #(.select(2), .disabled(0), .enable("false")) demultiplexer_4 (
    .out0(demultiplexer_4_out0), .out1(demultiplexer_4_out1), .out2(demultiplexer_4_out2), .in(1'b1),
    .sel(Inst[12:11]));  // open: out3
  assign controlled_buffer_1_out = ExpSrc0 ? 32'h1 : 32'bz;  // Controlled_Buffer controlled_buffer_1
  assign controlled_buffer_1_out = ExpSrc1 ? 32'h3 : 32'bz;  // Controlled_Buffer controlled_buffer_2
  assign controlled_buffer_1_out = ExpSrc2 ? 32'h7 : 32'bz;  // Controlled_Buffer controlled_buffer_3
  and and_5 (and_5_out, demultiplexer_4_out0, and_4_out);
  and and_6 (and_6_out, demultiplexer_4_out1, and_4_out);
  and and_7 (and_7_out, demultiplexer_4_out2, and_4_out);
  or or_2 (or_2_out, HasExp, and_5_out);
  Register #(.width(32), .trigger("low")) EPC (
    .D(multiplexer_1_out), .en(or_2_out), .Q(PCout), .clk(clk));  // open: clr
  Register #(.width(32)) Status (.D(Din), .en(and_6_out), .Q({Status_q, ExpBlock}), .clk(clk));  // open: clr
  Register #(.width(32)) Block (
    .D(Din), .en(and_7_out), .Q({Block_q, BlockSrc2, BlockSrc1, BlockSrc0}), .clk(clk));  // open: clr
  Register #(.width(32)) Cause (.D(controlled_buffer_1_out), .Q(Cause_q), .clk(ExpClick));  // open: en, clr
  Multiplexer #(.select(2), .width(32), .enable("false")) multiplexer_2 (
    .in0(PCout), .in1({Status_q, ExpBlock}), .in2({Block_q, BlockSrc2, BlockSrc1, BlockSrc0}), .in3(Cause_q),
    .out(Dout), .sel(Inst[12:11]));
  // also tied to GND on the sheet: {demultiplexer_1_out1, demultiplexer_2_out1, demultiplexer_3_out1}

  // Other names for the same wires on the sheet: Sel[1:0] = Inst[12:11]

  // Notes on the sheet:
  //   Signal Decoding
  //   Exception Signals
  //   Input & Output
  //   Registers
endmodule
