// Logisim project immediate_extender.circ as structural Verilog: 1 circuit, main circuit Immediate Extender
module Immediate_Extender (
  input  ZeroExtend,
  input  [15:0] Input,
  output [31:0] Output
);

  wire [31:0] bit_extender_1_out, bit_extender_2_out;

  assign bit_extender_1_out = {{16{Input[15]}}, Input};  // Bit_Extender bit_extender_1
  assign bit_extender_2_out = {{16{1'b0}}, Input};  // Bit_Extender bit_extender_2
  Multiplexer #(.width(32), .enable("false")) multiplexer_1 (
    .in0(bit_extender_1_out), .in1(bit_extender_2_out), .out(Output), .sel(ZeroExtend));
endmodule
