// Logisim project syscall_decoder.circ as structural Verilog: 1 circuit, main circuit syscall_decoder
module syscall_decoder (
  input  clk,
  input  Enable,
  input  [31:0] a0,
  input  [31:0] v0,
  output [31:0] Hex,
  output Halt
);

  wire comparator_1_eq;

  Comparator #(.width(32)) comparator_1 (.a(v0), .b(32'ha), .eq(comparator_1_eq));  // open: gt, lt
  Register #(.width(32)) register_1 (.D(a0), .en(Enable), .Q(Hex), .clk(clk));  // open: clr
  Multiplexer #(.enable("false")) multiplexer_1 (.in0(1'b0), .in1(comparator_1_eq), .out(Halt), .sel(Enable));
  D_Flip_Flop d_ff_1 (.clk(clk));  // open: D, Q, Qn, preset, en, reset
endmodule
