// Logisim project pipeline_cpu.circ as structural Verilog: 4 circuits, main circuit main
module main (
);

  wire alu_1_equal, and_1_out, BranchSuccess, clk, clock_1_out, control_1_alusrc, control_1_bneorbeq,
       control_1_branch, control_1_isjal, control_1_isjr, control_1_isshamt, control_1_issyscall,
       control_1_jump, control_1_memread, control_1_memtoreg, control_1_memwrite, control_1_regwrite,
       cp0_1_iseret, ex_mem_1_isjalmem, ex_mem_1_issyscallmem, ex_mem_1_memreadmem, ex_mem_1_memwritemem,
       ExpBlock, ExpSrc0, ExpSrc1, ExpSrc2, ExRegWrite, Halt, HasExp, hazard_unit_1_flushid,
       hazard_unit_1_flushif, hazard_unit_1_stallid, hazard_unit_1_stallif, id_ex_1_alusrcex,
       id_ex_1_bneorbeqex, id_ex_1_branchex, id_ex_1_isshamtex, id_ex_1_issyscallex, id_ex_1_memtoregex,
       id_ex_1_memwriteex, IsCOP0, IsCOP0EX, IsCOP0MEM, IsEretEX, IsJALEX, IsJREX, JumpEX,
       mem_wb_1_isexceptionwb, mem_wb_1_isjalwb, mem_wb_1_issyscallwb, mem_wb_1_memtoregwb,
       mem_wb_1_regwritewb, MemReadEX, MemtoRegMEM, multiplexer_7_out, not_1_out, not_2_out, not_3_out,
       not_4_out, or_1_out, or_2_out, ReadRs, ReadRt, RegDstID, regwrite_decider_1_finalregwrite, RegWriteEX,
       RegWriteMEM, statistics_1_i, statistics_1_j, statistics_1_r, xor_1_out, ZeroExtendID;
  wire [1:0] RsOutput, RtOutput;
  wire [3:0] control_1_aluop, id_ex_1_aluopex, syscall_decoder_1_hex_2, syscall_decoder_1_hex_3,
       syscall_decoder_1_hex_4, syscall_decoder_1_hex_5, syscall_decoder_1_hex_6;
  wire [4:0] ex_mem_1_writereg_mem, id_ex_1_writereg_ex, mem_wb_1_writereg_wb, multiplexer_9_out,
       multiplexer_10_out, Rs, Rt;
  wire [5:0] multiplexer_8_out_2;
  wire [8:0] demultiplexer_1_out0, demultiplexer_1_out1;
  wire [11:0] syscall_decoder_1_hex;
  wire [25:0] multiplexer_8_out;
  wire [27:0] if_id_1_pcplus4if;
  wire [31:0] a0, adder_1_out, adder_2_out, alu_1_result, bit_extender_1_out, counter_1_q, counter_2_q,
       counter_3_q, counter_4_q, cp0_1_dout, cp0_1_pcout, Cycle_q, ex_mem_1_aluresultmem, ex_mem_1_cp0dout_2,
       ex_mem_1_jumpaddrmem, ex_mem_1_writedatamem, hazard_unit_1_bubblenum, id_ex_1_cp0dout_2,
       id_ex_1_immex, id_ex_1_jumpaddr_2, id_ex_1_pcplusex, id_ex_1_r1ex, id_ex_1_r2ex, id_ex_1_shamtex,
       immediate_extender_1_output, mem_wb_1_aluresultwb, mem_wb_1_jumpaddrwb, mem_wb_1_jumpaddrwb_2,
       mem_wb_1_readdatawb, multiplexer_1_out, multiplexer_2_out, multiplexer_4_out, multiplexer_5_out,
       multiplexer_6_out, multiplexer_11_out, multiplexer_12_out, multiplexer_13_out, multiplexer_14_out,
       multiplexer_15_out, multiplexer_16_out, multiplexer_17_out, multiplexer_18_out, multiplexer_19_out,
       multiplexer_20_out, multiplexer_21_out, PC_q, ram_1_data, regfile_1_r1, regfile_1_r2, rom_1_data,
       rom_2_data, shifter_1_out, v0;
  wire [31:2] if_id_1_instid_2;
  wire [31:26] if_id_1_instid;

  Multiplexer #(.width(32), .enable("false")) multiplexer_1 (
    .in0(adder_1_out), .in1(adder_2_out), .out(multiplexer_1_out), .sel(BranchSuccess));
  Multiplexer #(.width(32), .enable("false")) multiplexer_2 (
    .in0(multiplexer_1_out), .in1(id_ex_1_jumpaddr_2), .out(multiplexer_2_out), .sel(JumpEX));
  Multiplexer #(.enable("false")) multiplexer_3 (.in0(clock_1_out), .in1(1'b0), .out(clk), .sel(Halt));
  Clock clock_1 (.out(clock_1_out));
  Multiplexer #(.width(32), .enable("false")) multiplexer_4 (
    .in0(multiplexer_2_out), .in1(id_ex_1_r1ex), .out(multiplexer_4_out), .sel(IsJREX));
  Multiplexer #(.width(32), .enable("false")) multiplexer_5 (
    .in0(multiplexer_4_out), .in1(cp0_1_pcout), .out(multiplexer_5_out), .sel(and_1_out));
  and and_1 (and_1_out, IsEretEX, IsCOP0EX);
  Counter #(.width(32), .max('hffffffff)) Cycle (.Q(Cycle_q), .clk(clk));  // open: load, D, count, carry, clr
  Multiplexer #(.width(32), .enable("false")) multiplexer_6 (
    .in0(multiplexer_5_out), .in1(32'h800), .out(multiplexer_6_out), .sel(HasExp));
  or or_1 (or_1_out, HasExp, and_1_out);
  not not_1 (not_1_out, hazard_unit_1_stallif);
  Hazard_Unit hazard_unit_1 (
    .clk(clk), .FlushIF(hazard_unit_1_flushif), .FlushID(hazard_unit_1_flushid), .IsToBranchOrJump(or_2_out),
    .WriteReg_MEM(ex_mem_1_writereg_mem), .RT(Rt), .RegWriteMEM(RegWriteMEM), .RS(Rs),
    .StallIF(hazard_unit_1_stallif), .StallID(hazard_unit_1_stallid), .WriteReg_EX(id_ex_1_writereg_ex),
    .RegWriteEX(RegWriteEX), .ReadRs(ReadRs), .ReadRt(ReadRt), .BubbleNum(hazard_unit_1_bubblenum),
    .RsOutput(RsOutput), .RtOutput(RtOutput), .IsLW(MemReadEX));
  Hex_Digit_Display hex_digit_display_1 (.value(syscall_decoder_1_hex_5));  // open: dp
  Hex_Digit_Display hex_digit_display_2 (.value(syscall_decoder_1_hex_6));  // open: dp
  Counter #(.width(32), .max('hffffffff)) counter_1 (
    .count(statistics_1_j), .Q(counter_1_q), .clk(clk));  // open: load, D, carry, clr
  // Probe on Cycle_q
  Register #(.width(32)) PC (.D(multiplexer_6_out), .en(not_1_out), .Q(PC_q), .clk(multiplexer_7_out));  // open: clr
  Multiplexer #(.enable("false")) multiplexer_7 (.in0(clk), .in1(not_2_out), .out(multiplexer_7_out), .sel(or_1_out));
  not not_2 (not_2_out, clk);
  Hex_Digit_Display hex_digit_display_3 (.value(syscall_decoder_1_hex_4));  // open: dp
  Hex_Digit_Display hex_digit_display_4 (.value(syscall_decoder_1_hex_3));  // open: dp
  Counter #(.width(32), .max('hffffffff)) counter_2 (
    .count(statistics_1_r), .Q(counter_2_q), .clk(clk));  // open: load, D, carry, clr
  // Probe on counter_2_q
  // Probe on counter_1_q
  Demultiplexer #(.width(9), .enable("false")) demultiplexer_1 (
    .out0(demultiplexer_1_out0), .out1(demultiplexer_1_out1), .in(PC_q[10:2]), .sel(PC_q[11]));
  Button button_1 (.out(ExpSrc0));
  // Probe on counter_3_q
  Counter #(.width(32), .max('hffffffff)) counter_3 (
    .count(BranchSuccess), .Q(counter_3_q), .clk(clk));  // open: load, D, carry, clr
  Hex_Digit_Display hex_digit_display_5 (.value(syscall_decoder_1_hex_2));  // open: dp
  Hex_Digit_Display hex_digit_display_6 (.value(syscall_decoder_1_hex[11:8]));  // open: dp
  Counter #(.width(32), .max('hffffffff)) counter_4 (
    .count(statistics_1_i), .Q(counter_4_q), .clk(clk));  // open: load, D, carry, clr
  // Probe on counter_4_q
  Button button_2 (.out(ExpSrc1));
  Hex_Digit_Display hex_digit_display_7 (.value(syscall_decoder_1_hex[3:0]));  // open: dp
  Hex_Digit_Display hex_digit_display_8 (.value(syscall_decoder_1_hex[7:4]));  // open: dp
  Statistics statistics_1 (
    .op0(multiplexer_8_out_2[5]), .op1(multiplexer_8_out_2[4]), .op2(multiplexer_8_out_2[3]),
    .op3(multiplexer_8_out_2[2]), .op4(multiplexer_8_out_2[1]), .op5(multiplexer_8_out_2[0]),
    .i(statistics_1_i), .r(statistics_1_r), .j(statistics_1_j));
  ROM #(.addrWidth(9), .dataWidth(32)) rom_1 (.addr(demultiplexer_1_out0), .data(rom_1_data));  // open: sel
  ROM #(.addrWidth(9), .dataWidth(32)) rom_2 (.addr(demultiplexer_1_out1), .data(rom_2_data));  // open: sel
  Button button_3 (.out(ExpSrc2));
  Adder #(.width(32)) adder_1 (.a(PC_q), .b(32'h4), .out(adder_1_out));  // open: cin, cout
  // Probe on hazard_unit_1_bubblenum
  IF_ID if_id_1 (
    .InstIF({multiplexer_8_out_2, multiplexer_8_out}),
    .InstID({if_id_1_instid, Rs, Rt, if_id_1_instid_2[17:2]}), .clk(clk), .En(not_3_out),
    .clr(hazard_unit_1_flushif), .PCPlus4ID(adder_1_out),
    .PCPlus4IF({if_id_1_instid_2[31:28], if_id_1_pcplus4if}));
  Multiplexer #(.width(32), .enable("false")) multiplexer_8 (
    .in0(rom_1_data), .in1(rom_2_data), .out({multiplexer_8_out_2, multiplexer_8_out}), .sel(PC_q[11]));
  not not_3 (not_3_out, hazard_unit_1_stallid);
  Control control_1 (
    .op(if_id_1_instid), .Funct(if_id_1_instid_2[7:2]), .ALUop(control_1_aluop), .IsJAL(control_1_isjal),
    .IsShamt(control_1_isshamt), .MemtoReg(control_1_memtoreg), .RegWrite(control_1_regwrite),
    .MemRead(control_1_memread), .MemWrite(control_1_memwrite), .Jump(control_1_jump),
    .Branch(control_1_branch), .RegDst(RegDstID), .BneOrBeq(control_1_bneorbeq), .ALUSrc(control_1_alusrc),
    .IsJR(control_1_isjr), .IsSyscall(control_1_issyscall), .IsCOP0(IsCOP0), .ZeroExtend(ZeroExtendID),
    .ReadRs(ReadRs), .ReadRt(ReadRt));
  Immediate_Extender immediate_extender_1 (
    .Input(if_id_1_instid_2[17:2]), .Output(immediate_extender_1_output), .ZeroExtend(ZeroExtendID));
  Multiplexer #(.width(5), .enable("false")) multiplexer_9 (
    .in0(Rt), .in1(if_id_1_instid_2[17:13]), .out(multiplexer_9_out), .sel(RegDstID));
  CP0 cp0_1 (
    .ExpSrc0(ExpSrc0), .clk(clk), .ExpSrc1(ExpSrc1), .enable(IsCOP0), .ExpSrc2(ExpSrc2),
    .Inst({if_id_1_instid, Rs, Rt, if_id_1_instid_2[17:2]}), .PCin(PC_q), .Din(multiplexer_12_out),
    .ExRegWrite(ExRegWrite), .IsEret(cp0_1_iseret), .ExpBlock(ExpBlock), .HasExp(HasExp),
    .PCout(cp0_1_pcout), .Dout(cp0_1_dout));
  Multiplexer #(.width(5), .enable("false")) multiplexer_10 (
    .in0(multiplexer_9_out), .in1({5{1'b1}}), .out(multiplexer_10_out), .sel(control_1_isjal));
  not not_4 (not_4_out, clk);
  Regfile regfile_1 (
    .R1_num(Rs), .R2_num(Rt), .RW(mem_wb_1_writereg_wb), .R1(regfile_1_r1), .R2(regfile_1_r2),
    .Din(multiplexer_21_out), .WE(mem_wb_1_regwritewb), .clk(not_4_out), .v0(v0), .a0(a0));
  assign bit_extender_1_out = {{27{1'b0}}, if_id_1_instid_2[12:8]};  // Bit_Extender bit_extender_1
  RegWrite_Decider regwrite_decider_1 (
    .RegWrite(control_1_regwrite), .ExRegWrite(ExRegWrite), .FinalRegWrite(regwrite_decider_1_finalregwrite),
    .IsException(IsCOP0));
  Multiplexer #(.select(2), .width(32), .enable("false")) multiplexer_11 (
    .in0(regfile_1_r1), .in1(multiplexer_16_out), .in2(multiplexer_18_out), .out(multiplexer_11_out),
    .sel(RsOutput));  // open: in3
  Multiplexer #(.select(2), .width(32), .enable("false")) multiplexer_12 (
    .in0(regfile_1_r2), .in1(multiplexer_16_out), .in2(multiplexer_18_out), .out(multiplexer_12_out),
    .sel(RtOutput));  // open: in3
  ID_EX id_ex_1 (
    .clk(clk), .IsJALID(control_1_isjal), .MemReadID(control_1_memread), .IsShamtID(control_1_isshamt),
    .MemWriteID(control_1_memwrite), .MemtoRegID(control_1_memtoreg), .JumpID(control_1_jump),
    .RegWriteID(regwrite_decider_1_finalregwrite), .BranchID(control_1_branch),
    .BneOrBeqID(control_1_bneorbeq), .ALUSrcID(control_1_alusrc), .IsJRID(control_1_isjr),
    .IsExceptionID(IsCOP0), .IsJALEX(IsJALEX), .MemReadEX(MemReadEX), .IsShamtEX(id_ex_1_isshamtex),
    .MemWriteEX(id_ex_1_memwriteex), .MemtoRegEX(id_ex_1_memtoregex), .JumpEX(JumpEX),
    .RegWriteEX(RegWriteEX), .BranchEX(id_ex_1_branchex), .BneOrBeqEX(id_ex_1_bneorbeqex),
    .ALUSrcEX(id_ex_1_alusrcex), .IsJREX(IsJREX), .IsExceptionEX(IsCOP0EX), .ALUopID(control_1_aluop),
    .ALUopEX(id_ex_1_aluopex), .WriteReg_ID(multiplexer_10_out), .WriteReg_EX(id_ex_1_writereg_ex),
    .ImmID(immediate_extender_1_output), .ImmEX(id_ex_1_immex), .R1ID(multiplexer_11_out),
    .R1EX(id_ex_1_r1ex), .R2ID(multiplexer_12_out), .R2EX(id_ex_1_r2ex),
    .PCPlus4ID({if_id_1_instid_2[31:28], if_id_1_pcplus4if}), .PCPlusEX(id_ex_1_pcplusex),
    .ShamtID(bit_extender_1_out), .ShamtEX(id_ex_1_shamtex),
    .JumpAddr({if_id_1_instid_2[31:28], Rs, Rt, if_id_1_instid_2[17:2], 2'b00}),
    .JumpAddr_2(id_ex_1_jumpaddr_2), .IsSyscallID(control_1_issyscall), .IsSyscallEX(id_ex_1_issyscallex),
    .clr(hazard_unit_1_flushid), .En(1'b1), .CP0Dout(cp0_1_dout), .CP0Dout_2(id_ex_1_cp0dout_2),
    .IsEret(cp0_1_iseret), .IsEret_2(IsEretEX));
  Multiplexer #(.width(32), .enable("false")) multiplexer_13 (
    .in0(id_ex_1_r1ex), .in1(id_ex_1_r2ex), .out(multiplexer_13_out), .sel(id_ex_1_isshamtex));
  Multiplexer #(.width(32), .enable("false")) multiplexer_14 (
    .in0(id_ex_1_r2ex), .in1(id_ex_1_shamtex), .out(multiplexer_14_out), .sel(id_ex_1_isshamtex));
  Adder #(.width(32)) adder_2 (.a(id_ex_1_pcplusex), .b(shifter_1_out), .out(adder_2_out));  // open: cin, cout
  Shifter #(.width(32)) shifter_1 (.in(id_ex_1_immex), .\dist (5'b00010), .out(shifter_1_out));
  ALU alu_1 (
    .AluOP(id_ex_1_aluopex), .X(multiplexer_13_out), .Equal(alu_1_equal), .Result(alu_1_result),
    .Y(multiplexer_15_out));  // open: Signed_Overflow, Result_2, UnSigned_Overflow
  Multiplexer #(.width(32), .enable("false")) multiplexer_15 (
    .in0(multiplexer_14_out), .in1(id_ex_1_immex), .out(multiplexer_15_out), .sel(id_ex_1_alusrcex));
  or or_2 (or_2_out, JumpEX, IsEretEX, BranchSuccess, IsJREX, IsJALEX);
  and and_2 (BranchSuccess, id_ex_1_branchex, xor_1_out);
  xor xor_1 (xor_1_out, id_ex_1_bneorbeqex, alu_1_equal);
  Multiplexer #(.width(32), .enable("false")) multiplexer_16 (
    .in0(alu_1_result), .in1(id_ex_1_cp0dout_2), .out(multiplexer_16_out), .sel(IsCOP0EX));
  EX_MEM ex_mem_1 (
    .MemReadEX(MemReadEX), .MemReadMEM(ex_mem_1_memreadmem), .MemWriteEX(id_ex_1_memwriteex),
    .MemWriteMEM(ex_mem_1_memwritemem), .IsExceptionEX(IsCOP0EX), .IsExceptionMEM(IsCOP0MEM),
    .IsJALEX(IsJALEX), .IsJALMEM(ex_mem_1_isjalmem), .RegWriteEX(RegWriteEX), .RegWriteMEM(RegWriteMEM),
    .MemtoRegEX(id_ex_1_memtoregex), .MemtoRegMEM(MemtoRegMEM), .clk(clk), .IsSyscallEX(id_ex_1_issyscallex),
    .IsSyscallMEM(ex_mem_1_issyscallmem), .ALUResultEX(alu_1_result), .ALUResultMEM(ex_mem_1_aluresultmem),
    .WriteDataEX(id_ex_1_r2ex), .WriteDataMEM(ex_mem_1_writedatamem), .JumpAddrEX(id_ex_1_pcplusex),
    .JumpAddrMEM(ex_mem_1_jumpaddrmem), .WriteReg_EX(id_ex_1_writereg_ex),
    .WriteReg_MEM(ex_mem_1_writereg_mem), .clr(1'b0), .En(1'b1), .CP0Dout(id_ex_1_cp0dout_2),
    .CP0Dout_2(ex_mem_1_cp0dout_2));
  Multiplexer #(.width(32), .enable("false")) multiplexer_17 (
    .in0(ex_mem_1_aluresultmem), .in1(ram_1_data), .out(multiplexer_17_out), .sel(MemtoRegMEM));
  Multiplexer #(.width(32), .enable("false")) multiplexer_18 (
    .in0(multiplexer_17_out), .in1(ex_mem_1_cp0dout_2), .out(multiplexer_18_out), .sel(IsCOP0MEM));
  RAM #(.addrWidth(10), .dataWidth(32), .bus("separate")) ram_1 (
    .addr(ex_mem_1_aluresultmem[11:2]), .din(ex_mem_1_writedatamem), .data(ram_1_data),
    .str(ex_mem_1_memwritemem), .clk(clk), .ld(ex_mem_1_memreadmem));  // open: sel, clr
  MEM_WB mem_wb_1 (
    .IsJALMEM(ex_mem_1_isjalmem), .clk(clk), .MemtoRegMEM(MemtoRegMEM), .RegWriteMEM(RegWriteMEM),
    .IsExceptionMEM(IsCOP0MEM), .IsJALWB(mem_wb_1_isjalwb), .MemtoRegWB(mem_wb_1_memtoregwb),
    .RegWriteWB(mem_wb_1_regwritewb), .IsExceptionWB(mem_wb_1_isexceptionwb),
    .ALUResultMEM(ex_mem_1_aluresultmem), .ALUResultWB(mem_wb_1_aluresultwb), .JumpAddrMEM(ram_1_data),
    .JumpAddrWB(mem_wb_1_jumpaddrwb), .ReadDataMEM(ex_mem_1_jumpaddrmem), .ReadDataWB(mem_wb_1_readdatawb),
    .WriteReg_MEM(ex_mem_1_writereg_mem), .WriteReg_WB(mem_wb_1_writereg_wb),
    .IsSyscallMEM(ex_mem_1_issyscallmem), .IsSyscallWB(mem_wb_1_issyscallwb), .clr(1'b0), .En(1'b1),
    .JumpAddrMEM_2(ex_mem_1_cp0dout_2), .JumpAddrWB_2(mem_wb_1_jumpaddrwb_2));
  Syscall_Decoder syscall_decoder_1 (
    .v0(v0), .a0(a0), .Enable(mem_wb_1_issyscallwb),
    .Hex({syscall_decoder_1_hex_6, syscall_decoder_1_hex_5, syscall_decoder_1_hex_4, syscall_decoder_1_hex_3, syscall_decoder_1_hex_2, syscall_decoder_1_hex}),
    .Halt(Halt), .clk(clk));
  Multiplexer #(.width(32), .enable("false")) multiplexer_19 (
    .in0(mem_wb_1_aluresultwb), .in1(mem_wb_1_jumpaddrwb_2), .out(multiplexer_19_out),
    .sel(mem_wb_1_isexceptionwb));
  Multiplexer #(.width(32), .enable("false")) multiplexer_20 (
    .in0(multiplexer_19_out), .in1(mem_wb_1_jumpaddrwb), .out(multiplexer_20_out), .sel(mem_wb_1_memtoregwb));
  Multiplexer #(.width(32), .enable("false")) multiplexer_21 (
    .in0(multiplexer_20_out), .in1(mem_wb_1_readdatawb), .out(multiplexer_21_out), .sel(mem_wb_1_isjalwb));

  // Notes on the sheet:
  //   Screen
  //   contents of rom_1 (hex, n*v repeats v):
  //   20110001 8000c05 20110001 20120002 20130003 8000c09 20110001 20120002 20130003 8000c0d 20110001
  //   20120002 20130003 8000c11 20110001 20120002 20130003 c000d2e 20100001 20110001 118fc0 112020
  //   20020022 c 118882 12200001 8000c15 112020 20020022 c 20110001 118880 112020 20020022 c 12200001
  //   8000c1f 20110001 118fc0 112020 20020022 c 1188c3 112020 20020022 c 118903 112020 20020022 c 118903
  //   112020 20020022 c 118903 112020 20020022 c 118903 112020 20020022 c 118903 112020 20020022 c 118903
  //   112020 20020022 c 118903 112020 20020022 c 20100001 109fc0 139fc3 8021 2012000c 24160003 26100001
  //   3210000f 20080008 20090001 139900 2709825 132020 20020022 c 1094022 1500fff9 22100001 2018000f
  //   2188024 108700 20080008 20090001 139902 2709825 132021 20020022 c 1094022 1500fff9 108702 2c9b022
  //   12c00001 8000c50 4020 1084027 84400 3508ffff 82021 20020022 c 20110004 ae310000 8e320000 2252fffc
  //   20100000 22110001 2118020 22520004 ae500000 22310001 2118020 22520004 ae500000 22310001 2118020
  //   22520004 ae500000 22310001 2118020 22520004 ae500000 22310001 2118020 22520004 ae500000 22310001
  //   2118020 22520004 ae500000 22310001 2118020 22520004 ae500000 20090001 8c080004 1509008f ac000004
  //   20090003 8c080008 1509008b ac000008 20090006 8c08000c 15090087 ac00000c 2009000a 8c080010 15090083
  //   ac000010 2009000f 8c080014 1509007f ac000014 20090015 8c080018 1509007b ac000018 2009001c 8c08001c
  //   15090077 ac00001c 2010ffff 20110000 ae300000 22100001 22310004 ae300000 22100001 22310004 ae300000
  //   22100001 22310004 ae300000 22100001 22310004 ae300000 22100001 22310004 ae300000 22100001 22310004
  //   ae300000 22100001 22310004 ae300000 22100001 22310004 ae300000 22100001 22310004 ae300000 22100001
  //   22310004 ae300000 22100001 22310004 ae300000 22100001 22310004 ae300000 22100001 22310004 ae300000
  //   22100001 22310004 ae300000 22100001 22310004 ae300000 22100001 22310004 22100001 8020 2011003c
  //   8e130000 8e340000 274402a 11000002 ae330000 ae140000 2231fffc 1611fff8 102020 20020022 c 22100004
  //   2011003c 1611fff2 20100001 201200ff 20110001 20130003 12120005 12100004 20110001 20120002 20130003
  //   8000d26 102020 20020001 c 16310005 16320004 20110001 20120002 20130003 8000d26 132020 20020001 c
  //   2011ffff 118c00 2020 24840064 2484ff9c 14800017 2020 2484ff9c 24840064 14800013 2020 34847fff 912024
  //   1480000f 2020 34848000 912024 1480000b 24040000 8000d20 8000d26 2002000a c 20041ced 42400 3484cafe
  //   20020022 c 8000d1e 3c010000 3421baad 12020 42400 3484c0de 20020022 c 8000d1e 20100000 22100001
  //   102020 20020022 c 22100002 102020 20020022 c 22100003 102020 20020022 c 22100004 102020 20020022 c
  //   22100005 102020 20020022 c 22100006 102020 20020022 c 22100007 102020 20020022 c 22100008 102020
  //   20020022 c 3e00008
  //   contents of rom_2 (hex, n*v repeats v):
  //   201a0001 409a0800 201c0400 39df020 401a0000 afda0000 23de0004 23bd0004 401b1000 401a1800 409a1000
  //   afd00000 23bd0004 23de0004 afd40000 23bd0004 23de0004 afd50000 23bd0004 23de0004 afd60000 23bd0004
  //   23de0004 afc40000 23bd0004 23de0004 afc20000 23bd0004 23de0004 afdb0000 23bd0004 23de0004 1ab020
  //   22d60001 201a0000 409a0800 20140005 20150001 168020 102020 20020022 c 108100 1600fffb 295a022
  //   1680fff8 201a0001 409a0800 23defffc 23bdfffc 8fdb0000 23defffc 23bdfffc 8fc20000 23defffc 23bdfffc
  //   8fc40000 23defffc 23bdfffc 8fd60000 23defffc 23bdfffc 8fd50000 23defffc 23bdfffc 8fd40000 23defffc
  //   23bdfffc 8fd00000 409b1000 23defffc 23bdfffc 8fda0000 409a0000 201a0000 409a0800 42000018
  //   PCPlus4IF
  //   OP
  //   Funct
  //   RS
  //   RT
  //   RD
  //   JR Addr
  //   Jump Addr
  //   Branch Addr
  //   Shamt
  //   WriteReg#
  //   JumpAddr
  //   Immediate
  //   PCPlus4ID
  //   IsEret
  //   ALU Result
  //   Memory Result
  //   IsToBranchOrJump
  //   WriteDataEX
  //   WriteReg#MEM
  //   WriteReg#WB
  //   WB_DATA
endmodule

module Hazard_Unit (
  input  clk,
  input  ReadRs,
  input  RegWriteMEM,
  input  IsToBranchOrJump,
  input  ReadRt,
  input  [4:0] RS,
  input  RegWriteEX,
  input  [4:0] WriteReg_MEM,
  input  [4:0] WriteReg_EX,
  input  [4:0] RT,
  input  IsLW,
  output FlushIF,
  output [1:0] RsOutput,
  output FlushID,
  output StallIF,
  output StallID,
  output [31:0] BubbleNum,
  output [1:0] RtOutput
);

  wire d_ff_1_q, d_ff_2_q, hazard_detector_1_hazard, hazard_detector_2_hazard, hazard_detector_3_hazard,
       hazard_detector_4_hazard, or_1_out;
  wire [1:0] multiplexer_1_out, multiplexer_2_out;

  Hazard_Detector hazard_detector_1 (
    .Read(ReadRs), .RegWrite(RegWriteMEM), .WriteReg(WriteReg_MEM), .Register_num(RS),
    .Hazard(hazard_detector_1_hazard));
  Hazard_Detector hazard_detector_2 (
    .Read(ReadRs), .RegWrite(RegWriteEX), .WriteReg(WriteReg_EX), .Register_num(RS),
    .Hazard(hazard_detector_2_hazard));
  Hazard_Detector hazard_detector_3 (
    .Read(ReadRt), .RegWrite(RegWriteMEM), .WriteReg(WriteReg_MEM), .Register_num(RT),
    .Hazard(hazard_detector_3_hazard));
  Hazard_Detector hazard_detector_4 (
    .Read(ReadRt), .RegWrite(RegWriteEX), .WriteReg(WriteReg_EX), .Register_num(RT),
    .Hazard(hazard_detector_4_hazard));
  Multiplexer #(.width(2), .enable("false")) multiplexer_1 (
    .in0(2'b00), .in1(2'b10), .out(multiplexer_1_out), .sel(hazard_detector_1_hazard));
  Multiplexer #(.width(2), .enable("false")) multiplexer_2 (
    .in0(2'b00), .in1(2'b10), .out(multiplexer_2_out), .sel(hazard_detector_3_hazard));
  Multiplexer #(.width(2), .enable("false")) multiplexer_3 (
    .in0(multiplexer_1_out), .in1(2'b01), .out(RsOutput), .sel(hazard_detector_2_hazard));
  Multiplexer #(.width(2), .enable("false")) multiplexer_4 (
    .in0(multiplexer_2_out), .in1(2'b01), .out(RtOutput), .sel(hazard_detector_4_hazard));
  or or_1 (or_1_out, hazard_detector_2_hazard, hazard_detector_4_hazard);
  and and_1 (StallID, IsLW, or_1_out);
  D_Flip_Flop #(.trigger("falling")) d_ff_1 (
    .clk(clk), .D(IsToBranchOrJump), .Q(d_ff_1_q));  // open: Qn, preset, en, reset
  D_Flip_Flop #(.trigger("falling")) d_ff_2 (.clk(clk), .D(StallID), .Q(d_ff_2_q));  // open: Qn, preset, en, reset
  Counter #(.width(32), .max('hffffffff)) counter_1 (
    .count(StallID), .Q(BubbleNum), .clk(clk));  // open: load, D, carry, clr
  and and_2 (FlushIF, ~clk, d_ff_1_q);  // AND_Gate
  and and_3 (FlushID, clk, d_ff_2_q);

  assign StallIF = StallID;

  // Other names for the same wires on the sheet: ReadWriteEX = RegWriteEX; ReadWriteMEM = RegWriteMEM

  // Notes on the sheet:
  //   Rs Hazard in MEM
  //   Rs Hazard in EX
  //   Rt Hazard in MEM
  //   Rt Hazard in EX
  //   hasHazard
endmodule

module Hazard_Detector (
  input  Read,
  input  RegWrite,
  input  [4:0] WriteReg,
  input  [4:0] Register_num,
  output Hazard
);

  wire comparator_1_eq, comparator_2_eq, not_1_out;

  Comparator #(.width(5)) comparator_1 (.a({5{1'b0}}), .b(WriteReg), .eq(comparator_1_eq));  // open: gt, lt
  not not_1 (not_1_out, comparator_1_eq);
  Comparator #(.width(5)) comparator_2 (.a(WriteReg), .b(Register_num), .eq(comparator_2_eq));  // open: gt, lt
  and and_1 (Hazard, Read, RegWrite, not_1_out, comparator_2_eq);
endmodule

module RegWrite_Decider (
  input  RegWrite,
  input  ExRegWrite,
  input  IsException,
  output FinalRegWrite
);

  Multiplexer #(.enable("false")) multiplexer_1 (
    .in0(RegWrite), .in1(ExRegWrite), .out(FinalRegWrite), .sel(IsException));
endmodule
