// Logisim project single_cycle_cpu.circ as structural Verilog: 8 circuits, main circuit main
module main (
);

  wire ALUSrc, and_1_out, and_2_out, BneOrBeq, Branch, clk, clock_1_out, Equal, ExpBlock, ExpSrc0, ExpSrc1,
       ExpSrc2, ExRegWrite, Halt, HasExp, IsCOP0, IsEret, IsJAL, IsJR, IsShamt, IsSyscall, Jump, MemRead,
       MemtoReg, MemWrite, multiplexer_4_out, multiplexer_11_out, not_1_out, not_2_out, not_3_out, not_4_out,
       not_5_out, not_6_out, not_7_out, or_1_out, RegDst, RegWrite, statistics_1_i, statistics_1_j,
       statistics_1_r, xor_1_out, ZeroExtend;
  wire [3:0] ALUop, syscall_decoder_1_hex0, syscall_decoder_1_hex1, syscall_decoder_1_hex2,
       syscall_decoder_1_hex3, syscall_decoder_1_hex4, syscall_decoder_1_hex5, syscall_decoder_1_hex6,
       syscall_decoder_1_hex7;
  wire [4:0] multiplexer_6_out, multiplexer_7_out, multiplexer_8_out, multiplexer_9_out;
  wire [5:0] multiplexer_5_out;
  wire [8:0] demultiplexer_1_out0, demultiplexer_1_out1;
  wire [25:0] multiplexer_5_out_2;
  wire [31:0] adder_1_out, adder_2_out, adder_3_out, alu_1_result, bit_extender_1_out, bit_extender_2_out,
       bit_extender_3_out, counter_1_q, counter_2_q, counter_3_q, cp0_1_dout, cp0_1_pcout, Cycle_q,
       main_1_reg1, main_1_reg2_2, multiplexer_1_out, multiplexer_2_out, multiplexer_10_out,
       multiplexer_12_out, multiplexer_13_out, multiplexer_14_out, multiplexer_15_out, multiplexer_16_out,
       multiplexer_17_out, multiplexer_18_out, multiplexer_19_out, multiplexer_20_out, PC_Buffer_q, PC_q,
       ram_1_data, rom_1_data, rom_2_data, shifter_1_out;

  and and_1 (and_1_out, IsEret, IsCOP0);
  Clock clock_1 (.out(clock_1_out));
  Multiplexer #(.width(32), .enable("false")) multiplexer_1 (
    .in0(32'h800), .in1(multiplexer_2_out), .out(multiplexer_1_out), .sel(not_1_out));
  Multiplexer #(.width(32), .enable("false")) multiplexer_2 (
    .in0(multiplexer_20_out), .in1(cp0_1_pcout), .out(multiplexer_2_out), .sel(and_1_out));
  not not_1 (not_1_out, HasExp);
  Multiplexer #(.enable("false")) multiplexer_3 (.in0(clock_1_out), .in1(1'b1), .out(clk), .sel(Halt));
  Counter #(.width(32), .max('hffffffff)) Cycle (.Q(Cycle_q), .clk(clk));  // open: load, D, count, carry, clr
  // Probe on Cycle_q
  Register #(.width(32)) PC (.D(multiplexer_1_out), .Q(PC_q), .clk(multiplexer_4_out));  // open: en, clr
  Multiplexer #(.enable("false")) multiplexer_4 (.in0(clk), .in1(not_2_out), .out(multiplexer_4_out), .sel(or_1_out));
  or or_1 (or_1_out, HasExp, and_1_out);
  not not_2 (not_2_out, clk);
  Demultiplexer #(.width(9), .enable("false")) demultiplexer_1 (
    .out0(demultiplexer_1_out0), .out1(demultiplexer_1_out1), .in(PC_q[10:2]), .sel(PC_q[11]));
  Adder #(.width(32)) adder_1 (.a(32'h4), .b(PC_q), .out(adder_1_out));  // open: cin, cout
  Counter #(.width(32), .max('hffffffff)) counter_1 (
    .count(statistics_1_j), .Q(counter_1_q), .clk(clk));  // open: load, D, carry, clr
  // Probe on counter_1_q
  Counter #(.width(32), .max('hffffffff)) counter_2 (
    .count(statistics_1_i), .Q(counter_2_q), .clk(clk));  // open: load, D, carry, clr
  Counter #(.width(32), .max('hffffffff)) counter_3 (
    .count(statistics_1_r), .Q(counter_3_q), .clk(clk));  // open: load, D, carry, clr
  // Probe on counter_3_q
  Register #(.width(32)) PC_Buffer (.D(PC_q), .Q(PC_Buffer_q), .clk(HasExp));  // open: en, clr
  Adder #(.width(32)) adder_2 (.a(PC_q), .b(32'h4), .out(adder_2_out));  // open: cin, cout
  Statistics statistics_1 (
    .op0(multiplexer_5_out[5]), .op1(multiplexer_5_out[4]), .op2(multiplexer_5_out[3]),
    .op3(multiplexer_5_out[2]), .op4(multiplexer_5_out[1]), .op5(multiplexer_5_out[0]), .i(statistics_1_i),
    .r(statistics_1_r), .j(statistics_1_j));
  // Probe on counter_2_q
  ROM #(.addrWidth(9), .dataWidth(32)) rom_1 (.addr(demultiplexer_1_out0), .data(rom_1_data));  // open: sel
  ROM #(.addrWidth(9), .dataWidth(32)) rom_2 (.addr(demultiplexer_1_out1), .data(rom_2_data));  // open: sel
  Control control_1 (
    .op(multiplexer_5_out), .Funct(multiplexer_5_out_2[5:0]), .ALUop(ALUop), .IsJAL(IsJAL),
    .IsShamt(IsShamt), .MemtoReg(MemtoReg), .RegWrite(RegWrite), .MemRead(MemRead), .MemWrite(MemWrite),
    .Jump(Jump), .Branch(Branch), .RegDst(RegDst), .BneOrBeq(BneOrBeq), .ALUSrc(ALUSrc), .IsJR(IsJR),
    .IsSyscall(IsSyscall), .IsCOP0(IsCOP0), .ZeroExtend(ZeroExtend));
  Multiplexer #(.width(32), .enable("false")) multiplexer_5 (
    .in0(rom_1_data), .in1(rom_2_data), .out({multiplexer_5_out, multiplexer_5_out_2}), .sel(PC_q[11]));
  Multiplexer #(.width(5), .enable("false")) multiplexer_6 (
    .in0(multiplexer_5_out_2[20:16]), .in1(multiplexer_5_out_2[15:11]), .out(multiplexer_6_out), .sel(RegDst));
  CP0 cp0_1 (
    .PCin(PC_Buffer_q), .Din(main_1_reg2_2), .Dout(cp0_1_dout), .ExRegWrite(ExRegWrite), .ExpSrc0(ExpSrc0),
    .IsEret(IsEret), .PCout(cp0_1_pcout), .Inst({multiplexer_5_out, multiplexer_5_out_2}), .clk(clk),
    .enable(IsCOP0), .ExpBlock(ExpBlock), .HasExp(HasExp), .ExpSrc1(ExpSrc1), .ExpSrc2(ExpSrc2));
  not not_3 (not_3_out, IsSyscall);
  Multiplexer #(.width(5), .enable("false")) multiplexer_7 (
    .in0(5'b00010), .in1(multiplexer_5_out_2[25:21]), .out(multiplexer_7_out), .sel(not_3_out));
  Multiplexer #(.width(5), .enable("false")) multiplexer_8 (
    .in0(multiplexer_6_out), .in1({5{1'b1}}), .out(multiplexer_8_out), .sel(IsJAL));
  Multiplexer #(.width(5), .enable("false")) multiplexer_9 (
    .in0(5'b00100), .in1(multiplexer_5_out_2[20:16]), .out(multiplexer_9_out), .sel(not_4_out));
  not not_4 (not_4_out, IsSyscall);
  assign bit_extender_1_out = {{16{multiplexer_5_out_2[15]}}, multiplexer_5_out_2[15:0]};  // Bit_Extender bit_extender_1
  Multiplexer #(.width(32), .enable("false")) multiplexer_10 (
    .in0(bit_extender_1_out), .in1(bit_extender_2_out), .out(multiplexer_10_out), .sel(ZeroExtend));
  assign bit_extender_2_out = {{16{1'b0}}, multiplexer_5_out_2[15:0]};  // Bit_Extender bit_extender_2
  not not_5 (not_5_out, IsJAL);
  regfile_main main_1 (
    .Reg1_num(multiplexer_7_out), .Reg2(multiplexer_9_out), .Write_Reg_num(multiplexer_8_out),
    .Din(multiplexer_12_out), .Write_Enable(multiplexer_11_out), .Clock(clk), .Reg1(main_1_reg1),
    .Reg2_2(main_1_reg2_2));  // open: s0_Value, s1_Value, s2_Value, ra_Value
  Multiplexer #(.enable("false")) multiplexer_11 (
    .in0(RegWrite), .in1(ExRegWrite), .out(multiplexer_11_out), .sel(IsCOP0));
  Multiplexer #(.width(32), .enable("false")) multiplexer_12 (
    .in0(cp0_1_dout), .in1(multiplexer_13_out), .out(multiplexer_12_out), .sel(not_6_out));
  not not_6 (not_6_out, IsCOP0);
  Multiplexer #(.width(32), .enable("false")) multiplexer_13 (
    .in0(adder_2_out), .in1(multiplexer_19_out), .out(multiplexer_13_out), .sel(not_5_out));
  Syscall_Decoder syscall_decoder_1 (
    .v0(main_1_reg1), .a0(main_1_reg2_2), .Enable(IsSyscall), .Hex0(syscall_decoder_1_hex0),
    .Hex1(syscall_decoder_1_hex1), .Hex2(syscall_decoder_1_hex2), .Hex3(syscall_decoder_1_hex3), .Halt(Halt),
    .Hex4(syscall_decoder_1_hex4), .Hex5(syscall_decoder_1_hex5), .Hex6(syscall_decoder_1_hex6),
    .Hex7(syscall_decoder_1_hex7), .clk(clk));
  assign bit_extender_3_out = {{27{1'b0}}, multiplexer_5_out_2[10:6]};  // Bit_Extender bit_extender_3
  Shifter #(.width(32)) shifter_1 (.in(multiplexer_10_out), .\dist (5'b00010), .out(shifter_1_out));
  xor xor_1 (xor_1_out, Equal, BneOrBeq);
  Hex_Digit_Display hex_digit_display_1 (.value(syscall_decoder_1_hex0));  // open: dp
  Multiplexer #(.width(32), .enable("false")) multiplexer_14 (
    .in0(main_1_reg1), .in1(main_1_reg2_2), .out(multiplexer_14_out), .sel(IsShamt));
  Multiplexer #(.width(32), .enable("false")) multiplexer_15 (
    .in0(main_1_reg2_2), .in1(multiplexer_10_out), .out(multiplexer_15_out), .sel(ALUSrc));
  Multiplexer #(.width(32), .enable("false")) multiplexer_16 (
    .in0(multiplexer_15_out), .in1(bit_extender_3_out), .out(multiplexer_16_out), .sel(IsShamt));
  Hex_Digit_Display hex_digit_display_2 (.value(syscall_decoder_1_hex2));  // open: dp
  Hex_Digit_Display hex_digit_display_3 (.value(syscall_decoder_1_hex1));  // open: dp
  ALU alu_1 (
    .AluOP(ALUop), .X(multiplexer_14_out), .Equal(Equal), .Result(alu_1_result), .Y(multiplexer_16_out));  // open: Signed_Overflow, Result_2, UnSigned_Overflow
  Button button_1 (.out(ExpSrc0));
  Adder #(.width(32)) adder_3 (.a(adder_1_out), .b(shifter_1_out), .out(adder_3_out));  // open: cin, cout
  and and_2 (and_2_out, Branch, xor_1_out);
  Hex_Digit_Display hex_digit_display_4 (.value(syscall_decoder_1_hex4));  // open: dp
  Hex_Digit_Display hex_digit_display_5 (.value(syscall_decoder_1_hex3));  // open: dp
  Button button_2 (.out(ExpSrc2));
  Button button_3 (.out(ExpSrc1));
  Multiplexer #(.width(32), .enable("false")) multiplexer_17 (
    .in0(adder_1_out), .in1(adder_3_out), .out(multiplexer_17_out), .sel(and_2_out));
  Hex_Digit_Display hex_digit_display_6 (.value(syscall_decoder_1_hex5));  // open: dp
  Hex_Digit_Display hex_digit_display_7 (.value(syscall_decoder_1_hex6));  // open: dp
  Multiplexer #(.width(32), .enable("false")) multiplexer_18 (
    .in0({adder_1_out[31:28], multiplexer_5_out_2, 2'b00}), .in1(multiplexer_17_out),
    .out(multiplexer_18_out), .sel(not_7_out));
  not not_7 (not_7_out, Jump);
  Hex_Digit_Display hex_digit_display_8 (.value(syscall_decoder_1_hex7));  // open: dp
  RAM #(.addrWidth(10), .dataWidth(32), .bus("separate")) ram_1 (
    .addr(alu_1_result[11:2]), .din(main_1_reg2_2), .data(ram_1_data), .str(MemWrite), .clk(clk), .ld(MemRead));  // open: sel, clr
  Multiplexer #(.width(32), .enable("false")) multiplexer_19 (
    .in0(alu_1_result), .in1(ram_1_data), .out(multiplexer_19_out), .sel(MemtoReg));
  Multiplexer #(.width(32), .enable("false")) multiplexer_20 (
    .in0(multiplexer_18_out), .in1(main_1_reg1), .out(multiplexer_20_out), .sel(IsJR));

  // Notes on the sheet:
  //   contents of rom_1 (hex, n*v repeats v):
  //   20110001 8000c05 20110001 20120002 20130003 8000c09 20110001 20120002 20130003 8000c0d 20110001
  //   20120002 20130003 8000c11 20110001 20120002 20130003 c000d2e 20100001 20110001 118fc0 112020
  //   20020022 c 118882 12200001 8000c15 112020 20020022 c 20110001 118880 112020 20020022 c 12200001
  //   8000c1f 20110001 118fc0 112020 20020022 c 1188c3 112020 20020022 c 118903 112020 20020022 c 118903
  //   112020 20020022 c 118903 112020 20020022 c 118903 112020 20020022 c 118903 112020 20020022 c 118903
  //   112020 20020022 c 118903 112020 20020022 c 20100001 109fc0 139fc3 8021 2012000c 24160003 26100001
  //   3210000f 20080008 20090001 139900 2709825 132020 20020022 c 1094022 1500fff9 22100001 2018000f
  //   2188024 108700 20080008 20090001 139902 2709825 132021 20020022 c 1094022 1500fff9 108702 2c9b022
  //   12c00001 8000c50 4020 1084027 84400 3508ffff 82021 20020022 c 20110004 ae310000 8e320000 2252fffc
  //   20100000 22110001 2118020 22520004 ae500000 22310001 2118020 22520004 ae500000 22310001 2118020
  //   22520004 ae500000 22310001 2118020 22520004 ae500000 22310001 2118020 22520004 ae500000 22310001
  //   2118020 22520004 ae500000 22310001 2118020 22520004 ae500000 20090001 8c080004 1509008f ac000004
  //   20090003 8c080008 1509008b ac000008 20090006 8c08000c 15090087 ac00000c 2009000a 8c080010 15090083
  //   ac000010 2009000f 8c080014 1509007f ac000014 20090015 8c080018 1509007b ac000018 2009001c 8c08001c
  //   15090077 ac00001c 2010ffff 20110000 ae300000 22100001 22310004 ae300000 22100001 22310004 ae300000
  //   22100001 22310004 ae300000 22100001 22310004 ae300000 22100001 22310004 ae300000 22100001 22310004
  //   ae300000 22100001 22310004 ae300000 22100001 22310004 ae300000 22100001 22310004 ae300000 22100001
  //   22310004 ae300000 22100001 22310004 ae300000 22100001 22310004 ae300000 22100001 22310004 ae300000
  //   22100001 22310004 ae300000 22100001 22310004 ae300000 22100001 22310004 22100001 8020 2011003c
  //   8e130000 8e340000 274402a 11000002 ae330000 ae140000 2231fffc 1611fff8 102020 20020022 c 22100004
  //   2011003c 1611fff2 20100001 201200ff 20110001 20130003 12120005 12100004 20110001 20120002 20130003
  //   8000d26 102020 20020001 c 16310005 16320004 20110001 20120002 20130003 8000d26 132020 20020001 c
  //   2011ffff 118c00 2020 24840064 2484ff9c 14800017 2020 2484ff9c 24840064 14800013 2020 34847fff 912024
  //   1480000f 2020 34848000 912024 1480000b 24040000 8000d20 8000d26 2002000a c 20041ced 42400 3484cafe
  //   20020022 c 8000d1e 3c010000 3421baad 12020 42400 3484c0de 20020022 c 8000d1e 20100000 22100001
  //   102020 20020022 c 22100002 102020 20020022 c 22100003 102020 20020022 c 22100004 102020 20020022 c
  //   22100005 102020 20020022 c 22100006 102020 20020022 c 22100007 102020 20020022 c 22100008 102020
  //   20020022 c 3e00008
  //   contents of rom_2 (hex, n*v repeats v):
  //   201a0001 409a0800 201c0040 39df020 401a0000 afda0000 23de0004 23bd0004 afd00000 23bd0004 23de0004
  //   afd40000 23bd0004 23de0004 afd50000 23bd0004 23de0004 afd60000 23bd0004 23de0004 afc40000 23bd0004
  //   23de0004 afc20000 23bd0004 23de0004 40161000 22d60001 201a0000 409a0800 20140005 20150001 168020
  //   102020 20020022 c 108100 1600fffb 295a022 1680fff8 201a0001 409a0800 23defffc 23bdfffc 8fc20000
  //   23defffc 23bdfffc 8fc40000 23defffc 23bdfffc 8fd60000 23defffc 23bdfffc 8fd50000 23defffc 23bdfffc
  //   8fd40000 23defffc 23bdfffc 8fd00000 23defffc 23bdfffc 8fda0000 409a0000 201a0000 409a0800 42000018
endmodule

module Control (
  input  [5:0] op,
  input  [5:0] Funct,
  output IsJAL,
  output MemRead,
  output IsShamt,
  output MemWrite,
  output MemtoReg,
  output Jump,
  output RegWrite,
  output Branch,
  output BneOrBeq,
  output RegDst,
  output [3:0] ALUop,
  output ALUSrc,
  output IsJR,
  output IsSyscall,
  output IsCOP0,
  output ZeroExtend
);

  wire funct_decoder_1_isjr, funct_decoder_1_isshamt, funct_decoder_1_issyscall, IsSpecial, not_1_out;
  wire [3:0] alu_decoder_1_aluop3, funct_decoder_1_alu3;

  Opcode_Decoder opcode_decoder_1 (
    .op0(op[5]), .MemRead(MemRead), .op1(op[4]), .op2(op[3]), .MemWrite(MemWrite), .op3(op[2]), .op4(op[1]),
    .op5(op[0]), .ALUSrc(ALUSrc), .Jump(Jump), .MemtoReg(MemtoReg), .Branch(Branch), .RegDst(RegDst),
    .RegWrite(RegWrite), .BneBeq(BneOrBeq), .IsJAL(IsJAL), .ZeroExtend(ZeroExtend));
  Funct_Decoder funct_decoder_1 (
    .Funct0(Funct[5]), .Funct1(Funct[4]), .Funct2(Funct[3]), .Funct3(Funct[2]),
    .ALU0(funct_decoder_1_alu3[3]), .Funct4(Funct[1]), .Funct5(Funct[0]), .ALU1(funct_decoder_1_alu3[2]),
    .ALU2(funct_decoder_1_alu3[1]), .ALU3(funct_decoder_1_alu3[0]), .IsJR(funct_decoder_1_isjr),
    .IsSyscall(funct_decoder_1_issyscall), .IsShamt(funct_decoder_1_isshamt));
  ALU_Decoder alu_decoder_1 (
    .op0(op[5]), .op1(op[4]), .op2(op[3]), .ALUop0(alu_decoder_1_aluop3[3]), .op3(op[2]), .op4(op[1]),
    .op5(op[0]), .ALUop1(alu_decoder_1_aluop3[2]), .ALUop2(alu_decoder_1_aluop3[1]),
    .ALUop3(alu_decoder_1_aluop3[0]));
  and and_1 (IsCOP0, ~op[5], op[4], ~op[3], ~op[2], ~op[1], ~op[0]);  // AND_Gate
  Multiplexer #(.enable("false")) multiplexer_1 (
    .in0(1'b0), .in1(funct_decoder_1_issyscall), .out(IsSyscall), .sel(IsSpecial));
  Multiplexer #(.enable("false")) multiplexer_2 (.in0(1'b0), .in1(funct_decoder_1_isjr), .out(IsJR), .sel(IsSpecial));
  Multiplexer #(.enable("false")) multiplexer_3 (
    .in0(1'b0), .in1(funct_decoder_1_isshamt), .out(IsShamt), .sel(IsSpecial));
  not not_1 (not_1_out, IsSpecial);
  Multiplexer #(.width(4), .enable("false")) multiplexer_4 (
    .in0(funct_decoder_1_alu3), .in1(alu_decoder_1_aluop3), .out(ALUop), .sel(not_1_out));
  and and_2 (IsSpecial, ~op[5], ~op[4], ~op[3], ~op[2], ~op[1], ~op[0]);  // AND_Gate

  // Notes on the sheet:
  //   Input & Output
  //   OP Decoding Area
  //   ALU Decoding Area
  //   Exception Handler
endmodule

module Funct_Decoder (
  input  Funct0,
  input  Funct1,
  input  Funct2,
  input  Funct3,
  input  Funct4,
  input  Funct5,
  output ALU0,
  output ALU1,
  output ALU2,
  output ALU3,
  output IsJR,
  output IsSyscall,
  output IsShamt
);

  wire and_1_out, and_2_out, and_3_out, and_4_out, and_5_out, and_6_out, and_7_out, and_8_out, and_9_out,
       and_10_out, and_11_out, and_12_out, and_13_out, and_14_out, and_15_out, and_16_out, and_17_out,
       and_20_out, and_21_out, and_22_out, not_1_out, not_2_out, not_3_out, not_4_out, not_5_out, not_6_out,
       not_7_out, not_8_out, not_9_out, not_10_out, not_11_out, not_12_out, not_13_out, not_14_out,
       not_15_out, not_16_out, not_17_out, not_18_out, not_19_out, not_20_out, not_21_out, not_22_out,
       not_23_out, not_24_out, not_25_out, not_26_out, not_27_out, not_28_out, not_29_out, not_30_out,
       not_31_out, not_32_out, not_33_out, not_34_out, not_35_out, not_36_out, not_37_out, not_38_out,
       not_39_out, not_40_out, not_41_out, not_42_out, not_43_out, not_44_out, not_45_out, not_46_out,
       not_47_out, not_48_out, not_49_out, not_50_out, not_51_out, not_52_out, not_53_out, not_54_out,
       not_55_out, not_56_out, not_57_out, not_58_out, not_59_out, not_60_out, not_61_out, not_62_out,
       not_63_out, not_64_out, not_65_out, not_66_out, not_67_out, not_68_out, not_69_out, not_70_out,
       not_71_out, not_72_out, not_73_out, not_74_out, not_75_out, not_76_out, not_77_out, not_78_out,
       not_79_out, not_80_out, not_81_out;

  not not_1 (not_1_out, Funct1);
  not not_2 (not_2_out, Funct2);
  not not_3 (not_3_out, Funct4);
  not not_4 (not_4_out, Funct1);
  not not_5 (not_5_out, Funct2);
  not not_6 (not_6_out, Funct1);
  not not_7 (not_7_out, Funct3);
  not not_8 (not_8_out, Funct5);
  not not_9 (not_9_out, Funct1);
  not not_10 (not_10_out, Funct3);
  not not_11 (not_11_out, Funct1);
  not not_12 (not_12_out, Funct2);
  not not_13 (not_13_out, Funct3);
  not not_14 (not_14_out, Funct4);
  not not_15 (not_15_out, Funct1);
  not not_16 (not_16_out, Funct2);
  not not_17 (not_17_out, Funct3);
  not not_18 (not_18_out, Funct5);
  not not_19 (not_19_out, Funct1);
  not not_20 (not_20_out, Funct2);
  not not_21 (not_21_out, Funct4);
  not not_22 (not_22_out, Funct5);
  not not_23 (not_23_out, Funct1);
  not not_24 (not_24_out, Funct3);
  not not_25 (not_25_out, Funct1);
  not not_26 (not_26_out, Funct2);
  not not_27 (not_27_out, Funct3);
  not not_28 (not_28_out, Funct5);
  not not_29 (not_29_out, Funct1);
  not not_30 (not_30_out, Funct2);
  not not_31 (not_31_out, Funct4);
  not not_32 (not_32_out, Funct5);
  not not_33 (not_33_out, Funct0);
  not not_34 (not_34_out, Funct1);
  not not_35 (not_35_out, Funct2);
  not not_36 (not_36_out, Funct3);
  not not_37 (not_37_out, Funct5);
  not not_38 (not_38_out, Funct1);
  not not_39 (not_39_out, Funct2);
  not not_40 (not_40_out, Funct1);
  not not_41 (not_41_out, Funct3);
  not not_42 (not_42_out, Funct5);
  not not_43 (not_43_out, Funct0);
  not not_44 (not_44_out, Funct1);
  not not_45 (not_45_out, Funct2);
  not not_46 (not_46_out, Funct3);
  not not_47 (not_47_out, Funct1);
  not not_48 (not_48_out, Funct2);
  not not_49 (not_49_out, Funct3);
  not not_50 (not_50_out, Funct4);
  not not_51 (not_51_out, Funct1);
  not not_52 (not_52_out, Funct2);
  not not_53 (not_53_out, Funct4);
  not not_54 (not_54_out, Funct5);
  not not_55 (not_55_out, Funct1);
  not not_56 (not_56_out, Funct3);
  not not_57 (not_57_out, Funct5);
  not not_58 (not_58_out, Funct0);
  not not_59 (not_59_out, Funct1);
  not not_60 (not_60_out, Funct3);
  not not_61 (not_61_out, Funct4);
  not not_62 (not_62_out, Funct5);
  not not_63 (not_63_out, Funct0);
  not not_64 (not_64_out, Funct1);
  not not_65 (not_65_out, Funct4);
  not not_66 (not_66_out, Funct5);
  not not_67 (not_67_out, Funct0);
  not not_68 (not_68_out, Funct1);
  not not_69 (not_69_out, Funct2);
  not not_70 (not_70_out, Funct3);
  not not_71 (not_71_out, Funct0);
  not not_72 (not_72_out, Funct1);
  not not_73 (not_73_out, Funct2);
  not not_74 (not_74_out, Funct3);
  not not_75 (not_75_out, Funct5);
  not not_76 (not_76_out, Funct0);
  not not_77 (not_77_out, Funct1);
  not not_78 (not_78_out, Funct2);
  not not_79 (not_79_out, Funct3);
  not not_80 (not_80_out, Funct4);
  not not_81 (not_81_out, Funct5);
  and and_1 (and_1_out, Funct0, not_1_out, not_2_out, Funct3, not_3_out, Funct5);
  and and_2 (and_2_out, Funct0, not_4_out, not_5_out, Funct3, Funct4, Funct5);
  and and_3 (and_3_out, Funct0, not_6_out, Funct2, not_7_out, Funct4, not_8_out);
  and and_4 (and_4_out, Funct0, not_9_out, Funct2, not_10_out, Funct4, Funct5);
  and and_5 (and_5_out, Funct0, not_11_out, not_12_out, not_13_out, not_14_out);
  and and_6 (and_6_out, Funct0, not_15_out, not_16_out, not_17_out, not_18_out);
  and and_7 (and_7_out, Funct0, not_19_out, not_20_out, not_21_out, not_22_out);
  and and_8 (and_8_out, Funct0, not_23_out, Funct2, not_24_out, Funct4, Funct5);
  and and_9 (and_9_out, Funct0, not_25_out, not_26_out, not_27_out, Funct4, not_28_out);
  and and_10 (and_10_out, Funct0, not_29_out, not_30_out, Funct3, not_31_out, not_32_out);
  and and_11 (and_11_out, not_33_out, not_34_out, not_35_out, not_36_out, Funct4, not_37_out);
  and and_12 (and_12_out, Funct0, not_38_out, not_39_out, Funct3, Funct4, Funct5);
  and and_13 (and_13_out, Funct0, not_40_out, Funct2, not_41_out, Funct4, not_42_out);
  and and_14 (and_14_out, not_43_out, not_44_out, not_45_out, not_46_out, Funct4, Funct5);
  and and_15 (and_15_out, Funct0, not_47_out, not_48_out, not_49_out, not_50_out);
  and and_16 (and_16_out, Funct0, not_51_out, not_52_out, not_53_out, not_54_out);
  and and_17 (and_17_out, Funct0, not_55_out, Funct2, not_56_out, Funct4, not_57_out);
  and and_18 (IsJR, not_58_out, not_59_out, Funct2, not_60_out, not_61_out, not_62_out);
  and and_19 (IsSyscall, not_63_out, not_64_out, Funct2, Funct3, not_65_out, not_66_out);
  and and_20 (and_20_out, not_67_out, not_68_out, not_69_out, not_70_out, Funct4, Funct5);
  and and_21 (and_21_out, not_71_out, not_72_out, not_73_out, not_74_out, Funct4, not_75_out);
  and and_22 (and_22_out, not_76_out, not_77_out, not_78_out, not_79_out, not_80_out, not_81_out);
  or or_1 (ALU0, and_1_out, and_2_out, and_3_out, and_4_out);
  or or_2 (ALU1, and_5_out, and_6_out, and_7_out, and_8_out);
  or or_3 (ALU2, and_9_out, and_10_out, and_11_out, and_12_out, and_13_out);
  or or_4 (ALU3, and_14_out, and_15_out, and_16_out, and_17_out);
  or or_5 (IsShamt, and_20_out, and_21_out, and_22_out);
endmodule

module ALU_Decoder (
  input  op0,
  input  op1,
  input  op2,
  input  op3,
  input  op4,
  input  op5,
  output ALUop0,
  output ALUop1,
  output ALUop2,
  output ALUop3
);

  wire and_1_out, and_2_out, and_3_out, and_4_out, and_5_out, and_6_out, and_7_out, and_8_out, and_9_out,
       and_10_out, and_11_out, and_12_out, and_13_out, and_14_out, and_15_out, and_16_out, and_17_out,
       and_18_out, and_19_out, and_20_out, and_21_out, and_22_out, and_23_out, and_24_out, and_25_out,
       and_26_out, and_27_out, and_28_out, and_29_out, not_1_out, not_2_out, not_3_out, not_4_out, not_5_out,
       not_6_out, not_7_out, not_8_out, not_9_out, not_10_out, not_11_out, not_12_out, not_13_out,
       not_14_out, not_15_out, not_16_out, not_17_out, not_18_out, not_19_out, not_20_out, not_21_out,
       not_22_out, not_23_out, not_24_out, not_25_out, not_26_out, not_27_out, not_28_out, not_29_out,
       not_30_out, not_31_out, not_32_out, not_33_out, not_34_out, not_35_out, not_36_out, not_37_out,
       not_38_out, not_39_out, not_40_out, not_41_out, not_42_out, not_43_out, not_44_out, not_45_out,
       not_46_out, not_47_out, not_48_out, not_49_out, not_50_out, not_51_out, not_52_out, not_53_out,
       not_54_out, not_55_out, not_56_out, not_57_out, not_58_out, not_59_out, not_60_out, not_61_out,
       not_62_out, not_63_out, not_64_out, not_65_out, not_66_out, not_67_out, not_68_out, not_69_out,
       not_70_out, not_71_out, not_72_out, not_73_out, not_74_out, not_75_out, not_76_out, not_77_out,
       not_78_out, not_79_out, not_80_out, not_81_out, not_82_out, not_83_out, not_84_out, not_85_out,
       not_86_out, not_87_out, not_88_out, not_89_out, not_90_out, not_91_out, not_92_out, not_93_out,
       not_94_out, not_95_out, not_96_out, not_97_out, not_98_out, not_99_out, not_100_out, not_101_out,
       not_102_out, not_103_out, not_104_out, not_105_out, not_106_out, not_107_out, not_108_out,
       not_109_out, not_110_out, not_111_out, not_112_out, not_113_out, not_114_out, not_115_out,
       not_116_out, not_117_out, not_118_out, not_119_out, not_120_out, not_121_out, not_122_out, not_123_out;

  not not_1 (not_1_out, op0);
  not not_2 (not_2_out, op1);
  not not_3 (not_3_out, op4);
  not not_4 (not_4_out, op0);
  not not_5 (not_5_out, op1);
  not not_6 (not_6_out, op3);
  not not_7 (not_7_out, op5);
  not not_8 (not_8_out, op0);
  not not_9 (not_9_out, op1);
  not not_10 (not_10_out, op2);
  not not_11 (not_11_out, op3);
  not not_12 (not_12_out, op4);
  not not_13 (not_13_out, op5);
  not not_14 (not_14_out, op0);
  not not_15 (not_15_out, op1);
  not not_16 (not_16_out, op3);
  not not_17 (not_17_out, op4);
  not not_18 (not_18_out, op5);
  not not_19 (not_19_out, op1);
  not not_20 (not_20_out, op2);
  not not_21 (not_21_out, op3);
  not not_22 (not_22_out, op1);
  not not_23 (not_23_out, op3);
  not not_24 (not_24_out, op0);
  not not_25 (not_25_out, op1);
  not not_26 (not_26_out, op2);
  not not_27 (not_27_out, op4);
  not not_28 (not_28_out, op0);
  not not_29 (not_29_out, op1);
  not not_30 (not_30_out, op2);
  not not_31 (not_31_out, op4);
  not not_32 (not_32_out, op5);
  not not_33 (not_33_out, op0);
  not not_34 (not_34_out, op1);
  not not_35 (not_35_out, op4);
  not not_36 (not_36_out, op5);
  not not_37 (not_37_out, op0);
  not not_38 (not_38_out, op1);
  not not_39 (not_39_out, op3);
  not not_40 (not_40_out, op4);
  not not_41 (not_41_out, op0);
  not not_42 (not_42_out, op1);
  not not_43 (not_43_out, op3);
  not not_44 (not_44_out, op4);
  not not_45 (not_45_out, op5);
  not not_46 (not_46_out, op0);
  not not_47 (not_47_out, op1);
  not not_48 (not_48_out, op2);
  not not_49 (not_49_out, op3);
  not not_50 (not_50_out, op5);
  not not_51 (not_51_out, op0);
  not not_52 (not_52_out, op1);
  not not_53 (not_53_out, op2);
  not not_54 (not_54_out, op3);
  not not_55 (not_55_out, op0);
  not not_56 (not_56_out, op2);
  not not_57 (not_57_out, op3);
  not not_58 (not_58_out, op4);
  not not_59 (not_59_out, op5);
  not not_60 (not_60_out, op0);
  not not_61 (not_61_out, op1);
  not not_62 (not_62_out, op4);
  not not_63 (not_63_out, op5);
  not not_64 (not_64_out, op0);
  not not_65 (not_65_out, op1);
  not not_66 (not_66_out, op3);
  not not_67 (not_67_out, op5);
  not not_68 (not_68_out, op0);
  not not_69 (not_69_out, op1);
  not not_70 (not_70_out, op2);
  not not_71 (not_71_out, op3);
  not not_72 (not_72_out, op4);
  not not_73 (not_73_out, op5);
  not not_74 (not_74_out, op0);
  not not_75 (not_75_out, op1);
  not not_76 (not_76_out, op3);
  not not_77 (not_77_out, op4);
  not not_78 (not_78_out, op5);
  not not_79 (not_79_out, op1);
  not not_80 (not_80_out, op2);
  not not_81 (not_81_out, op3);
  not not_82 (not_82_out, op1);
  not not_83 (not_83_out, op3);
  not not_84 (not_84_out, op0);
  not not_85 (not_85_out, op1);
  not not_86 (not_86_out, op2);
  not not_87 (not_87_out, op4);
  not not_88 (not_88_out, op0);
  not not_89 (not_89_out, op1);
  not not_90 (not_90_out, op2);
  not not_91 (not_91_out, op4);
  not not_92 (not_92_out, op5);
  not not_93 (not_93_out, op0);
  not not_94 (not_94_out, op1);
  not not_95 (not_95_out, op4);
  not not_96 (not_96_out, op5);
  not not_97 (not_97_out, op0);
  not not_98 (not_98_out, op1);
  not not_99 (not_99_out, op3);
  not not_100 (not_100_out, op5);
  not not_101 (not_101_out, op0);
  not not_102 (not_102_out, op1);
  not not_103 (not_103_out, op3);
  not not_104 (not_104_out, op4);
  not not_105 (not_105_out, op0);
  not not_106 (not_106_out, op1);
  not not_107 (not_107_out, op3);
  not not_108 (not_108_out, op4);
  not not_109 (not_109_out, op5);
  not not_110 (not_110_out, op0);
  not not_111 (not_111_out, op1);
  not not_112 (not_112_out, op2);
  not not_113 (not_113_out, op3);
  not not_114 (not_114_out, op5);
  not not_115 (not_115_out, op0);
  not not_116 (not_116_out, op1);
  not not_117 (not_117_out, op2);
  not not_118 (not_118_out, op3);
  not not_119 (not_119_out, op0);
  not not_120 (not_120_out, op2);
  not not_121 (not_121_out, op3);
  not not_122 (not_122_out, op4);
  not not_123 (not_123_out, op5);
  and and_1 (and_1_out, not_1_out, not_2_out, op2, op3, not_3_out, op5);
  and and_2 (and_2_out, not_4_out, not_5_out, op2, not_6_out, op4, not_7_out);
  and and_3 (and_3_out, not_8_out, not_9_out, not_10_out, not_11_out, not_12_out, not_13_out);
  and and_4 (and_4_out, not_14_out, not_15_out, op2, not_16_out, not_17_out, not_18_out);
  and and_5 (and_5_out, op0, not_19_out, not_20_out, not_21_out, op4, op5);
  and and_6 (and_6_out, op0, not_22_out, op2, not_23_out, op4, op5);
  and and_7 (and_7_out, not_24_out, not_25_out, not_26_out, op3, not_27_out, op5);
  and and_8 (and_8_out, not_28_out, not_29_out, not_30_out, op3, not_31_out, not_32_out);
  and and_9 (and_9_out, not_33_out, not_34_out, op2, op3, not_35_out, not_36_out);
  and and_10 (and_10_out, not_37_out, not_38_out, op2, not_39_out, not_40_out, op5);
  and and_11 (and_11_out, not_41_out, not_42_out, op2, not_43_out, not_44_out, not_45_out);
  and and_12 (and_12_out, not_46_out, not_47_out, not_48_out, not_49_out, op4, not_50_out);
  and and_13 (and_13_out, not_51_out, not_52_out, not_53_out, not_54_out, op4, op5);
  and and_14 (and_14_out, not_55_out, op1, not_56_out, not_57_out, not_58_out, not_59_out);
  and and_15 (and_15_out, not_60_out, not_61_out, op2, op3, not_62_out, not_63_out);
  and and_16 (and_16_out, not_64_out, not_65_out, op2, not_66_out, op4, not_67_out);
  and and_17 (and_17_out, not_68_out, not_69_out, not_70_out, not_71_out, not_72_out, not_73_out);
  and and_18 (and_18_out, not_74_out, not_75_out, op2, not_76_out, not_77_out, not_78_out);
  and and_19 (and_19_out, op0, not_79_out, not_80_out, not_81_out, op4, op5);
  and and_20 (and_20_out, op0, not_82_out, op2, not_83_out, op4, op5);
  and and_21 (and_21_out, not_84_out, not_85_out, not_86_out, op3, not_87_out, op5);
  and and_22 (and_22_out, not_88_out, not_89_out, not_90_out, op3, not_91_out, not_92_out);
  and and_23 (and_23_out, not_93_out, not_94_out, op2, op3, not_95_out, not_96_out);
  and and_24 (and_24_out, not_97_out, not_98_out, op2, not_99_out, op4, not_100_out);
  and and_25 (and_25_out, not_101_out, not_102_out, op2, not_103_out, not_104_out, op5);
  and and_26 (and_26_out, not_105_out, not_106_out, op2, not_107_out, not_108_out, not_109_out);
  and and_27 (and_27_out, not_110_out, not_111_out, not_112_out, not_113_out, op4, not_114_out);
  and and_28 (and_28_out, not_115_out, not_116_out, not_117_out, not_118_out, op4, op5);
  and and_29 (and_29_out, not_119_out, op1, not_120_out, not_121_out, not_122_out, not_123_out);
  or or_1 (ALUop0, and_1_out, and_2_out);
  or or_2 (ALUop2, and_15_out, and_16_out);
  or or_3 (ALUop1, and_3_out, and_4_out, and_5_out, and_6_out, and_7_out, and_8_out, and_9_out, and_10_out, and_11_out, and_12_out, and_13_out, and_14_out);
  or or_4 (ALUop3, and_17_out, and_18_out, and_19_out, and_20_out, and_21_out, and_22_out, and_23_out, and_24_out, and_25_out, and_26_out, and_27_out, and_28_out, and_29_out);
endmodule

module Opcode_Decoder (
  input  op0,
  input  op1,
  input  op2,
  input  op3,
  input  op4,
  input  op5,
  output MemRead,
  output MemWrite,
  output ALUSrc,
  output Jump,
  output MemtoReg,
  output Branch,
  output RegDst,
  output RegWrite,
  output BneBeq,
  output IsJAL,
  output ZeroExtend
);

  wire and_3_out, and_4_out, and_5_out, and_6_out, and_7_out, and_8_out, and_9_out, and_10_out, and_11_out,
       and_12_out, and_14_out, and_15_out, and_17_out, and_18_out, and_19_out, and_20_out, and_21_out,
       and_22_out, and_23_out, and_24_out, and_25_out, and_26_out, and_29_out, and_30_out, not_1_out,
       not_2_out, not_3_out, not_4_out, not_5_out, not_6_out, not_7_out, not_8_out, not_9_out, not_10_out,
       not_11_out, not_12_out, not_13_out, not_14_out, not_15_out, not_16_out, not_17_out, not_18_out,
       not_19_out, not_20_out, not_21_out, not_22_out, not_23_out, not_24_out, not_25_out, not_26_out,
       not_27_out, not_28_out, not_29_out, not_30_out, not_31_out, not_32_out, not_33_out, not_34_out,
       not_35_out, not_36_out, not_37_out, not_38_out, not_39_out, not_40_out, not_41_out, not_42_out,
       not_43_out, not_44_out, not_45_out, not_46_out, not_47_out, not_48_out, not_49_out, not_50_out,
       not_51_out, not_52_out, not_53_out, not_54_out, not_55_out, not_56_out, not_57_out, not_58_out,
       not_59_out, not_60_out, not_61_out, not_62_out, not_63_out, not_64_out, not_65_out, not_66_out,
       not_67_out, not_68_out, not_69_out, not_70_out, not_71_out, not_72_out, not_73_out, not_74_out,
       not_75_out, not_76_out, not_77_out, not_78_out, not_79_out, not_80_out, not_81_out, not_82_out,
       not_83_out, not_84_out, not_85_out, not_86_out, not_87_out, not_88_out, not_89_out, not_90_out,
       not_91_out, not_92_out, not_93_out, not_94_out, not_95_out, not_96_out, not_97_out, not_98_out,
       not_99_out, not_100_out, not_101_out, not_102_out, not_103_out, not_104_out, not_105_out, not_106_out,
       not_107_out, not_108_out, not_109_out, not_110_out, not_111_out, not_112_out, not_113_out,
       not_114_out, not_115_out, not_116_out, not_117_out, not_118_out, not_119_out;

  not not_1 (not_1_out, op1);
  not not_2 (not_2_out, op2);
  not not_3 (not_3_out, op3);
  not not_4 (not_4_out, op1);
  not not_5 (not_5_out, op3);
  not not_6 (not_6_out, op0);
  not not_7 (not_7_out, op1);
  not not_8 (not_8_out, op3);
  not not_9 (not_9_out, op4);
  not not_10 (not_10_out, op5);
  not not_11 (not_11_out, op1);
  not not_12 (not_12_out, op2);
  not not_13 (not_13_out, op3);
  not not_14 (not_14_out, op1);
  not not_15 (not_15_out, op3);
  not not_16 (not_16_out, op0);
  not not_17 (not_17_out, op1);
  not not_18 (not_18_out, op4);
  not not_19 (not_19_out, op5);
  not not_20 (not_20_out, op0);
  not not_21 (not_21_out, op1);
  not not_22 (not_22_out, op4);
  not not_23 (not_23_out, op0);
  not not_24 (not_24_out, op1);
  not not_25 (not_25_out, op3);
  not not_26 (not_26_out, op5);
  not not_27 (not_27_out, op0);
  not not_28 (not_28_out, op1);
  not not_29 (not_29_out, op3);
  not not_30 (not_30_out, op4);
  not not_31 (not_31_out, op0);
  not not_32 (not_32_out, op1);
  not not_33 (not_33_out, op3);
  not not_34 (not_34_out, op4);
  not not_35 (not_35_out, op5);
  not not_36 (not_36_out, op0);
  not not_37 (not_37_out, op1);
  not not_38 (not_38_out, op2);
  not not_39 (not_39_out, op3);
  not not_40 (not_40_out, op5);
  not not_41 (not_41_out, op0);
  not not_42 (not_42_out, op1);
  not not_43 (not_43_out, op2);
  not not_44 (not_44_out, op3);
  not not_45 (not_45_out, op1);
  not not_46 (not_46_out, op2);
  not not_47 (not_47_out, op3);
  not not_48 (not_48_out, op0);
  not not_49 (not_49_out, op1);
  not not_50 (not_50_out, op2);
  not not_51 (not_51_out, op4);
  not not_52 (not_52_out, op0);
  not not_53 (not_53_out, op1);
  not not_54 (not_54_out, op2);
  not not_55 (not_55_out, op4);
  not not_56 (not_56_out, op5);
  not not_57 (not_57_out, op0);
  not not_58 (not_58_out, op1);
  not not_59 (not_59_out, op2);
  not not_60 (not_60_out, op3);
  not not_61 (not_61_out, op4);
  not not_62 (not_62_out, op5);
  not not_63 (not_63_out, op0);
  not not_64 (not_64_out, op1);
  not not_65 (not_65_out, op2);
  not not_66 (not_66_out, op3);
  not not_67 (not_67_out, op4);
  not not_68 (not_68_out, op5);
  not not_69 (not_69_out, op0);
  not not_70 (not_70_out, op1);
  not not_71 (not_71_out, op3);
  not not_72 (not_72_out, op4);
  not not_73 (not_73_out, op5);
  not not_74 (not_74_out, op1);
  not not_75 (not_75_out, op2);
  not not_76 (not_76_out, op3);
  not not_77 (not_77_out, op0);
  not not_78 (not_78_out, op1);
  not not_79 (not_79_out, op4);
  not not_80 (not_80_out, op5);
  not not_81 (not_81_out, op0);
  not not_82 (not_82_out, op1);
  not not_83 (not_83_out, op4);
  not not_84 (not_84_out, op0);
  not not_85 (not_85_out, op1);
  not not_86 (not_86_out, op3);
  not not_87 (not_87_out, op5);
  not not_88 (not_88_out, op0);
  not not_89 (not_89_out, op1);
  not not_90 (not_90_out, op3);
  not not_91 (not_91_out, op4);
  not not_92 (not_92_out, op0);
  not not_93 (not_93_out, op1);
  not not_94 (not_94_out, op3);
  not not_95 (not_95_out, op4);
  not not_96 (not_96_out, op5);
  not not_97 (not_97_out, op0);
  not not_98 (not_98_out, op1);
  not not_99 (not_99_out, op2);
  not not_100 (not_100_out, op3);
  not not_101 (not_101_out, op0);
  not not_102 (not_102_out, op2);
  not not_103 (not_103_out, op3);
  not not_104 (not_104_out, op4);
  not not_105 (not_105_out, op5);
  not not_106 (not_106_out, op0);
  not not_107 (not_107_out, op1);
  not not_108 (not_108_out, op2);
  not not_109 (not_109_out, op4);
  not not_110 (not_110_out, op0);
  not not_111 (not_111_out, op1);
  not not_112 (not_112_out, op2);
  not not_113 (not_113_out, op3);
  not not_114 (not_114_out, op0);
  not not_115 (not_115_out, op1);
  not not_116 (not_116_out, op4);
  not not_117 (not_117_out, op0);
  not not_118 (not_118_out, op1);
  not not_119 (not_119_out, op5);
  and and_1 (MemRead, op0, not_1_out, not_2_out, not_3_out, op4, op5);
  and and_2 (MemWrite, op0, not_4_out, op2, not_5_out, op4, op5);
  and and_3 (and_3_out, not_6_out, not_7_out, op2, not_8_out, not_9_out, not_10_out);
  and and_4 (and_4_out, op0, not_11_out, not_12_out, not_13_out, op4, op5);
  and and_5 (and_5_out, op0, not_14_out, op2, not_15_out, op4, op5);
  and and_6 (and_6_out, not_16_out, not_17_out, op2, op3, not_18_out, not_19_out);
  and and_7 (and_7_out, not_20_out, not_21_out, op2, op3, not_22_out, op5);
  and and_8 (and_8_out, not_23_out, not_24_out, op2, not_25_out, op4, not_26_out);
  and and_9 (and_9_out, not_27_out, not_28_out, op2, not_29_out, not_30_out, op5);
  and and_10 (and_10_out, not_31_out, not_32_out, op2, not_33_out, not_34_out, not_35_out);
  and and_11 (and_11_out, not_36_out, not_37_out, not_38_out, not_39_out, op4, not_40_out);
  and and_12 (and_12_out, not_41_out, not_42_out, not_43_out, not_44_out, op4, op5);
  and and_13 (MemtoReg, op0, not_45_out, not_46_out, not_47_out, op4, op5);
  and and_14 (and_14_out, not_48_out, not_49_out, not_50_out, op3, not_51_out, op5);
  and and_15 (and_15_out, not_52_out, not_53_out, not_54_out, op3, not_55_out, not_56_out);
  and and_16 (RegDst, not_57_out, not_58_out, not_59_out, not_60_out, not_61_out, not_62_out);
  and and_17 (and_17_out, not_63_out, not_64_out, not_65_out, not_66_out, not_67_out, not_68_out);
  and and_18 (and_18_out, not_69_out, not_70_out, op2, not_71_out, not_72_out, not_73_out);
  and and_19 (and_19_out, op0, not_74_out, not_75_out, not_76_out, op4, op5);
  and and_20 (and_20_out, not_77_out, not_78_out, op2, op3, not_79_out, not_80_out);
  and and_21 (and_21_out, not_81_out, not_82_out, op2, op3, not_83_out, op5);
  and and_22 (and_22_out, not_84_out, not_85_out, op2, not_86_out, op4, not_87_out);
  and and_23 (and_23_out, not_88_out, not_89_out, op2, not_90_out, not_91_out, op5);
  and and_24 (and_24_out, not_92_out, not_93_out, op2, not_94_out, not_95_out, not_96_out);
  and and_25 (and_25_out, not_97_out, not_98_out, not_99_out, not_100_out, op4, op5);
  and and_26 (and_26_out, not_101_out, op1, not_102_out, not_103_out, not_104_out, not_105_out);
  and and_27 (BneBeq, not_106_out, not_107_out, not_108_out, op3, not_109_out, op5);
  and and_28 (IsJAL, not_110_out, not_111_out, not_112_out, not_113_out, op4, op5);
  and and_29 (and_29_out, not_114_out, not_115_out, op2, op3, not_116_out);
  and and_30 (and_30_out, not_117_out, not_118_out, op2, op3, op4, not_119_out);
  or or_1 (ALUSrc, and_3_out, and_4_out, and_5_out, and_6_out, and_7_out, and_8_out, and_9_out, and_10_out);
  or or_2 (Jump, and_11_out, and_12_out);
  or or_3 (Branch, and_14_out, and_15_out);
  or or_4 (ZeroExtend, and_29_out, and_30_out);
  or or_5 (RegWrite, and_17_out, and_18_out, and_19_out, and_20_out, and_21_out, and_22_out, and_23_out, and_24_out, and_25_out, and_26_out);
endmodule

module Syscall_Decoder (
  input  clk,
  input  Enable,
  input  [31:0] a0,
  input  [31:0] v0,
  output [3:0] Hex0,
  output [3:0] Hex1,
  output [3:0] Hex2,
  output [3:0] Hex3,
  output [3:0] Hex4,
  output [3:0] Hex5,
  output [3:0] Hex6,
  output [3:0] Hex7,
  output Halt
);

  wire comparator_1_eq, multiplexer_1_out;

  Comparator #(.width(32)) comparator_1 (.a(v0), .b(32'ha), .eq(comparator_1_eq));  // open: gt, lt
  Register #(.width(32)) register_1 (
    .D(a0), .en(Enable), .Q({Hex0, Hex1, Hex2, Hex3, Hex4, Hex5, Hex6, Hex7}), .clk(clk));  // open: clr
  Multiplexer #(.enable("false")) multiplexer_1 (
    .in0(1'b0), .in1(comparator_1_eq), .out(multiplexer_1_out), .sel(Enable));
  D_Flip_Flop d_ff_1 (.clk(clk), .D(multiplexer_1_out), .Q(Halt));  // open: Qn, preset, en, reset
endmodule

module CP0 (
  input  ExpSrc0,
  input  clk,
  input  ExpSrc1,
  input  enable,
  input  ExpSrc2,
  input  [31:0] Inst,
  input  [31:0] PCin,
  input  [31:0] Din,
  output ExRegWrite,
  output IsEret,
  output ExpBlock,
  output HasExp,
  output [31:0] PCout,
  output [31:0] Dout
);

  wire and_4_out, and_5_out, and_6_out, counter_1_q, counter_2_q, demultiplexer_1_out0, demultiplexer_1_out1,
       ExpClick, not_2_out, not_3_out, or_1_out, or_2_out;
  wire [31:0] Cause_q, controlled_buffer_1_out, multiplexer_1_out;
  wire [31:1] Status_q;

  or or_1 (or_1_out, ExpSrc0, ExpSrc1, ExpSrc2);
  and and_1 (ExpClick, or_1_out, ~ExpBlock);  // AND_Gate
  not not_1 (ExRegWrite, Inst[23]);
  and and_2 (IsEret, ~Inst[5], Inst[4], Inst[3], ~Inst[2], ~Inst[1], ~Inst[0]);  // AND_Gate
  Counter #(.width(1), .max('h1), .ongoal("stay")) counter_1 (
    .Q(counter_1_q), .clk(ExpClick), .clr(counter_2_q));  // open: load, D, count, carry
  and and_3 (HasExp, clk, counter_1_q);
  Counter #(.width(1), .max('h1), .ongoal("stay"), .trigger("falling")) counter_2 (
    .Q(counter_2_q), .clk(HasExp), .clr(not_2_out));  // open: load, D, count, carry
  not not_2 (not_2_out, counter_1_q);
  not not_3 (not_3_out, HasExp);
  Multiplexer #(.width(32), .enable("false")) multiplexer_1 (
    .in0(PCin), .in1(Din), .out(multiplexer_1_out), .sel(not_3_out));
  Demultiplexer #(.disabled(0), .enable("false")) demultiplexer_1 (
    .out0(demultiplexer_1_out0), .out1(demultiplexer_1_out1), .in(1'b1), .sel(Inst[11]));
  assign controlled_buffer_1_out = ExpSrc0 ? {32{1'b0}} : 32'bz;  // Controlled_Buffer controlled_buffer_1
  assign controlled_buffer_1_out = ExpSrc1 ? 32'h1 : 32'bz;  // Controlled_Buffer controlled_buffer_2
  assign controlled_buffer_1_out = ExpSrc2 ? 32'h2 : 32'bz;  // Controlled_Buffer controlled_buffer_3
  and and_4 (and_4_out, demultiplexer_1_out0, and_6_out);
  and and_5 (and_5_out, and_6_out, demultiplexer_1_out1);
  or or_2 (or_2_out, HasExp, and_4_out);
  and and_6 (and_6_out, enable, ~ExRegWrite);  // AND_Gate
  Register #(.width(32), .trigger("high")) EPC (
    .D(multiplexer_1_out), .en(or_2_out), .Q(PCout), .clk(clk));  // open: clr
  Register #(.width(32)) Status (.D(Din), .en(and_5_out), .Q({Status_q, ExpBlock}), .clk(clk));  // open: clr
  Register #(.width(32)) Cause (.D(controlled_buffer_1_out), .Q(Cause_q), .clk(ExpClick));  // open: en, clr
  Multiplexer #(.select(2), .width(32), .enable("false")) multiplexer_2 (
    .in0(PCout), .in1({Status_q, ExpBlock}), .in2(Cause_q), .in3({32{1'b0}}), .out(Dout), .sel(Inst[12:11]));

  // Other names for the same wires on the sheet: Sel[1:0] = Inst[12:11]

  // Notes on the sheet:
  //   Signal Decoding
  //   Exception Signals
  //   Input & Output
  //   Registers
endmodule

module Statistics (
  input  op0,
  input  op1,
  input  op2,
  input  op3,
  input  op4,
  input  op5,
  output i,
  output r,
  output j
);

  wire and_1_out, and_2_out, and_3_out, and_4_out, and_5_out, and_6_out, and_7_out, and_8_out, and_9_out,
       and_10_out, and_12_out, and_13_out, not_1_out, not_2_out, not_3_out, not_4_out, not_5_out, not_6_out,
       not_7_out, not_8_out, not_9_out, not_10_out, not_11_out, not_12_out, not_13_out, not_14_out,
       not_15_out, not_16_out, not_17_out, not_18_out, not_19_out, not_20_out, not_21_out, not_22_out,
       not_23_out, not_24_out, not_25_out, not_26_out, not_27_out, not_28_out, not_29_out, not_30_out,
       not_31_out, not_32_out, not_33_out, not_34_out, not_35_out, not_36_out, not_37_out, not_38_out,
       not_39_out, not_40_out, not_41_out, not_42_out, not_43_out, not_44_out, not_45_out, not_46_out,
       not_47_out, not_48_out, not_49_out, not_50_out, not_51_out, not_52_out, not_53_out, not_54_out;

  not not_1 (not_1_out, op1);
  not not_2 (not_2_out, op2);
  not not_3 (not_3_out, op3);
  not not_4 (not_4_out, op1);
  not not_5 (not_5_out, op3);
  not not_6 (not_6_out, op0);
  not not_7 (not_7_out, op1);
  not not_8 (not_8_out, op2);
  not not_9 (not_9_out, op4);
  not not_10 (not_10_out, op0);
  not not_11 (not_11_out, op1);
  not not_12 (not_12_out, op2);
  not not_13 (not_13_out, op4);
  not not_14 (not_14_out, op5);
  not not_15 (not_15_out, op0);
  not not_16 (not_16_out, op1);
  not not_17 (not_17_out, op4);
  not not_18 (not_18_out, op5);
  not not_19 (not_19_out, op0);
  not not_20 (not_20_out, op1);
  not not_21 (not_21_out, op4);
  not not_22 (not_22_out, op0);
  not not_23 (not_23_out, op1);
  not not_24 (not_24_out, op3);
  not not_25 (not_25_out, op5);
  not not_26 (not_26_out, op0);
  not not_27 (not_27_out, op1);
  not not_28 (not_28_out, op3);
  not not_29 (not_29_out, op4);
  not not_30 (not_30_out, op5);
  not not_31 (not_31_out, op0);
  not not_32 (not_32_out, op1);
  not not_33 (not_33_out, op3);
  not not_34 (not_34_out, op4);
  not not_35 (not_35_out, op0);
  not not_36 (not_36_out, op1);
  not not_37 (not_37_out, op3);
  not not_38 (not_38_out, op4);
  not not_39 (not_39_out, op5);
  not not_40 (not_40_out, op0);
  not not_41 (not_41_out, op1);
  not not_42 (not_42_out, op2);
  not not_43 (not_43_out, op3);
  not not_44 (not_44_out, op4);
  not not_45 (not_45_out, op5);
  not not_46 (not_46_out, op0);
  not not_47 (not_47_out, op1);
  not not_48 (not_48_out, op2);
  not not_49 (not_49_out, op3);
  not not_50 (not_50_out, op5);
  not not_51 (not_51_out, op0);
  not not_52 (not_52_out, op1);
  not not_53 (not_53_out, op2);
  not not_54 (not_54_out, op3);
  and and_1 (and_1_out, op0, not_1_out, not_2_out, not_3_out, op4, op5);
  and and_2 (and_2_out, op0, not_4_out, op2, not_5_out, op4, op5);
  and and_3 (and_3_out, not_6_out, not_7_out, not_8_out, op3, not_9_out, op5);
  and and_4 (and_4_out, not_10_out, not_11_out, not_12_out, op3, not_13_out, not_14_out);
  and and_5 (and_5_out, not_15_out, not_16_out, op2, op3, not_17_out, not_18_out);
  and and_6 (and_6_out, not_19_out, not_20_out, op2, op3, not_21_out, op5);
  and and_7 (and_7_out, not_22_out, not_23_out, op2, not_24_out, op4, not_25_out);
  and and_8 (and_8_out, not_26_out, not_27_out, op2, not_28_out, not_29_out, not_30_out);
  and and_9 (and_9_out, not_31_out, not_32_out, op2, not_33_out, not_34_out, op5);
  and and_10 (and_10_out, not_35_out, not_36_out, op2, not_37_out, not_38_out, not_39_out);
  and and_11 (r, not_40_out, not_41_out, not_42_out, not_43_out, not_44_out, not_45_out);
  and and_12 (and_12_out, not_46_out, not_47_out, not_48_out, not_49_out, op4, not_50_out);
  and and_13 (and_13_out, not_51_out, not_52_out, not_53_out, not_54_out, op4, op5);
  or or_1 (j, and_12_out, and_13_out);
  or or_2 (i, and_1_out, and_2_out, and_3_out, and_4_out, and_5_out, and_6_out, and_7_out, and_8_out, and_9_out, and_10_out);
endmodule
